// Logisim project projet.circ as structural Verilog: 32 circuits, main circuit main
module main (
  output buzzer_0,
  output buzzer_1
);

  wire alarme_2_1_alarme, and_1_out, and_2_out, B_0_out, B_1_out, clock_1_out, clock_2_out, comparator_1_eq,
       debouncer_1_output_1, debouncer_2_output_1, dip_switch_sw1, dip_switch_sw2, dip_switch_sw3,
       dip_switch_sw4, dip_switch_sw5, dip_switch_sw6, dip_switch_sw7, dip_switch_sw8, dip_switch_sw9,
       dip_switch_sw10, jukebox_1_set_music_on, not_1_out, or_1_out, output_logic_1_a, output_logic_1_b,
       output_logic_1_c, output_logic_1_d, output_logic_1_e, output_logic_1_f, output_logic_1_g,
       output_logic_1_p, output_logic_2_a, output_logic_2_b, output_logic_2_c, output_logic_2_d,
       output_logic_2_e, output_logic_2_f, output_logic_2_g, output_logic_2_p, output_logic_3_a,
       output_logic_3_b, output_logic_3_c, output_logic_3_d, output_logic_3_e, output_logic_3_f,
       output_logic_3_g, output_logic_3_p, output_logic_4_a, output_logic_4_b, output_logic_4_c,
       output_logic_4_d, output_logic_4_e, output_logic_4_f, output_logic_4_g, output_logic_4_p,
       output_logic_5_a, output_logic_5_b, output_logic_5_c, output_logic_5_d, output_logic_5_e,
       output_logic_5_f, output_logic_5_g, output_logic_5_p, output_logic_6_a, output_logic_6_b,
       output_logic_6_c, output_logic_6_d, output_logic_6_e, output_logic_6_f, output_logic_6_g,
       output_logic_6_p, reset_mode_1_r, transition_logic_1_s_0, transition_logic_1_s_1,
       transition_logic_1_s_2, transition_logic_1_s_3;
  wire [1:0] jukebox_1_o_music;
  wire [3:0] d_ff_4_q;
  wire [4:0] multiplexer_2_out, multiplexer_3_out, multiplexer_4_out, multiplexer_5_out, multiplexer_6_out,
       multiplexer_7_out;
  wire [11:0] demultiplexer_1_out3, demultiplexer_1_out5, demultiplexer_1_out7, demultiplexer_1_out9,
       demultiplexer_1_out11, transition_logic_1_input_bus;
  wire [29:0] alarme_2_1_o_0, chrono_1_o_0, jukebox_1_o_text, memory_time_1_o_0, multiplexer_1_out,
       set_time_setter_1_o_0, set_time_zone_1_o_text, set_time_zone_1_o_time;

  Button B_1 (.out(B_1_out));
  Button B_0 (.out(B_0_out));
  to_one_tic debouncer_1 (.I_0(B_1_out), .R(reset_mode_1_r), .Output_1(debouncer_1_output_1));
  to_one_tic debouncer_2 (.I_0(B_0_out), .R(reset_mode_1_r), .Output_1(debouncer_2_output_1));
  not not_1 (not_1_out, 1'b0);
  DipSwitch #(.number(10)) dip_switch (
    .sw1(dip_switch_sw1), .sw2(dip_switch_sw2), .sw3(dip_switch_sw3), .sw4(dip_switch_sw4),
    .sw5(dip_switch_sw5), .sw6(dip_switch_sw6), .sw7(dip_switch_sw7), .sw8(dip_switch_sw8),
    .sw9(dip_switch_sw9), .sw10(dip_switch_sw10));
  and and_1 (and_1_out, not_1_out, debouncer_1_output_1);
  and and_2 (and_2_out, debouncer_2_output_1, not_1_out);
  or or_1 (or_1_out, alarme_2_1_alarme, jukebox_1_set_music_on);
  reset_mode reset_mode_1 (.B_1(B_1_out), .B_0(B_0_out), .R(reset_mode_1_r));
  musique musique_1 (.set_on(or_1_out), .music(jukebox_1_o_music), .buzzer_0(buzzer_0), .buzzer_1(buzzer_1));
  transition_logic transition_logic_1 (
    .C_3(d_ff_4_q[3]), .C_2(d_ff_4_q[2]), .C_1(d_ff_4_q[1]), .C_0(d_ff_4_q[0]), .B_1(and_1_out),
    .B_0(and_2_out), .DS_9(dip_switch_sw10), .DS_8(dip_switch_sw9), .DS_7(dip_switch_sw8),
    .DS_6(dip_switch_sw7), .DS_5(dip_switch_sw6), .DS_4(dip_switch_sw5), .DS_3(dip_switch_sw4),
    .DS_2(dip_switch_sw3), .DS_1(dip_switch_sw2), .DS_0(dip_switch_sw1), .S_3(transition_logic_1_s_3),
    .S_2(transition_logic_1_s_2), .S_1(transition_logic_1_s_1), .S_0(transition_logic_1_s_0),
    .input_bus(transition_logic_1_input_bus));
  Clock clock_1 (.out(clock_1_out));
  D_Flip_Flop d_ff_1 (
    .D(transition_logic_1_s_3), .clk(clock_1_out), .Q(d_ff_4_q[3]), .reset(reset_mode_1_r));  // open: Qn, preset
  D_Flip_Flop d_ff_2 (
    .D(transition_logic_1_s_2), .clk(clock_1_out), .Q(d_ff_4_q[2]), .reset(reset_mode_1_r));  // open: Qn, preset
  D_Flip_Flop d_ff_3 (
    .D(transition_logic_1_s_1), .clk(clock_1_out), .Q(d_ff_4_q[1]), .reset(reset_mode_1_r));  // open: Qn, preset
  D_Flip_Flop d_ff_4 (
    .D(transition_logic_1_s_0), .clk(clock_1_out), .Q(d_ff_4_q[0]), .reset(reset_mode_1_r));  // open: Qn, preset
  Demultiplexer #(.select(4), .width(12), .enable("false")) demultiplexer_1 (
    .out3(demultiplexer_1_out3), .out5(demultiplexer_1_out5), .out7(demultiplexer_1_out7),
    .out9(demultiplexer_1_out9), .out11(demultiplexer_1_out11), .in(transition_logic_1_input_bus),
    .sel(d_ff_4_q));  // open: out0, out1, out2, out4, out6, out8, out10, out12, out13, out14, out15
  Clock #(.highDuration(1000000), .lowDuration(1000000)) clock_2 (.out(clock_2_out));
  Comparator #(.width(4)) comparator_1 (.a(d_ff_4_q), .b(4'b0011), .eq(comparator_1_eq));  // open: gt, lt
  Multiplexer #(.select(4), .width(30), .enable("false")) multiplexer_1 (
    .in0({30{1'b0}}), .in1({30{1'b0}}), .in2({30{1'b0}}), .in3(set_time_setter_1_o_0), .in4({30{1'b0}}),
    .in5({30{1'b0}}), .in6({30{1'b0}}), .in7(set_time_zone_1_o_time), .in8({30{1'b0}}), .in9({30{1'b0}}),
    .in10({30{1'b0}}), .in11({30{1'b0}}), .in12({30{1'b0}}), .in13({30{1'b0}}), .in14({30{1'b0}}),
    .in15({30{1'b0}}), .out(multiplexer_1_out), .sel(d_ff_4_q));
  // Probe on memory_time_1_o_0
  // Probe on set_time_zone_1_o_time[29:25]
  // Probe on set_time_zone_1_o_time[24:20]
  // Probe on set_time_zone_1_o_time[19:15]
  // Probe on set_time_zone_1_o_time[14:10]
  // Probe on set_time_zone_1_o_time[9:5]
  // Probe on set_time_zone_1_o_time[4:0]
  memory_time memory_time_1 (
    .I_0(multiplexer_1_out), .clock_in(clock_2_out), .reset(reset_mode_1_r), .load(d_ff_4_q),
    .O_0(memory_time_1_o_0));  // open: carry
  set_time_setter set_time_setter_1 (
    .I_0(memory_time_1_o_0), .input_bus(demultiplexer_1_out3), .mode_on(comparator_1_eq), .R(reset_mode_1_r),
    .O_0(set_time_setter_1_o_0));
  alarme_2 alarme_2_1 (
    .time_bus(memory_time_1_o_0), .input_bus(demultiplexer_1_out5), .mode_on(d_ff_4_q),
    .B_1(debouncer_1_output_1), .B_0(debouncer_2_output_1), .R(reset_mode_1_r), .alarme(alarme_2_1_alarme),
    .O_0(alarme_2_1_o_0));
  set_time_zone set_time_zone_1 (
    .time_bus(memory_time_1_o_0), .mode_on(d_ff_4_q), .input_bus(demultiplexer_1_out7), .R(reset_mode_1_r),
    .O_text(set_time_zone_1_o_text), .O_time(set_time_zone_1_o_time));
  jukebox jukebox_1 (
    .mode_on(d_ff_4_q), .input_bus(demultiplexer_1_out9), .R(reset_mode_1_r), .O_text(jukebox_1_o_text),
    .O_music(jukebox_1_o_music), .set_music_on(jukebox_1_set_music_on));
  chrono chrono_1 (.input_bus(demultiplexer_1_out11), .mode_on(d_ff_4_q), .R(reset_mode_1_r), .O_0(chrono_1_o_0));
  // Probe on set_time_zone_1_o_time
  Multiplexer #(.select(4), .width(5), .enable("false")) multiplexer_2 (
    .in0(memory_time_1_o_0[29:25]), .in1(5'b11101), .in2(5'b11100), .in3(set_time_setter_1_o_0[29:25]),
    .in4(5'b11100), .in5(alarme_2_1_o_0[29:25]), .in6(5'b11011), .in7(set_time_zone_1_o_text[29:25]),
    .in8(5'b10011), .in9(jukebox_1_o_text[29:25]), .in10(5'b01100), .in11(chrono_1_o_0[29:25]),
    .out(multiplexer_2_out), .sel(d_ff_4_q));  // open: in12, in13, in14, in15
  Multiplexer #(.select(4), .width(5), .enable("false")) multiplexer_3 (
    .in0(memory_time_1_o_0[24:20]), .in1(5'b10010), .in2(5'b01110), .in3(set_time_setter_1_o_0[24:20]),
    .in4(5'b01110), .in5(alarme_2_1_o_0[24:20]), .in6(5'b01110), .in7(set_time_zone_1_o_text[24:20]),
    .in8(5'b11110), .in9(jukebox_1_o_text[24:20]), .in10(5'b10001), .in11(chrono_1_o_0[24:20]),
    .out(multiplexer_3_out), .sel(d_ff_4_q));  // open: in12, in13, in14, in15
  Multiplexer #(.select(4), .width(5), .enable("false")) multiplexer_4 (
    .in0(memory_time_1_o_0[19:15]), .in1(5'b11110), .in2(5'b11101), .in3(set_time_setter_1_o_0[19:15]),
    .in4(5'b11101), .in5(alarme_2_1_o_0[19:15]), .in6(5'b10000), .in7(set_time_zone_1_o_text[19:15]),
    .in8(5'b10100), .in9(jukebox_1_o_text[19:15]), .in10(5'b11011), .in11(chrono_1_o_0[19:15]),
    .out(multiplexer_4_out), .sel(d_ff_4_q));  // open: in12, in13, in14, in15
  Multiplexer #(.select(4), .width(5), .enable("false")) multiplexer_5 (
    .in0(memory_time_1_o_0[14:10]), .in1(5'b01110), .in2({5{1'b1}}), .in3(set_time_setter_1_o_0[14:10]),
    .in4({5{1'b1}}), .in5(alarme_2_1_o_0[14:10]), .in6(5'b10010), .in7(set_time_zone_1_o_text[14:10]),
    .in8(5'b01110), .in9(jukebox_1_o_text[14:10]), .in10(5'b11000), .in11(chrono_1_o_0[14:10]),
    .out(multiplexer_5_out), .sel(d_ff_4_q));  // open: in12, in13, in14, in15
  Multiplexer #(.select(4), .width(5), .enable("false")) multiplexer_6 (
    .in0(memory_time_1_o_0[9:5]), .in1({5{1'b1}}), .in2(5'b11101), .in3(set_time_setter_1_o_0[9:5]),
    .in4(5'b01010), .in5(alarme_2_1_o_0[9:5]), .in6(5'b11000), .in7(set_time_zone_1_o_text[9:5]),
    .in8(5'b01011), .in9(jukebox_1_o_text[9:5]), .in10(5'b10111), .in11(chrono_1_o_0[9:5]),
    .out(multiplexer_6_out), .sel(d_ff_4_q));  // open: in12, in13, in14, in15
  Multiplexer #(.select(4), .width(5), .enable("false")) multiplexer_7 (
    .in0(memory_time_1_o_0[4:0]), .in1({5{1'b1}}), .in2({5{1'b1}}), .in3(set_time_setter_1_o_0[4:0]),
    .in4({5{1'b1}}), .in5(alarme_2_1_o_0[4:0]), .in6(5'b10111), .in7(set_time_zone_1_o_text[4:0]),
    .in8(5'b11000), .in9(jukebox_1_o_text[4:0]), .in10(5'b11000), .in11(chrono_1_o_0[4:0]),
    .out(multiplexer_7_out), .sel(d_ff_4_q));  // open: in12, in13, in14, in15
  LED LED_1 (.in(1'b0));
  LED LED_2 (.in(1'b0));
  LED LED_3 (.in(1'b0));
  LED LED_4 (.in(1'b0));
  LED LED_5 (.in(1'b0));
  LED LED_6 (.in(1'b0));
  LED LED_7 (.in(1'b0));
  LED LED_8 (.in(1'b0));
  LED LED_9 (.in(1'b0));
  LED LED_10 (.in(1'b0));
  output_logic output_logic_1 (
    .I(multiplexer_2_out), .a(output_logic_1_a), .b(output_logic_1_b), .c(output_logic_1_c),
    .d(output_logic_1_d), .e(output_logic_1_e), .f(output_logic_1_f), .g(output_logic_1_g),
    .p(output_logic_1_p));  // open: point
  output_logic output_logic_2 (
    .I(multiplexer_3_out), .a(output_logic_2_a), .b(output_logic_2_b), .c(output_logic_2_c),
    .d(output_logic_2_d), .e(output_logic_2_e), .f(output_logic_2_f), .g(output_logic_2_g),
    .p(output_logic_2_p));  // open: point
  output_logic output_logic_3 (
    .I(multiplexer_4_out), .a(output_logic_3_a), .b(output_logic_3_b), .c(output_logic_3_c),
    .d(output_logic_3_d), .e(output_logic_3_e), .f(output_logic_3_f), .g(output_logic_3_g),
    .p(output_logic_3_p));  // open: point
  output_logic output_logic_4 (
    .I(multiplexer_5_out), .a(output_logic_4_a), .b(output_logic_4_b), .c(output_logic_4_c),
    .d(output_logic_4_d), .e(output_logic_4_e), .f(output_logic_4_f), .g(output_logic_4_g),
    .p(output_logic_4_p));  // open: point
  output_logic output_logic_5 (
    .I(multiplexer_6_out), .a(output_logic_5_a), .b(output_logic_5_b), .c(output_logic_5_c),
    .d(output_logic_5_d), .e(output_logic_5_e), .f(output_logic_5_f), .g(output_logic_5_g),
    .p(output_logic_5_p));  // open: point
  output_logic output_logic_6 (
    .I(multiplexer_7_out), .a(output_logic_6_a), .b(output_logic_6_b), .c(output_logic_6_c),
    .d(output_logic_6_d), .e(output_logic_6_e), .f(output_logic_6_f), .g(output_logic_6_g),
    .p(output_logic_6_p));  // open: point
  _7_Segment_Display L_7_Segment_Display_1 (
    .g(output_logic_1_g), .f(output_logic_1_f), .a(output_logic_1_a), .b(output_logic_1_b),
    .e(output_logic_1_e), .d(output_logic_1_d), .c(output_logic_1_c), .dp(output_logic_1_p));
  _7_Segment_Display L_7_Segment_Display_2 (
    .g(output_logic_2_g), .f(output_logic_2_f), .a(output_logic_2_a), .b(output_logic_2_b),
    .e(output_logic_2_e), .d(output_logic_2_d), .c(output_logic_2_c), .dp(output_logic_2_p));
  _7_Segment_Display L_7_Segment_Display_3 (
    .g(output_logic_3_g), .f(output_logic_3_f), .a(output_logic_3_a), .b(output_logic_3_b),
    .e(output_logic_3_e), .d(output_logic_3_d), .c(output_logic_3_c), .dp(output_logic_3_p));
  _7_Segment_Display L_7_Segment_Display_4 (
    .g(output_logic_4_g), .f(output_logic_4_f), .a(output_logic_4_a), .b(output_logic_4_b),
    .e(output_logic_4_e), .d(output_logic_4_d), .c(output_logic_4_c), .dp(output_logic_4_p));
  _7_Segment_Display L_7_Segment_Display_5 (
    .g(output_logic_5_g), .f(output_logic_5_f), .a(output_logic_5_a), .b(output_logic_5_b),
    .e(output_logic_5_e), .d(output_logic_5_d), .c(output_logic_5_c), .dp(output_logic_5_p));
  _7_Segment_Display L_7_Segment_Display_6 (
    .g(output_logic_6_g), .f(output_logic_6_f), .a(output_logic_6_a), .b(output_logic_6_b),
    .e(output_logic_6_e), .d(output_logic_6_d), .c(output_logic_6_c), .dp(output_logic_6_p));
endmodule

module output_logic (
  input  point,
  input  [4:0] I,
  output a,
  output b,
  output c,
  output d,
  output e,
  output f,
  output g,
  output p
);

  wire and_1_out, and_2_out, and_3_out, and_4_out, and_5_out, and_6_out, and_7_out, and_8_out, and_9_out,
       and_10_out, and_11_out, and_12_out, and_13_out, and_14_out, and_15_out, and_16_out, and_17_out,
       and_18_out, and_19_out, and_20_out, and_21_out, and_22_out, and_23_out, and_24_out, and_25_out,
       and_26_out, and_27_out, and_28_out, and_29_out, and_30_out, and_31_out, and_32_out, and_33_out,
       and_34_out, and_35_out, and_36_out, and_37_out, and_38_out, and_39_out, and_40_out, and_41_out,
       nand_1_out, nand_2_out, nand_3_out, nand_4_out, nand_5_out, nand_6_out, nand_7_out, nand_8_out,
       nand_9_out, nand_10_out, nand_11_out, nand_12_out, nand_13_out, nand_14_out, nand_15_out, nand_16_out,
       nand_17_out, nand_18_out, nand_19_out, nand_20_out, nand_21_out, nand_22_out, nand_23_out,
       nand_24_out, nand_25_out, nand_26_out, nand_27_out, nand_28_out, nand_29_out, nand_30_out,
       nand_31_out, nand_32_out, nand_33_out, nand_34_out, nand_35_out, nand_36_out, nand_37_out,
       nand_38_out, nand_39_out, nand_40_out, nand_41_out, nand_42_out, nand_43_out, nand_44_out,
       nand_45_out, nand_46_out, nand_47_out, nand_48_out, nand_49_out, nand_50_out, nand_51_out,
       nand_52_out, nand_53_out, nand_54_out, nand_55_out, nand_56_out, nand_57_out, nand_58_out,
       nand_59_out, nand_60_out, nand_61_out, nand_62_out, nand_63_out, nand_64_out, nand_65_out,
       nand_66_out, nand_67_out, nand_68_out, nand_69_out, nand_70_out, nand_71_out, nand_72_out,
       nand_73_out, nand_74_out, nand_75_out, nand_76_out, nand_77_out, nand_78_out, nand_79_out,
       nand_80_out, nand_81_out, nand_82_out, nand_83_out, nand_84_out, nand_85_out, nand_86_out,
       nand_87_out, nand_88_out, nand_89_out, nand_90_out, nand_91_out, nand_92_out, nand_93_out,
       nand_94_out, nand_95_out, nand_96_out, nand_97_out, nand_98_out, nand_99_out, nand_100_out,
       nand_101_out, nand_102_out, nand_103_out, nand_104_out, nand_105_out, nand_106_out, nand_107_out,
       nand_108_out, nand_109_out, nand_110_out, nand_111_out, nand_112_out, nand_113_out, nand_114_out,
       nand_115_out, nand_116_out, nand_117_out, nand_118_out, nand_119_out, nand_120_out, nand_121_out,
       nand_122_out, nand_123_out, nand_124_out, nand_125_out, nand_126_out, nand_127_out, nand_128_out,
       nand_129_out, nand_130_out, nand_131_out, nand_132_out, nand_133_out, nand_134_out, nand_135_out,
       nand_136_out, nand_137_out, nand_138_out, nand_139_out, nand_140_out, nand_141_out, nand_142_out,
       nand_143_out, nand_144_out, nand_145_out, nand_146_out, nand_147_out, nand_148_out, nand_149_out,
       nand_150_out, nand_151_out, nand_152_out, nand_153_out, nand_154_out, nand_155_out, nand_156_out,
       nand_157_out, nand_158_out, nand_159_out, nand_160_out, nand_161_out, nand_162_out, nand_163_out,
       nand_164_out, nand_165_out, nand_166_out, nand_167_out, nand_168_out, nand_169_out, nand_170_out,
       nand_171_out, nand_172_out, nand_173_out, nand_174_out, nand_175_out, nand_176_out, nand_177_out,
       nand_178_out, nand_179_out, nand_180_out, nand_181_out, nand_182_out, nand_183_out, nand_184_out,
       nand_185_out, nand_186_out, nand_187_out, nand_188_out, nand_189_out, nand_190_out, nand_191_out,
       nand_192_out, nand_193_out, nand_194_out, nand_195_out, nand_196_out, nand_197_out, nand_198_out,
       nand_199_out, nand_200_out, nand_201_out, nand_202_out, nand_203_out, nand_204_out, nand_205_out,
       nand_206_out, nand_207_out, nand_208_out, nand_209_out, nand_210_out, nand_211_out, nand_212_out,
       nand_213_out, nand_214_out, nand_215_out, nand_216_out, nand_217_out, nand_218_out, nand_219_out,
       nand_220_out, nand_221_out, nand_222_out, nand_223_out, nand_224_out, nand_225_out, nand_226_out,
       nand_227_out, nand_228_out, nand_229_out, nand_230_out, nand_231_out, nand_232_out, nand_233_out,
       nand_234_out, nand_235_out, nand_236_out, nand_237_out, nand_238_out, nand_239_out, nand_240_out,
       nand_241_out, nand_242_out, nand_243_out, nand_244_out, nand_245_out, nand_246_out, nand_247_out,
       nand_248_out, nand_249_out, nand_250_out, nand_251_out, nand_252_out, nand_253_out, nand_254_out,
       nand_255_out, nand_256_out, nand_257_out, nand_258_out, nand_259_out, nand_260_out, nand_261_out,
       nand_262_out, nand_263_out, nand_264_out, nand_265_out, nand_266_out, nand_267_out, nand_268_out,
       nand_269_out, nand_270_out, nand_271_out, nand_272_out, nand_273_out, nand_274_out, nand_275_out,
       nand_276_out, nand_277_out, nand_278_out, nand_279_out, nand_280_out, nand_281_out, nand_282_out,
       nand_283_out, nand_284_out, nand_285_out, nand_286_out, nand_287_out, nand_288_out, nand_289_out,
       nand_290_out, nand_291_out, nand_292_out, nand_293_out, nand_294_out, nand_295_out, nand_296_out,
       nand_297_out, nand_298_out, nand_299_out, nand_300_out, nand_301_out, nand_302_out, nand_303_out,
       nand_304_out, nand_305_out, nand_306_out, nand_307_out, nand_308_out, nand_309_out, nand_310_out,
       nand_311_out, nand_312_out, nand_313_out, nand_314_out, nand_315_out, nand_316_out, nand_317_out,
       nand_318_out, nand_319_out, nand_320_out, nand_321_out, nand_322_out, nand_323_out, nand_324_out,
       nand_325_out, nand_326_out, nand_327_out, nand_328_out, nand_329_out, nand_330_out, nand_331_out,
       nand_332_out, nand_333_out, nand_334_out, nand_335_out, nand_336_out, nand_337_out, nand_338_out,
       nand_339_out, nand_340_out, nand_341_out, nand_342_out, nand_343_out, nand_344_out, nand_345_out,
       nand_346_out, nand_347_out, nand_348_out, nand_349_out, nand_350_out, nand_351_out, nand_352_out,
       nand_353_out, nand_354_out, nand_355_out, nand_356_out, nand_357_out, nand_358_out, nand_359_out,
       nand_360_out, nand_361_out, nand_362_out, nand_363_out, nand_364_out, nand_365_out, nand_366_out,
       nand_367_out, nand_368_out, nand_369_out, nand_370_out, nand_371_out, nand_372_out, nand_373_out,
       nand_374_out, nand_375_out, nand_376_out, nand_377_out, nand_378_out, nand_379_out, nand_380_out,
       nand_381_out, nand_382_out, nand_383_out, nand_384_out, nand_385_out, nand_386_out, nand_387_out,
       nand_388_out, nand_389_out, nand_390_out, nand_391_out, nand_392_out, nand_393_out, nand_394_out,
       nand_395_out, nand_396_out, nand_397_out, nand_398_out, nand_399_out, nand_400_out, nand_401_out,
       nand_402_out, nand_403_out, nand_404_out, nand_405_out, nand_406_out, nand_407_out, nand_408_out,
       nand_409_out, nand_410_out, nand_411_out, nand_412_out, nand_413_out, nand_414_out, nand_415_out,
       nand_416_out, nand_417_out, nand_418_out, nand_419_out, nand_420_out, nand_421_out, nand_422_out,
       nand_423_out, nand_424_out, nand_425_out, nand_426_out, nand_427_out, nand_428_out, nand_429_out,
       nand_430_out, nand_431_out, nand_432_out, nand_433_out, nand_434_out, nand_435_out, nand_436_out,
       nand_437_out, nand_438_out, nand_439_out, nand_440_out, nand_441_out, nand_442_out, nand_443_out,
       nand_444_out, nand_445_out, nand_446_out, nand_447_out, nand_448_out, nand_449_out, nand_450_out,
       nand_451_out, nand_452_out, nand_453_out, nand_454_out, nand_455_out, nand_456_out, nand_457_out,
       nand_458_out, nand_459_out, nand_460_out, nand_461_out, nand_462_out, nand_463_out, nand_464_out,
       nand_465_out, nand_466_out, nand_467_out, nand_468_out, nand_469_out, nand_470_out, nand_471_out,
       nand_472_out, nand_473_out, nand_474_out, nand_475_out, nand_476_out, nand_477_out, nand_478_out,
       nand_479_out, nand_480_out, nand_481_out, nand_482_out, nand_483_out, nand_484_out, nand_485_out,
       nand_486_out, nand_487_out, nand_488_out, nand_489_out, nand_490_out, nand_491_out, nand_492_out,
       nand_493_out, nand_494_out, nand_495_out, nand_496_out, nand_497_out, nand_498_out, nand_499_out,
       nand_500_out, nand_501_out, nand_502_out, nand_503_out, nand_504_out, nand_505_out, nand_506_out,
       nand_507_out, nand_508_out, nand_509_out, nand_510_out, nand_511_out, nand_512_out, nand_513_out,
       nand_514_out, nand_515_out, nand_516_out, nand_517_out, nand_518_out, nand_519_out, nand_520_out,
       nand_521_out, nand_522_out, nand_523_out, nand_524_out, nand_525_out, nand_526_out, nand_527_out,
       nand_528_out, nand_529_out, nand_530_out, nand_531_out, nand_532_out, nand_533_out, nand_534_out,
       nand_535_out, nand_536_out, nand_537_out, nand_538_out, nand_539_out, nand_540_out, nand_541_out,
       nand_542_out, nand_543_out, nand_544_out, nand_545_out, nand_546_out, nand_547_out, nand_548_out,
       nand_549_out, nand_550_out, nand_551_out, nand_552_out, nand_553_out, nand_554_out, nand_555_out,
       nand_556_out, nand_557_out, nand_558_out, nand_559_out, nand_560_out, nand_561_out, nand_562_out,
       nand_563_out, nand_564_out, nand_565_out, nand_566_out, nand_567_out, nand_568_out, nand_569_out,
       nand_570_out, nand_571_out, nand_572_out, not_1_out, not_2_out, not_3_out, not_4_out, not_5_out,
       not_6_out, not_7_out, not_8_out, not_9_out, not_10_out, not_11_out, not_12_out, not_13_out,
       not_14_out, not_15_out, not_16_out, not_17_out, not_18_out, not_19_out, not_20_out, not_21_out,
       not_22_out, not_23_out, not_24_out, not_25_out, not_26_out, not_27_out, not_28_out, not_29_out,
       not_30_out, not_31_out, not_32_out, not_33_out, not_34_out, not_35_out, not_36_out, not_37_out,
       not_38_out, not_39_out, not_40_out, not_41_out, not_42_out, not_43_out, not_44_out, not_45_out,
       not_46_out, not_47_out, not_48_out, not_49_out, not_50_out, not_51_out, not_52_out, not_53_out,
       not_54_out, not_55_out, not_56_out, not_57_out, not_58_out, not_59_out, not_60_out, not_61_out,
       not_62_out, not_63_out, not_64_out, not_65_out, not_66_out;

  nand nand_1 (nand_1_out, I[2], I[2]);
  nand nand_2 (nand_2_out, I[1], I[1]);
  nand nand_3 (nand_3_out, I[2], I[2]);
  nand nand_4 (nand_4_out, I[1], I[1]);
  nand nand_5 (nand_5_out, I[4], I[4]);
  nand nand_6 (nand_6_out, I[3], I[3]);
  nand nand_7 (nand_7_out, I[4], I[4]);
  nand nand_8 (nand_8_out, I[3], I[3]);
  nand nand_9 (nand_9_out, I[2], I[2]);
  nand nand_10 (nand_10_out, I[1], I[1]);
  nand nand_11 (nand_11_out, I[2], I[2]);
  nand nand_12 (nand_12_out, I[1], I[1]);
  nand nand_13 (nand_13_out, I[4], I[4]);
  nand nand_14 (nand_14_out, I[3], I[3]);
  nand nand_15 (nand_15_out, I[4], I[4]);
  nand nand_16 (nand_16_out, I[3], I[3]);
  nand nand_17 (nand_17_out, I[4], I[4]);
  nand nand_18 (nand_18_out, I[3], I[3]);
  nand nand_19 (nand_19_out, I[4], I[4]);
  nand nand_20 (nand_20_out, I[3], I[3]);
  nand nand_21 (nand_21_out, I[4], I[4]);
  nand nand_22 (nand_22_out, I[4], I[4]);
  nand nand_23 (nand_23_out, I[4], I[4]);
  nand nand_24 (nand_24_out, I[3], I[3]);
  nand nand_25 (nand_25_out, I[4], I[4]);
  nand nand_26 (nand_26_out, I[3], I[3]);
  nand nand_27 (nand_27_out, I[4], I[4]);
  nand nand_28 (nand_28_out, I[4], I[4]);
  nand nand_29 (nand_29_out, I[2], I[2]);
  nand nand_30 (nand_30_out, I[1], I[1]);
  nand nand_31 (nand_31_out, I[2], I[2]);
  nand nand_32 (nand_32_out, I[1], I[1]);
  nand nand_33 (nand_33_out, I[4], I[4]);
  nand nand_34 (nand_34_out, I[3], I[3]);
  nand nand_35 (nand_35_out, I[4], I[4]);
  nand nand_36 (nand_36_out, I[3], I[3]);
  nand nand_37 (nand_37_out, I[2], I[2]);
  nand nand_38 (nand_38_out, I[1], I[1]);
  nand nand_39 (nand_39_out, I[2], I[2]);
  nand nand_40 (nand_40_out, I[1], I[1]);
  nand nand_41 (nand_41_out, I[4], I[4]);
  nand nand_42 (nand_42_out, I[3], I[3]);
  nand nand_43 (nand_43_out, I[4], I[4]);
  nand nand_44 (nand_44_out, I[3], I[3]);
  nand nand_45 (nand_45_out, I[4], I[4]);
  nand nand_46 (nand_46_out, I[3], I[3]);
  nand nand_47 (nand_47_out, I[4], I[4]);
  nand nand_48 (nand_48_out, I[3], I[3]);
  nand nand_49 (nand_49_out, I[4], I[4]);
  nand nand_50 (nand_50_out, I[4], I[4]);
  nand nand_51 (nand_51_out, I[4], I[4]);
  nand nand_52 (nand_52_out, I[3], I[3]);
  nand nand_53 (nand_53_out, I[4], I[4]);
  nand nand_54 (nand_54_out, I[3], I[3]);
  nand nand_55 (nand_55_out, I[4], I[4]);
  nand nand_56 (nand_56_out, I[4], I[4]);
  nand nand_57 (nand_57_out, I[2], I[2]);
  nand nand_58 (nand_58_out, I[2], I[2]);
  nand nand_59 (nand_59_out, I[2], I[2]);
  nand nand_60 (nand_60_out, I[2], I[2]);
  nand nand_61 (nand_61_out, I[2], I[2]);
  nand nand_62 (nand_62_out, I[2], I[2]);
  nand nand_63 (nand_63_out, I[2], I[2]);
  nand nand_64 (nand_64_out, I[2], I[2]);
  nand nand_65 (nand_65_out, I[2], I[2]);
  nand nand_66 (nand_66_out, I[2], I[2]);
  nand nand_67 (nand_67_out, I[2], I[2]);
  nand nand_68 (nand_68_out, I[2], I[2]);
  nand nand_69 (nand_69_out, I[2], I[2]);
  nand nand_70 (nand_70_out, I[2], I[2]);
  nand nand_71 (nand_71_out, I[2], I[2]);
  nand nand_72 (nand_72_out, I[2], I[2]);
  not not_1 (not_1_out, I[4]);
  not not_2 (not_2_out, I[3]);
  not not_3 (not_3_out, I[1]);
  not not_4 (not_4_out, I[0]);
  not not_5 (not_5_out, I[4]);
  not not_6 (not_6_out, I[2]);
  not not_7 (not_7_out, I[0]);
  not not_8 (not_8_out, I[3]);
  not not_9 (not_9_out, I[2]);
  not not_10 (not_10_out, I[4]);
  not not_11 (not_11_out, I[3]);
  not not_12 (not_12_out, I[2]);
  not not_13 (not_13_out, I[1]);
  not not_14 (not_14_out, I[4]);
  not not_15 (not_15_out, I[1]);
  not not_16 (not_16_out, I[0]);
  not not_17 (not_17_out, I[4]);
  not not_18 (not_18_out, I[3]);
  not not_19 (not_19_out, I[1]);
  not not_20 (not_20_out, I[4]);
  not not_21 (not_21_out, I[3]);
  not not_22 (not_22_out, I[4]);
  not not_23 (not_23_out, I[1]);
  not not_24 (not_24_out, I[3]);
  not not_25 (not_25_out, I[4]);
  not not_26 (not_26_out, I[2]);
  not not_27 (not_27_out, I[3]);
  not not_28 (not_28_out, I[2]);
  not not_29 (not_29_out, I[0]);
  nand nand_73 (nand_73_out, I[2], I[2]);
  nand nand_74 (nand_74_out, I[1], I[1]);
  nand nand_75 (nand_75_out, I[2], I[2]);
  nand nand_76 (nand_76_out, I[1], I[1]);
  nand nand_77 (nand_77_out, I[4], I[4]);
  nand nand_78 (nand_78_out, I[3], I[3]);
  nand nand_79 (nand_79_out, I[4], I[4]);
  nand nand_80 (nand_80_out, I[3], I[3]);
  nand nand_81 (nand_81_out, I[0], I[0]);
  nand nand_82 (nand_82_out, I[0], I[0]);
  nand nand_83 (nand_83_out, I[2], I[2]);
  nand nand_84 (nand_84_out, I[1], I[1]);
  nand nand_85 (nand_85_out, I[2], I[2]);
  nand nand_86 (nand_86_out, I[1], I[1]);
  nand nand_87 (nand_87_out, I[4], I[4]);
  nand nand_88 (nand_88_out, I[3], I[3]);
  nand nand_89 (nand_89_out, I[4], I[4]);
  nand nand_90 (nand_90_out, I[3], I[3]);
  nand nand_91 (nand_91_out, I[0], I[0]);
  nand nand_92 (nand_92_out, I[0], I[0]);
  nand nand_93 (nand_93_out, I[3], I[3]);
  nand nand_94 (nand_94_out, I[2], I[2]);
  nand nand_95 (nand_95_out, I[3], I[3]);
  nand nand_96 (nand_96_out, I[2], I[2]);
  nand nand_97 (nand_97_out, I[4], I[4]);
  nand nand_98 (nand_98_out, I[4], I[4]);
  nand nand_99 (nand_99_out, I[1], I[1]);
  nand nand_100 (nand_100_out, I[1], I[1]);
  nand nand_101 (nand_101_out, I[3], I[3]);
  nand nand_102 (nand_102_out, I[2], I[2]);
  nand nand_103 (nand_103_out, I[3], I[3]);
  nand nand_104 (nand_104_out, I[2], I[2]);
  nand nand_105 (nand_105_out, I[4], I[4]);
  nand nand_106 (nand_106_out, I[4], I[4]);
  nand nand_107 (nand_107_out, I[1], I[1]);
  nand nand_108 (nand_108_out, I[1], I[1]);
  nand nand_109 (nand_109_out, I[2], I[2]);
  nand nand_110 (nand_110_out, I[1], I[1]);
  nand nand_111 (nand_111_out, I[2], I[2]);
  nand nand_112 (nand_112_out, I[1], I[1]);
  nand nand_113 (nand_113_out, I[4], I[4]);
  nand nand_114 (nand_114_out, I[3], I[3]);
  nand nand_115 (nand_115_out, I[4], I[4]);
  nand nand_116 (nand_116_out, I[3], I[3]);
  nand nand_117 (nand_117_out, I[0], I[0]);
  nand nand_118 (nand_118_out, I[0], I[0]);
  nand nand_119 (nand_119_out, I[2], I[2]);
  nand nand_120 (nand_120_out, I[1], I[1]);
  nand nand_121 (nand_121_out, I[2], I[2]);
  nand nand_122 (nand_122_out, I[1], I[1]);
  nand nand_123 (nand_123_out, I[4], I[4]);
  nand nand_124 (nand_124_out, I[3], I[3]);
  nand nand_125 (nand_125_out, I[4], I[4]);
  nand nand_126 (nand_126_out, I[3], I[3]);
  nand nand_127 (nand_127_out, I[0], I[0]);
  nand nand_128 (nand_128_out, I[0], I[0]);
  nand nand_129 (nand_129_out, I[3], I[3]);
  nand nand_130 (nand_130_out, I[2], I[2]);
  nand nand_131 (nand_131_out, I[3], I[3]);
  nand nand_132 (nand_132_out, I[2], I[2]);
  nand nand_133 (nand_133_out, I[4], I[4]);
  nand nand_134 (nand_134_out, I[4], I[4]);
  nand nand_135 (nand_135_out, I[1], I[1]);
  nand nand_136 (nand_136_out, I[1], I[1]);
  nand nand_137 (nand_137_out, I[3], I[3]);
  nand nand_138 (nand_138_out, I[2], I[2]);
  nand nand_139 (nand_139_out, I[3], I[3]);
  nand nand_140 (nand_140_out, I[2], I[2]);
  nand nand_141 (nand_141_out, I[4], I[4]);
  nand nand_142 (nand_142_out, I[4], I[4]);
  nand nand_143 (nand_143_out, I[1], I[1]);
  nand nand_144 (nand_144_out, I[1], I[1]);
  nand nand_145 (nand_145_out, I[4], I[4]);
  nand nand_146 (nand_146_out, I[4], I[4]);
  nand nand_147 (nand_147_out, I[4], I[4]);
  nand nand_148 (nand_148_out, I[4], I[4]);
  nand nand_149 (nand_149_out, I[2], I[2]);
  nand nand_150 (nand_150_out, I[2], I[2]);
  nand nand_151 (nand_151_out, I[4], I[4]);
  nand nand_152 (nand_152_out, I[4], I[4]);
  nand nand_153 (nand_153_out, I[4], I[4]);
  nand nand_154 (nand_154_out, I[4], I[4]);
  nand nand_155 (nand_155_out, I[2], I[2]);
  nand nand_156 (nand_156_out, I[2], I[2]);
  nand nand_157 (nand_157_out, I[3], I[3]);
  nand nand_158 (nand_158_out, I[3], I[3]);
  nand nand_159 (nand_159_out, I[1], I[1]);
  nand nand_160 (nand_160_out, I[1], I[1]);
  nand nand_161 (nand_161_out, I[3], I[3]);
  nand nand_162 (nand_162_out, I[3], I[3]);
  nand nand_163 (nand_163_out, I[1], I[1]);
  nand nand_164 (nand_164_out, I[1], I[1]);
  nand nand_165 (nand_165_out, I[4], I[4]);
  nand nand_166 (nand_166_out, I[4], I[4]);
  nand nand_167 (nand_167_out, I[4], I[4]);
  nand nand_168 (nand_168_out, I[4], I[4]);
  nand nand_169 (nand_169_out, I[2], I[2]);
  nand nand_170 (nand_170_out, I[2], I[2]);
  nand nand_171 (nand_171_out, I[4], I[4]);
  nand nand_172 (nand_172_out, I[4], I[4]);
  nand nand_173 (nand_173_out, I[4], I[4]);
  nand nand_174 (nand_174_out, I[4], I[4]);
  nand nand_175 (nand_175_out, I[2], I[2]);
  nand nand_176 (nand_176_out, I[2], I[2]);
  nand nand_177 (nand_177_out, I[3], I[3]);
  nand nand_178 (nand_178_out, I[3], I[3]);
  nand nand_179 (nand_179_out, I[1], I[1]);
  nand nand_180 (nand_180_out, I[1], I[1]);
  nand nand_181 (nand_181_out, I[3], I[3]);
  nand nand_182 (nand_182_out, I[3], I[3]);
  nand nand_183 (nand_183_out, I[1], I[1]);
  nand nand_184 (nand_184_out, I[1], I[1]);
  not not_30 (not_30_out, I[4]);
  not not_31 (not_31_out, I[2]);
  not not_32 (not_32_out, I[0]);
  not not_33 (not_33_out, I[0]);
  not not_34 (not_34_out, I[2]);
  not not_35 (not_35_out, I[4]);
  not not_36 (not_36_out, I[2]);
  not not_37 (not_37_out, I[1]);
  not not_38 (not_38_out, I[1]);
  not not_39 (not_39_out, I[3]);
  not not_40 (not_40_out, I[1]);
  not not_41 (not_41_out, I[0]);
  not not_42 (not_42_out, I[3]);
  not not_43 (not_43_out, I[1]);
  not not_44 (not_44_out, I[0]);
  not not_45 (not_45_out, I[2]);
  not not_46 (not_46_out, I[1]);
  not not_47 (not_47_out, I[0]);
  not not_48 (not_48_out, I[4]);
  not not_49 (not_49_out, I[1]);
  not not_50 (not_50_out, I[4]);
  not not_51 (not_51_out, I[2]);
  not not_52 (not_52_out, I[4]);
  not not_53 (not_53_out, I[1]);
  not not_54 (not_54_out, I[3]);
  not not_55 (not_55_out, I[0]);
  not not_56 (not_56_out, I[4]);
  not not_57 (not_57_out, I[2]);
  not not_58 (not_58_out, I[1]);
  not not_59 (not_59_out, I[2]);
  not not_60 (not_60_out, I[1]);
  not not_61 (not_61_out, I[3]);
  not not_62 (not_62_out, I[4]);
  not not_63 (not_63_out, I[3]);
  not not_64 (not_64_out, I[2]);
  not not_65 (not_65_out, I[1]);
  not not_66 (not_66_out, I[0]);
  nand nand_185 (nand_185_out, nand_1_out, nand_2_out);
  nand nand_186 (nand_186_out, nand_3_out, nand_4_out);
  nand nand_187 (nand_187_out, nand_5_out, nand_6_out);
  nand nand_188 (nand_188_out, nand_7_out, nand_8_out);
  nand nand_189 (nand_189_out, nand_9_out, nand_10_out);
  nand nand_190 (nand_190_out, nand_11_out, nand_12_out);
  nand nand_191 (nand_191_out, nand_13_out, nand_14_out);
  nand nand_192 (nand_192_out, nand_15_out, nand_16_out);
  nand nand_193 (nand_193_out, nand_17_out, nand_18_out);
  nand nand_194 (nand_194_out, nand_19_out, nand_20_out);
  nand nand_195 (nand_195_out, I[2], I[0]);
  nand nand_196 (nand_196_out, I[2], I[0]);
  nand nand_197 (nand_197_out, nand_21_out, I[2]);
  nand nand_198 (nand_198_out, nand_22_out, I[2]);
  nand nand_199 (nand_199_out, nand_23_out, nand_24_out);
  nand nand_200 (nand_200_out, nand_25_out, nand_26_out);
  nand nand_201 (nand_201_out, I[2], I[0]);
  nand nand_202 (nand_202_out, I[2], I[0]);
  nand nand_203 (nand_203_out, nand_27_out, I[2]);
  nand nand_204 (nand_204_out, nand_28_out, I[2]);
  nand nand_205 (nand_205_out, nand_29_out, nand_30_out);
  nand nand_206 (nand_206_out, nand_31_out, nand_32_out);
  nand nand_207 (nand_207_out, nand_33_out, nand_34_out);
  nand nand_208 (nand_208_out, nand_35_out, nand_36_out);
  nand nand_209 (nand_209_out, nand_37_out, nand_38_out);
  nand nand_210 (nand_210_out, nand_39_out, nand_40_out);
  nand nand_211 (nand_211_out, nand_41_out, nand_42_out);
  nand nand_212 (nand_212_out, nand_43_out, nand_44_out);
  nand nand_213 (nand_213_out, nand_45_out, nand_46_out);
  nand nand_214 (nand_214_out, nand_47_out, nand_48_out);
  nand nand_215 (nand_215_out, I[2], I[0]);
  nand nand_216 (nand_216_out, I[2], I[0]);
  nand nand_217 (nand_217_out, nand_49_out, I[2]);
  nand nand_218 (nand_218_out, nand_50_out, I[2]);
  nand nand_219 (nand_219_out, nand_51_out, nand_52_out);
  nand nand_220 (nand_220_out, nand_53_out, nand_54_out);
  nand nand_221 (nand_221_out, I[2], I[0]);
  nand nand_222 (nand_222_out, I[2], I[0]);
  nand nand_223 (nand_223_out, nand_55_out, I[2]);
  nand nand_224 (nand_224_out, nand_56_out, I[2]);
  nand nand_225 (nand_225_out, I[3], nand_57_out);
  nand nand_226 (nand_226_out, I[3], nand_58_out);
  nand nand_227 (nand_227_out, I[3], nand_59_out);
  nand nand_228 (nand_228_out, I[3], nand_60_out);
  nand nand_229 (nand_229_out, I[3], nand_61_out);
  nand nand_230 (nand_230_out, I[3], nand_62_out);
  nand nand_231 (nand_231_out, I[3], nand_63_out);
  nand nand_232 (nand_232_out, I[3], nand_64_out);
  nand nand_233 (nand_233_out, I[3], nand_65_out);
  nand nand_234 (nand_234_out, I[3], nand_66_out);
  nand nand_235 (nand_235_out, I[3], nand_67_out);
  nand nand_236 (nand_236_out, I[3], nand_68_out);
  nand nand_237 (nand_237_out, I[3], nand_69_out);
  nand nand_238 (nand_238_out, I[3], nand_70_out);
  nand nand_239 (nand_239_out, I[3], nand_71_out);
  nand nand_240 (nand_240_out, I[3], nand_72_out);
  and and_1 (and_1_out, not_1_out, not_2_out, not_3_out, not_4_out);
  and and_2 (and_2_out, not_5_out, not_6_out, not_7_out);
  and and_3 (and_3_out, not_8_out, not_9_out, I[0]);
  and and_4 (and_4_out, not_10_out, not_11_out, I[1], I[0]);
  and and_5 (and_5_out, I[3], not_12_out, not_13_out);
  and and_6 (and_6_out, not_14_out, I[3], not_15_out, I[0]);
  and and_7 (and_7_out, I[4], I[1], not_16_out);
  and and_8 (and_8_out, not_17_out, not_18_out, not_19_out);
  and and_9 (and_9_out, not_20_out, not_21_out, I[0]);
  and and_10 (and_10_out, not_22_out, not_23_out, I[0]);
  and and_11 (and_11_out, not_24_out, I[2], I[1]);
  and and_12 (and_12_out, not_25_out, I[3], not_26_out);
  and and_13 (and_13_out, I[4], not_27_out, not_28_out);
  and and_14 (and_14_out, I[4], I[3], not_29_out);
  nand nand_241 (nand_241_out, nand_73_out, nand_74_out);
  nand nand_242 (nand_242_out, nand_75_out, nand_76_out);
  nand nand_243 (nand_243_out, nand_77_out, nand_78_out);
  nand nand_244 (nand_244_out, nand_79_out, nand_80_out);
  nand nand_245 (nand_245_out, I[1], nand_81_out);
  nand nand_246 (nand_246_out, I[1], nand_82_out);
  nand nand_247 (nand_247_out, nand_83_out, nand_84_out);
  nand nand_248 (nand_248_out, nand_85_out, nand_86_out);
  nand nand_249 (nand_249_out, nand_87_out, nand_88_out);
  nand nand_250 (nand_250_out, nand_89_out, nand_90_out);
  nand nand_251 (nand_251_out, I[1], nand_91_out);
  nand nand_252 (nand_252_out, I[1], nand_92_out);
  nand nand_253 (nand_253_out, nand_93_out, nand_94_out);
  nand nand_254 (nand_254_out, nand_95_out, nand_96_out);
  nand nand_255 (nand_255_out, I[1], I[0]);
  nand nand_256 (nand_256_out, I[1], I[0]);
  nand nand_257 (nand_257_out, nand_97_out, I[2]);
  nand nand_258 (nand_258_out, nand_98_out, I[2]);
  nand nand_259 (nand_259_out, nand_99_out, I[0]);
  nand nand_260 (nand_260_out, nand_100_out, I[0]);
  nand nand_261 (nand_261_out, nand_101_out, nand_102_out);
  nand nand_262 (nand_262_out, nand_103_out, nand_104_out);
  nand nand_263 (nand_263_out, I[1], I[0]);
  nand nand_264 (nand_264_out, I[1], I[0]);
  nand nand_265 (nand_265_out, nand_105_out, I[2]);
  nand nand_266 (nand_266_out, nand_106_out, I[2]);
  nand nand_267 (nand_267_out, nand_107_out, I[0]);
  nand nand_268 (nand_268_out, nand_108_out, I[0]);
  nand nand_269 (nand_269_out, nand_109_out, nand_110_out);
  nand nand_270 (nand_270_out, nand_111_out, nand_112_out);
  nand nand_271 (nand_271_out, nand_113_out, nand_114_out);
  nand nand_272 (nand_272_out, nand_115_out, nand_116_out);
  nand nand_273 (nand_273_out, I[1], nand_117_out);
  nand nand_274 (nand_274_out, I[1], nand_118_out);
  nand nand_275 (nand_275_out, nand_119_out, nand_120_out);
  nand nand_276 (nand_276_out, nand_121_out, nand_122_out);
  nand nand_277 (nand_277_out, nand_123_out, nand_124_out);
  nand nand_278 (nand_278_out, nand_125_out, nand_126_out);
  nand nand_279 (nand_279_out, I[1], nand_127_out);
  nand nand_280 (nand_280_out, I[1], nand_128_out);
  nand nand_281 (nand_281_out, nand_129_out, nand_130_out);
  nand nand_282 (nand_282_out, nand_131_out, nand_132_out);
  nand nand_283 (nand_283_out, I[1], I[0]);
  nand nand_284 (nand_284_out, I[1], I[0]);
  nand nand_285 (nand_285_out, nand_133_out, I[2]);
  nand nand_286 (nand_286_out, nand_134_out, I[2]);
  nand nand_287 (nand_287_out, nand_135_out, I[0]);
  nand nand_288 (nand_288_out, nand_136_out, I[0]);
  nand nand_289 (nand_289_out, nand_137_out, nand_138_out);
  nand nand_290 (nand_290_out, nand_139_out, nand_140_out);
  nand nand_291 (nand_291_out, I[1], I[0]);
  nand nand_292 (nand_292_out, I[1], I[0]);
  nand nand_293 (nand_293_out, nand_141_out, I[2]);
  nand nand_294 (nand_294_out, nand_142_out, I[2]);
  nand nand_295 (nand_295_out, nand_143_out, I[0]);
  nand nand_296 (nand_296_out, nand_144_out, I[0]);
  nand nand_297 (nand_297_out, nand_145_out, I[3]);
  nand nand_298 (nand_298_out, nand_146_out, I[3]);
  nand nand_299 (nand_299_out, nand_147_out, I[3]);
  nand nand_300 (nand_300_out, nand_148_out, I[3]);
  nand nand_301 (nand_301_out, nand_149_out, I[0]);
  nand nand_302 (nand_302_out, nand_150_out, I[0]);
  nand nand_303 (nand_303_out, nand_151_out, I[3]);
  nand nand_304 (nand_304_out, nand_152_out, I[3]);
  nand nand_305 (nand_305_out, nand_153_out, I[3]);
  nand nand_306 (nand_306_out, nand_154_out, I[3]);
  nand nand_307 (nand_307_out, nand_155_out, I[0]);
  nand nand_308 (nand_308_out, nand_156_out, I[0]);
  nand nand_309 (nand_309_out, I[3], I[2]);
  nand nand_310 (nand_310_out, I[3], I[2]);
  nand nand_311 (nand_311_out, I[4], nand_157_out);
  nand nand_312 (nand_312_out, I[4], nand_158_out);
  nand nand_313 (nand_313_out, I[2], nand_159_out);
  nand nand_314 (nand_314_out, I[2], nand_160_out);
  nand nand_315 (nand_315_out, I[3], I[2]);
  nand nand_316 (nand_316_out, I[3], I[2]);
  nand nand_317 (nand_317_out, I[4], nand_161_out);
  nand nand_318 (nand_318_out, I[4], nand_162_out);
  nand nand_319 (nand_319_out, I[2], nand_163_out);
  nand nand_320 (nand_320_out, I[2], nand_164_out);
  nand nand_321 (nand_321_out, nand_165_out, I[3]);
  nand nand_322 (nand_322_out, nand_166_out, I[3]);
  nand nand_323 (nand_323_out, nand_167_out, I[3]);
  nand nand_324 (nand_324_out, nand_168_out, I[3]);
  nand nand_325 (nand_325_out, nand_169_out, I[0]);
  nand nand_326 (nand_326_out, nand_170_out, I[0]);
  nand nand_327 (nand_327_out, nand_171_out, I[3]);
  nand nand_328 (nand_328_out, nand_172_out, I[3]);
  nand nand_329 (nand_329_out, nand_173_out, I[3]);
  nand nand_330 (nand_330_out, nand_174_out, I[3]);
  nand nand_331 (nand_331_out, nand_175_out, I[0]);
  nand nand_332 (nand_332_out, nand_176_out, I[0]);
  nand nand_333 (nand_333_out, I[3], I[2]);
  nand nand_334 (nand_334_out, I[3], I[2]);
  nand nand_335 (nand_335_out, I[4], nand_177_out);
  nand nand_336 (nand_336_out, I[4], nand_178_out);
  nand nand_337 (nand_337_out, I[2], nand_179_out);
  nand nand_338 (nand_338_out, I[2], nand_180_out);
  nand nand_339 (nand_339_out, I[3], I[2]);
  nand nand_340 (nand_340_out, I[3], I[2]);
  nand nand_341 (nand_341_out, I[4], nand_181_out);
  nand nand_342 (nand_342_out, I[4], nand_182_out);
  nand nand_343 (nand_343_out, I[2], nand_183_out);
  nand nand_344 (nand_344_out, I[2], nand_184_out);
  and and_15 (and_15_out, not_30_out, not_31_out, not_32_out);
  and and_16 (and_16_out, I[2], I[1], not_33_out);
  and and_17 (and_17_out, I[3], not_34_out, I[1], I[0]);
  and and_18 (and_18_out, not_35_out, I[3], I[2]);
  and and_19 (and_19_out, I[4], not_36_out, not_37_out);
  and and_20 (and_20_out, I[4], not_38_out, I[0]);
  and and_21 (and_21_out, I[4], not_39_out, I[2]);
  and and_22 (and_22_out, not_40_out, not_41_out);
  and and_23 (and_23_out, not_42_out, I[2], not_43_out);
  and and_24 (and_24_out, I[2], not_44_out);
  and and_25 (and_25_out, I[3], not_45_out, not_46_out);
  and and_26 (and_26_out, I[3], not_47_out);
  and and_27 (and_27_out, not_48_out, I[3], I[1]);
  and and_28 (and_28_out, I[4], not_49_out);
  and and_29 (and_29_out, not_50_out, not_51_out, I[1]);
  and and_30 (and_30_out, not_52_out, I[2], not_53_out);
  and and_31 (and_31_out, not_54_out, I[2], not_55_out);
  and and_32 (and_32_out, not_56_out, I[3]);
  and and_33 (and_33_out, I[3], not_57_out, I[1]);
  and and_34 (and_34_out, I[3], I[2], not_58_out);
  and and_35 (and_35_out, I[4], not_59_out, not_60_out, I[0]);
  and and_36 (and_36_out, I[4], not_61_out, I[2], I[1]);
  and and_37 (and_37_out, point, not_62_out);
  and and_38 (and_38_out, point, not_63_out);
  and and_39 (and_39_out, point, not_64_out);
  and and_40 (and_40_out, point, not_65_out);
  and and_41 (and_41_out, point, not_66_out);
  nand nand_345 (nand_345_out, nand_185_out, nand_186_out);
  nand nand_346 (nand_346_out, I[0], I[0]);
  nand nand_347 (nand_347_out, nand_187_out, nand_188_out);
  nand nand_348 (nand_348_out, nand_189_out, nand_190_out);
  nand nand_349 (nand_349_out, I[0], I[0]);
  nand nand_350 (nand_350_out, nand_191_out, nand_192_out);
  nand nand_351 (nand_351_out, nand_193_out, nand_194_out);
  nand nand_352 (nand_352_out, nand_195_out, nand_196_out);
  nand nand_353 (nand_353_out, nand_197_out, nand_198_out);
  nand nand_354 (nand_354_out, nand_199_out, nand_200_out);
  nand nand_355 (nand_355_out, nand_201_out, nand_202_out);
  nand nand_356 (nand_356_out, nand_203_out, nand_204_out);
  nand nand_357 (nand_357_out, nand_205_out, nand_206_out);
  nand nand_358 (nand_358_out, I[0], I[0]);
  nand nand_359 (nand_359_out, nand_207_out, nand_208_out);
  nand nand_360 (nand_360_out, nand_209_out, nand_210_out);
  nand nand_361 (nand_361_out, I[0], I[0]);
  nand nand_362 (nand_362_out, nand_211_out, nand_212_out);
  nand nand_363 (nand_363_out, nand_213_out, nand_214_out);
  nand nand_364 (nand_364_out, nand_215_out, nand_216_out);
  nand nand_365 (nand_365_out, nand_217_out, nand_218_out);
  nand nand_366 (nand_366_out, nand_219_out, nand_220_out);
  nand nand_367 (nand_367_out, nand_221_out, nand_222_out);
  nand nand_368 (nand_368_out, nand_223_out, nand_224_out);
  nand nand_369 (nand_369_out, nand_225_out, nand_226_out);
  nand nand_370 (nand_370_out, I[1], I[1]);
  nand nand_371 (nand_371_out, nand_227_out, nand_228_out);
  nand nand_372 (nand_372_out, I[0], I[0]);
  nand nand_373 (nand_373_out, nand_229_out, nand_230_out);
  nand nand_374 (nand_374_out, I[1], I[1]);
  nand nand_375 (nand_375_out, nand_231_out, nand_232_out);
  nand nand_376 (nand_376_out, I[0], I[0]);
  nand nand_377 (nand_377_out, I[1], I[1]);
  nand nand_378 (nand_378_out, I[1], I[1]);
  nand nand_379 (nand_379_out, nand_233_out, nand_234_out);
  nand nand_380 (nand_380_out, I[1], I[1]);
  nand nand_381 (nand_381_out, nand_235_out, nand_236_out);
  nand nand_382 (nand_382_out, I[0], I[0]);
  nand nand_383 (nand_383_out, nand_237_out, nand_238_out);
  nand nand_384 (nand_384_out, I[1], I[1]);
  nand nand_385 (nand_385_out, nand_239_out, nand_240_out);
  nand nand_386 (nand_386_out, I[0], I[0]);
  nand nand_387 (nand_387_out, I[1], I[1]);
  nand nand_388 (nand_388_out, I[1], I[1]);
  or or_1 (b, and_1_out, and_2_out, and_3_out, and_4_out, and_5_out, and_6_out, and_7_out);
  or or_2 (c, and_8_out, and_9_out, and_10_out, and_11_out, and_12_out, and_13_out, and_14_out);
  nand nand_389 (nand_389_out, nand_241_out, nand_242_out);
  nand nand_390 (nand_390_out, I[0], I[0]);
  nand nand_391 (nand_391_out, nand_243_out, nand_244_out);
  nand nand_392 (nand_392_out, nand_245_out, nand_246_out);
  nand nand_393 (nand_393_out, nand_247_out, nand_248_out);
  nand nand_394 (nand_394_out, I[0], I[0]);
  nand nand_395 (nand_395_out, nand_249_out, nand_250_out);
  nand nand_396 (nand_396_out, nand_251_out, nand_252_out);
  nand nand_397 (nand_397_out, nand_253_out, nand_254_out);
  nand nand_398 (nand_398_out, nand_255_out, nand_256_out);
  nand nand_399 (nand_399_out, nand_257_out, nand_258_out);
  nand nand_400 (nand_400_out, nand_259_out, nand_260_out);
  nand nand_401 (nand_401_out, nand_261_out, nand_262_out);
  nand nand_402 (nand_402_out, nand_263_out, nand_264_out);
  nand nand_403 (nand_403_out, nand_265_out, nand_266_out);
  nand nand_404 (nand_404_out, nand_267_out, nand_268_out);
  nand nand_405 (nand_405_out, nand_269_out, nand_270_out);
  nand nand_406 (nand_406_out, I[0], I[0]);
  nand nand_407 (nand_407_out, nand_271_out, nand_272_out);
  nand nand_408 (nand_408_out, nand_273_out, nand_274_out);
  nand nand_409 (nand_409_out, nand_275_out, nand_276_out);
  nand nand_410 (nand_410_out, I[0], I[0]);
  nand nand_411 (nand_411_out, nand_277_out, nand_278_out);
  nand nand_412 (nand_412_out, nand_279_out, nand_280_out);
  nand nand_413 (nand_413_out, nand_281_out, nand_282_out);
  nand nand_414 (nand_414_out, nand_283_out, nand_284_out);
  nand nand_415 (nand_415_out, nand_285_out, nand_286_out);
  nand nand_416 (nand_416_out, nand_287_out, nand_288_out);
  nand nand_417 (nand_417_out, nand_289_out, nand_290_out);
  nand nand_418 (nand_418_out, nand_291_out, nand_292_out);
  nand nand_419 (nand_419_out, nand_293_out, nand_294_out);
  nand nand_420 (nand_420_out, nand_295_out, nand_296_out);
  nand nand_421 (nand_421_out, nand_297_out, nand_298_out);
  nand nand_422 (nand_422_out, I[1], I[1]);
  nand nand_423 (nand_423_out, nand_299_out, nand_300_out);
  nand nand_424 (nand_424_out, nand_301_out, nand_302_out);
  nand nand_425 (nand_425_out, nand_303_out, nand_304_out);
  nand nand_426 (nand_426_out, I[1], I[1]);
  nand nand_427 (nand_427_out, nand_305_out, nand_306_out);
  nand nand_428 (nand_428_out, nand_307_out, nand_308_out);
  nand nand_429 (nand_429_out, nand_309_out, nand_310_out);
  nand nand_430 (nand_430_out, I[0], I[0]);
  nand nand_431 (nand_431_out, nand_311_out, nand_312_out);
  nand nand_432 (nand_432_out, nand_313_out, nand_314_out);
  nand nand_433 (nand_433_out, nand_315_out, nand_316_out);
  nand nand_434 (nand_434_out, I[0], I[0]);
  nand nand_435 (nand_435_out, nand_317_out, nand_318_out);
  nand nand_436 (nand_436_out, nand_319_out, nand_320_out);
  nand nand_437 (nand_437_out, nand_321_out, nand_322_out);
  nand nand_438 (nand_438_out, I[1], I[1]);
  nand nand_439 (nand_439_out, nand_323_out, nand_324_out);
  nand nand_440 (nand_440_out, nand_325_out, nand_326_out);
  nand nand_441 (nand_441_out, nand_327_out, nand_328_out);
  nand nand_442 (nand_442_out, I[1], I[1]);
  nand nand_443 (nand_443_out, nand_329_out, nand_330_out);
  nand nand_444 (nand_444_out, nand_331_out, nand_332_out);
  nand nand_445 (nand_445_out, nand_333_out, nand_334_out);
  nand nand_446 (nand_446_out, I[0], I[0]);
  nand nand_447 (nand_447_out, nand_335_out, nand_336_out);
  nand nand_448 (nand_448_out, nand_337_out, nand_338_out);
  nand nand_449 (nand_449_out, nand_339_out, nand_340_out);
  nand nand_450 (nand_450_out, I[0], I[0]);
  nand nand_451 (nand_451_out, nand_341_out, nand_342_out);
  nand nand_452 (nand_452_out, nand_343_out, nand_344_out);
  or or_3 (e, and_15_out, and_16_out, and_17_out, and_18_out, and_19_out, and_20_out, and_21_out);
  or or_4 (f, and_22_out, and_23_out, and_24_out, and_25_out, and_26_out, and_27_out, and_28_out);
  or or_5 (g, and_29_out, and_30_out, and_31_out, and_32_out, and_33_out, and_34_out, and_35_out, and_36_out);
  or or_6 (p, and_37_out, and_38_out, and_39_out, and_40_out, and_41_out);
  nand nand_453 (nand_453_out, nand_345_out, nand_346_out);
  nand nand_454 (nand_454_out, nand_347_out, I[1]);
  nand nand_455 (nand_455_out, nand_348_out, nand_349_out);
  nand nand_456 (nand_456_out, nand_350_out, I[1]);
  nand nand_457 (nand_457_out, nand_351_out, nand_352_out);
  nand nand_458 (nand_458_out, nand_353_out, I[1]);
  nand nand_459 (nand_459_out, nand_354_out, nand_355_out);
  nand nand_460 (nand_460_out, nand_356_out, I[1]);
  nand nand_461 (nand_461_out, nand_357_out, nand_358_out);
  nand nand_462 (nand_462_out, nand_359_out, I[1]);
  nand nand_463 (nand_463_out, nand_360_out, nand_361_out);
  nand nand_464 (nand_464_out, nand_362_out, I[1]);
  nand nand_465 (nand_465_out, nand_363_out, nand_364_out);
  nand nand_466 (nand_466_out, nand_365_out, I[1]);
  nand nand_467 (nand_467_out, nand_366_out, nand_367_out);
  nand nand_468 (nand_468_out, nand_368_out, I[1]);
  nand nand_469 (nand_469_out, nand_369_out, nand_370_out);
  nand nand_470 (nand_470_out, nand_371_out, nand_372_out);
  nand nand_471 (nand_471_out, nand_373_out, nand_374_out);
  nand nand_472 (nand_472_out, nand_375_out, nand_376_out);
  nand nand_473 (nand_473_out, I[3], nand_377_out);
  nand nand_474 (nand_474_out, I[3], nand_378_out);
  nand nand_475 (nand_475_out, nand_379_out, nand_380_out);
  nand nand_476 (nand_476_out, nand_381_out, nand_382_out);
  nand nand_477 (nand_477_out, nand_383_out, nand_384_out);
  nand nand_478 (nand_478_out, nand_385_out, nand_386_out);
  nand nand_479 (nand_479_out, I[3], nand_387_out);
  nand nand_480 (nand_480_out, I[3], nand_388_out);
  nand nand_481 (nand_481_out, nand_389_out, nand_390_out);
  nand nand_482 (nand_482_out, nand_391_out, nand_392_out);
  nand nand_483 (nand_483_out, nand_393_out, nand_394_out);
  nand nand_484 (nand_484_out, nand_395_out, nand_396_out);
  nand nand_485 (nand_485_out, nand_397_out, nand_398_out);
  nand nand_486 (nand_486_out, nand_399_out, nand_400_out);
  nand nand_487 (nand_487_out, nand_401_out, nand_402_out);
  nand nand_488 (nand_488_out, nand_403_out, nand_404_out);
  nand nand_489 (nand_489_out, nand_405_out, nand_406_out);
  nand nand_490 (nand_490_out, nand_407_out, nand_408_out);
  nand nand_491 (nand_491_out, nand_409_out, nand_410_out);
  nand nand_492 (nand_492_out, nand_411_out, nand_412_out);
  nand nand_493 (nand_493_out, nand_413_out, nand_414_out);
  nand nand_494 (nand_494_out, nand_415_out, nand_416_out);
  nand nand_495 (nand_495_out, nand_417_out, nand_418_out);
  nand nand_496 (nand_496_out, nand_419_out, nand_420_out);
  nand nand_497 (nand_497_out, nand_421_out, nand_422_out);
  nand nand_498 (nand_498_out, nand_423_out, nand_424_out);
  nand nand_499 (nand_499_out, nand_425_out, nand_426_out);
  nand nand_500 (nand_500_out, nand_427_out, nand_428_out);
  nand nand_501 (nand_501_out, nand_429_out, nand_430_out);
  nand nand_502 (nand_502_out, nand_431_out, nand_432_out);
  nand nand_503 (nand_503_out, nand_433_out, nand_434_out);
  nand nand_504 (nand_504_out, nand_435_out, nand_436_out);
  nand nand_505 (nand_505_out, nand_437_out, nand_438_out);
  nand nand_506 (nand_506_out, nand_439_out, nand_440_out);
  nand nand_507 (nand_507_out, nand_441_out, nand_442_out);
  nand nand_508 (nand_508_out, nand_443_out, nand_444_out);
  nand nand_509 (nand_509_out, nand_445_out, nand_446_out);
  nand nand_510 (nand_510_out, nand_447_out, nand_448_out);
  nand nand_511 (nand_511_out, nand_449_out, nand_450_out);
  nand nand_512 (nand_512_out, nand_451_out, nand_452_out);
  nand nand_513 (nand_513_out, nand_453_out, nand_454_out);
  nand nand_514 (nand_514_out, nand_455_out, nand_456_out);
  nand nand_515 (nand_515_out, nand_457_out, nand_458_out);
  nand nand_516 (nand_516_out, nand_459_out, nand_460_out);
  nand nand_517 (nand_517_out, nand_461_out, nand_462_out);
  nand nand_518 (nand_518_out, nand_463_out, nand_464_out);
  nand nand_519 (nand_519_out, nand_465_out, nand_466_out);
  nand nand_520 (nand_520_out, nand_467_out, nand_468_out);
  nand nand_521 (nand_521_out, nand_469_out, nand_470_out);
  nand nand_522 (nand_522_out, nand_471_out, nand_472_out);
  nand nand_523 (nand_523_out, nand_473_out, nand_474_out);
  nand nand_524 (nand_524_out, I[0], I[0]);
  nand nand_525 (nand_525_out, nand_475_out, nand_476_out);
  nand nand_526 (nand_526_out, nand_477_out, nand_478_out);
  nand nand_527 (nand_527_out, nand_479_out, nand_480_out);
  nand nand_528 (nand_528_out, I[0], I[0]);
  nand nand_529 (nand_529_out, nand_481_out, nand_482_out);
  nand nand_530 (nand_530_out, nand_483_out, nand_484_out);
  nand nand_531 (nand_531_out, nand_485_out, nand_486_out);
  nand nand_532 (nand_532_out, nand_487_out, nand_488_out);
  nand nand_533 (nand_533_out, nand_489_out, nand_490_out);
  nand nand_534 (nand_534_out, nand_491_out, nand_492_out);
  nand nand_535 (nand_535_out, nand_493_out, nand_494_out);
  nand nand_536 (nand_536_out, nand_495_out, nand_496_out);
  nand nand_537 (nand_537_out, nand_497_out, nand_498_out);
  nand nand_538 (nand_538_out, nand_499_out, nand_500_out);
  nand nand_539 (nand_539_out, nand_501_out, nand_502_out);
  nand nand_540 (nand_540_out, nand_503_out, nand_504_out);
  nand nand_541 (nand_541_out, nand_505_out, nand_506_out);
  nand nand_542 (nand_542_out, nand_507_out, nand_508_out);
  nand nand_543 (nand_543_out, nand_509_out, nand_510_out);
  nand nand_544 (nand_544_out, nand_511_out, nand_512_out);
  nand nand_545 (nand_545_out, nand_513_out, nand_514_out);
  nand nand_546 (nand_546_out, nand_515_out, nand_516_out);
  nand nand_547 (nand_547_out, nand_517_out, nand_518_out);
  nand nand_548 (nand_548_out, nand_519_out, nand_520_out);
  nand nand_549 (nand_549_out, nand_521_out, nand_522_out);
  nand nand_550 (nand_550_out, nand_523_out, nand_524_out);
  nand nand_551 (nand_551_out, nand_525_out, nand_526_out);
  nand nand_552 (nand_552_out, nand_527_out, nand_528_out);
  nand nand_553 (nand_553_out, nand_529_out, nand_530_out);
  nand nand_554 (nand_554_out, nand_531_out, nand_532_out);
  nand nand_555 (nand_555_out, nand_533_out, nand_534_out);
  nand nand_556 (nand_556_out, nand_535_out, nand_536_out);
  nand nand_557 (nand_557_out, nand_537_out, nand_538_out);
  nand nand_558 (nand_558_out, nand_539_out, nand_540_out);
  nand nand_559 (nand_559_out, nand_541_out, nand_542_out);
  nand nand_560 (nand_560_out, nand_543_out, nand_544_out);
  nand nand_561 (nand_561_out, nand_545_out, nand_546_out);
  nand nand_562 (nand_562_out, nand_547_out, nand_548_out);
  nand nand_563 (nand_563_out, nand_549_out, nand_550_out);
  nand nand_564 (nand_564_out, nand_551_out, nand_552_out);
  nand nand_565 (nand_565_out, nand_553_out, nand_554_out);
  nand nand_566 (nand_566_out, nand_555_out, nand_556_out);
  nand nand_567 (nand_567_out, nand_557_out, nand_558_out);
  nand nand_568 (nand_568_out, nand_559_out, nand_560_out);
  nand nand_569 (nand_569_out, nand_561_out, nand_562_out);
  nand nand_570 (nand_570_out, nand_563_out, nand_564_out);
  nand nand_571 (nand_571_out, nand_565_out, nand_566_out);
  nand nand_572 (nand_572_out, nand_567_out, nand_568_out);
  nand nand_573 (a, nand_569_out, nand_570_out);
  nand nand_574 (d, nand_571_out, nand_572_out);
endmodule

module transition_logic (
  input  C_3,
  input  C_2,
  input  C_1,
  input  C_0,
  input  B_1,
  input  B_0,
  input  DS_9,
  input  DS_8,
  input  DS_7,
  input  DS_6,
  input  DS_5,
  input  DS_4,
  input  DS_3,
  input  DS_2,
  input  DS_1,
  input  DS_0,
  output S_3,
  output S_2,
  output S_1,
  output S_0,
  output [11:0] input_bus
);

  wire in_impeach_1_o_0, in_impeach_1_o_1;

  in_impeach in_impeach_1 (
    .B_1(B_1), .B_0(B_0), .DS_9(DS_9), .DS_8(DS_8), .DS_7(DS_7), .DS_6(DS_6), .DS_5(DS_5), .DS_4(DS_4),
    .DS_3(DS_3), .DS_2(DS_2), .DS_1(DS_1), .DS_0(DS_0), .O_1(in_impeach_1_o_1), .O_0(in_impeach_1_o_0));
  transition_logic_half transition_logic_half_1 (
    .C_3(C_3), .C_2(C_2), .C_1(C_1), .C_0(C_0), .B_1(in_impeach_1_o_1), .B_0(in_impeach_1_o_0), .S_3(S_3),
    .S_2(S_2), .S_1(S_1), .S_0(S_0));

  assign input_bus = {B_1, B_0, DS_9, DS_8, DS_7, DS_6, DS_5, DS_4, DS_3, DS_2, DS_1, DS_0};
endmodule

module transition_logic_half (
  input  C_3,
  input  C_2,
  input  C_1,
  input  C_0,
  input  B_1,
  input  B_0,
  output S_3,
  output S_2,
  output S_1,
  output S_0
);

  wire nand_1_out, nand_2_out, nand_3_out, nand_4_out, nand_5_out, nand_6_out, nand_7_out, nand_8_out,
       nand_9_out, nand_10_out, nand_11_out, nand_12_out, nand_13_out, nand_14_out, nand_15_out, nand_16_out,
       nand_17_out, nand_18_out, nand_19_out, nand_20_out, nand_21_out, nand_22_out, nand_23_out,
       nand_24_out, nand_25_out, nand_26_out, nand_27_out, nand_28_out, nand_29_out, nand_30_out,
       nand_31_out, nand_32_out, nand_33_out, nand_34_out, nand_35_out, nand_36_out, nand_37_out,
       nand_38_out, nand_39_out, nand_40_out, nand_41_out, nand_42_out, nand_43_out, nand_44_out,
       nand_45_out, nand_46_out, nand_47_out, nand_48_out, nand_49_out, nand_50_out, nand_51_out,
       nand_52_out, nand_53_out, nand_54_out, nand_55_out, nand_56_out, nand_57_out, nand_58_out,
       nand_59_out, nand_60_out, nand_61_out, nand_62_out, nand_63_out, nand_64_out, nand_65_out,
       nand_66_out, nand_67_out, nand_68_out, nand_69_out, nand_70_out, nand_71_out, nand_72_out,
       nand_73_out, nand_74_out, nand_75_out, nand_76_out, nand_77_out, nand_78_out, nand_79_out,
       nand_80_out, nand_81_out, nand_82_out, nand_83_out, nand_84_out, nand_85_out, nand_86_out,
       nand_87_out, nand_88_out, nand_89_out, nand_90_out, nand_91_out, nand_92_out, nand_93_out,
       nand_94_out, nand_95_out, nand_96_out, nand_97_out, nand_98_out, nand_99_out, nand_100_out,
       nand_101_out, nand_102_out, nand_103_out, nand_104_out, nand_105_out, nand_106_out, nand_107_out,
       nand_108_out, nand_109_out, nand_110_out, nand_112_out, nand_113_out, nand_114_out, nand_115_out;

  nand nand_1 (nand_1_out, C_2, C_2);
  nand nand_2 (nand_2_out, C_1, C_1);
  nand nand_3 (nand_3_out, C_0, C_0);
  nand nand_4 (nand_4_out, B_1, B_1);
  nand nand_5 (nand_5_out, B_1, B_1);
  nand nand_6 (nand_6_out, nand_1_out, C_1);
  nand nand_7 (nand_7_out, C_2, nand_2_out);
  nand nand_8 (nand_8_out, nand_3_out, nand_4_out);
  nand nand_9 (nand_9_out, C_0, nand_5_out);
  nand nand_10 (nand_10_out, C_1, C_0);
  nand nand_11 (nand_11_out, C_2, C_0);
  nand nand_12 (nand_12_out, nand_6_out, nand_6_out);
  nand nand_13 (nand_13_out, C_0, C_0);
  nand nand_14 (nand_14_out, B_0, B_0);
  nand nand_15 (nand_15_out, C_3, C_3);
  nand nand_16 (nand_16_out, C_2, C_2);
  nand nand_17 (nand_17_out, B_0, B_0);
  nand nand_18 (nand_18_out, B_1, B_1);
  nand nand_19 (nand_19_out, C_3, C_3);
  nand nand_20 (nand_20_out, C_2, C_2);
  nand nand_21 (nand_21_out, nand_7_out, nand_7_out);
  nand nand_22 (nand_22_out, C_0, C_0);
  nand nand_23 (nand_23_out, B_0, B_0);
  nand nand_24 (nand_24_out, nand_8_out, nand_8_out);
  nand nand_25 (nand_25_out, nand_9_out, nand_9_out);
  nand nand_26 (nand_26_out, B_0, B_0);
  nand nand_27 (nand_27_out, nand_10_out, nand_10_out);
  nand nand_28 (nand_28_out, B_0, B_0);
  nand nand_29 (nand_29_out, nand_11_out, nand_11_out);
  nand nand_30 (nand_30_out, B_0, B_0);
  nand nand_31 (nand_31_out, B_0, B_0);
  nand nand_32 (nand_32_out, nand_12_out, nand_13_out);
  nand nand_33 (nand_33_out, B_1, nand_14_out);
  nand nand_34 (nand_34_out, nand_15_out, C_2);
  nand nand_35 (nand_35_out, nand_16_out, C_0);
  nand nand_36 (nand_36_out, B_1, nand_17_out);
  nand nand_37 (nand_37_out, C_1, nand_18_out);
  nand nand_38 (nand_38_out, nand_19_out, C_1);
  nand nand_39 (nand_39_out, nand_20_out, C_1);
  nand nand_40 (nand_40_out, nand_21_out, nand_22_out);
  nand nand_41 (nand_41_out, B_1, nand_23_out);
  nand nand_42 (nand_42_out, nand_24_out, B_0);
  nand nand_43 (nand_43_out, nand_25_out, nand_26_out);
  nand nand_44 (nand_44_out, C_0, B_1);
  nand nand_45 (nand_45_out, nand_27_out, nand_28_out);
  nand nand_46 (nand_46_out, nand_29_out, nand_30_out);
  nand nand_47 (nand_47_out, C_2, C_1);
  nand nand_48 (nand_48_out, B_1, nand_31_out);
  nand nand_49 (nand_49_out, nand_32_out, nand_32_out);
  nand nand_50 (nand_50_out, nand_33_out, nand_33_out);
  nand nand_51 (nand_51_out, C_1, C_1);
  nand nand_52 (nand_52_out, B_1, B_1);
  nand nand_53 (nand_53_out, nand_34_out, nand_34_out);
  nand nand_54 (nand_54_out, nand_35_out, nand_35_out);
  nand nand_55 (nand_55_out, nand_36_out, nand_36_out);
  nand nand_56 (nand_56_out, nand_37_out, nand_37_out);
  nand nand_57 (nand_57_out, B_0, B_0);
  nand nand_58 (nand_58_out, nand_38_out, nand_38_out);
  nand nand_59 (nand_59_out, nand_39_out, nand_39_out);
  nand nand_60 (nand_60_out, nand_40_out, nand_40_out);
  nand nand_61 (nand_61_out, nand_41_out, nand_41_out);
  nand nand_62 (nand_62_out, nand_42_out, nand_43_out);
  nand nand_63 (nand_63_out, nand_44_out, nand_44_out);
  nand nand_64 (nand_64_out, nand_45_out, nand_46_out);
  nand nand_65 (nand_65_out, nand_47_out, nand_47_out);
  nand nand_66 (nand_66_out, nand_48_out, nand_48_out);
  nand nand_67 (nand_67_out, nand_49_out, nand_50_out);
  nand nand_68 (nand_68_out, C_2, nand_51_out);
  nand nand_69 (nand_69_out, C_2, nand_52_out);
  nand nand_70 (nand_70_out, nand_53_out, B_0);
  nand nand_71 (nand_71_out, C_2, C_0);
  nand nand_72 (nand_72_out, C_3, C_2);
  nand nand_73 (nand_73_out, nand_54_out, nand_55_out);
  nand nand_74 (nand_74_out, nand_56_out, nand_57_out);
  nand nand_75 (nand_75_out, nand_58_out, B_0);
  nand nand_76 (nand_76_out, nand_59_out, B_0);
  nand nand_77 (nand_77_out, C_1, C_0);
  nand nand_78 (nand_78_out, nand_60_out, nand_61_out);
  nand nand_79 (nand_79_out, C_3, C_2);
  nand nand_80 (nand_80_out, C_1, B_1);
  nand nand_81 (nand_81_out, nand_62_out, nand_62_out);
  nand nand_82 (nand_82_out, nand_63_out, B_0);
  nand nand_83 (nand_83_out, nand_64_out, nand_64_out);
  nand nand_84 (nand_84_out, nand_65_out, nand_66_out);
  nand nand_85 (nand_85_out, nand_67_out, nand_68_out);
  nand nand_86 (nand_86_out, nand_69_out, nand_69_out);
  nand nand_87 (nand_87_out, B_0, B_0);
  nand nand_88 (nand_88_out, nand_70_out, nand_71_out);
  nand nand_89 (nand_89_out, nand_72_out, nand_72_out);
  nand nand_90 (nand_90_out, nand_73_out, nand_74_out);
  nand nand_91 (nand_91_out, nand_75_out, nand_76_out);
  nand nand_92 (nand_92_out, nand_77_out, nand_78_out);
  nand nand_93 (nand_93_out, nand_79_out, nand_79_out);
  nand nand_94 (nand_94_out, nand_80_out, nand_80_out);
  nand nand_95 (nand_95_out, nand_81_out, nand_82_out);
  nand nand_96 (nand_96_out, nand_83_out, nand_84_out);
  nand nand_97 (nand_97_out, nand_85_out, nand_85_out);
  nand nand_98 (nand_98_out, nand_86_out, nand_87_out);
  nand nand_99 (nand_99_out, nand_88_out, nand_88_out);
  nand nand_100 (nand_100_out, nand_89_out, B_1);
  nand nand_101 (nand_101_out, nand_90_out, nand_90_out);
  nand nand_102 (nand_102_out, nand_91_out, nand_91_out);
  nand nand_103 (nand_103_out, nand_92_out, nand_92_out);
  nand nand_104 (nand_104_out, nand_93_out, nand_94_out);
  nand nand_105 (nand_105_out, nand_95_out, nand_95_out);
  nand nand_106 (nand_106_out, nand_96_out, nand_96_out);
  nand nand_107 (nand_107_out, nand_97_out, nand_98_out);
  nand nand_108 (nand_108_out, nand_99_out, nand_100_out);
  nand nand_109 (nand_109_out, nand_101_out, nand_102_out);
  nand nand_110 (nand_110_out, nand_103_out, nand_104_out);
  nand nand_111 (S_0, nand_105_out, nand_106_out);
  nand nand_112 (nand_112_out, nand_107_out, nand_107_out);
  nand nand_113 (nand_113_out, nand_108_out, nand_108_out);
  nand nand_114 (nand_114_out, nand_109_out, nand_109_out);
  nand nand_115 (nand_115_out, nand_110_out, nand_110_out);
  nand nand_116 (S_2, nand_112_out, nand_113_out);
  nand nand_117 (S_1, nand_114_out, nand_115_out);

  assign S_3 = 1'b0;
endmodule

module in_impeach (
  input  B_1,
  input  B_0,
  input  DS_9,
  input  DS_8,
  input  DS_7,
  input  DS_6,
  input  DS_5,
  input  DS_4,
  input  DS_3,
  input  DS_2,
  input  DS_1,
  input  DS_0,
  output O_1,
  output O_0
);

  wire nand_1_out, nand_2_out, nand_3_out, nand_4_out, nand_5_out, nand_6_out, nand_7_out, nand_8_out,
       nand_9_out, nand_10_out, nand_11_out, nand_12_out, nand_13_out, nand_14_out, nand_15_out, nand_16_out,
       nand_17_out, nand_18_out, nand_19_out, nand_20_out, nand_21_out, nand_22_out, nand_23_out,
       nand_24_out, nand_25_out, nand_26_out, nand_27_out, nand_28_out, nand_29_out, nand_30_out,
       nand_31_out, nand_32_out, nand_33_out, nand_34_out, nand_35_out, nand_36_out, nand_37_out,
       nand_38_out, nand_39_out, nand_40_out, nand_41_out, nand_42_out, nand_43_out, nand_44_out,
       nand_45_out, nand_46_out, nand_47_out, nand_48_out, nand_49_out, nand_50_out, nand_51_out,
       nand_52_out, nand_53_out, nand_54_out, nand_55_out, nand_56_out, nand_57_out, nand_58_out;

  nand nand_1 (nand_1_out, DS_0, DS_0);
  nand nand_2 (nand_2_out, DS_1, DS_1);
  nand nand_3 (nand_3_out, DS_3, DS_3);
  nand nand_4 (nand_4_out, DS_4, DS_4);
  nand nand_5 (nand_5_out, DS_6, DS_6);
  nand nand_6 (nand_6_out, DS_7, DS_7);
  nand nand_7 (nand_7_out, DS_0, DS_0);
  nand nand_8 (nand_8_out, DS_1, DS_1);
  nand nand_9 (nand_9_out, DS_3, DS_3);
  nand nand_10 (nand_10_out, DS_4, DS_4);
  nand nand_11 (nand_11_out, DS_6, DS_6);
  nand nand_12 (nand_12_out, DS_7, DS_7);
  nand nand_13 (nand_13_out, nand_1_out, nand_2_out);
  nand nand_14 (nand_14_out, nand_3_out, nand_4_out);
  nand nand_15 (nand_15_out, nand_5_out, nand_6_out);
  nand nand_16 (nand_16_out, nand_7_out, nand_8_out);
  nand nand_17 (nand_17_out, nand_9_out, nand_10_out);
  nand nand_18 (nand_18_out, nand_11_out, nand_12_out);
  nand nand_19 (nand_19_out, nand_13_out, nand_13_out);
  nand nand_20 (nand_20_out, DS_2, DS_2);
  nand nand_21 (nand_21_out, nand_14_out, nand_14_out);
  nand nand_22 (nand_22_out, DS_5, DS_5);
  nand nand_23 (nand_23_out, nand_15_out, nand_15_out);
  nand nand_24 (nand_24_out, DS_8, DS_8);
  nand nand_25 (nand_25_out, DS_9, DS_9);
  nand nand_26 (nand_26_out, nand_16_out, nand_16_out);
  nand nand_27 (nand_27_out, DS_2, DS_2);
  nand nand_28 (nand_28_out, nand_17_out, nand_17_out);
  nand nand_29 (nand_29_out, DS_5, DS_5);
  nand nand_30 (nand_30_out, nand_18_out, nand_18_out);
  nand nand_31 (nand_31_out, DS_8, DS_8);
  nand nand_32 (nand_32_out, DS_9, DS_9);
  nand nand_33 (nand_33_out, nand_19_out, nand_20_out);
  nand nand_34 (nand_34_out, nand_21_out, nand_22_out);
  nand nand_35 (nand_35_out, nand_23_out, nand_24_out);
  nand nand_36 (nand_36_out, nand_25_out, B_1);
  nand nand_37 (nand_37_out, nand_26_out, nand_27_out);
  nand nand_38 (nand_38_out, nand_28_out, nand_29_out);
  nand nand_39 (nand_39_out, nand_30_out, nand_31_out);
  nand nand_40 (nand_40_out, nand_32_out, B_0);
  nand nand_41 (nand_41_out, nand_33_out, nand_33_out);
  nand nand_42 (nand_42_out, nand_34_out, nand_34_out);
  nand nand_43 (nand_43_out, nand_35_out, nand_35_out);
  nand nand_44 (nand_44_out, nand_36_out, nand_36_out);
  nand nand_45 (nand_45_out, nand_37_out, nand_37_out);
  nand nand_46 (nand_46_out, nand_38_out, nand_38_out);
  nand nand_47 (nand_47_out, nand_39_out, nand_39_out);
  nand nand_48 (nand_48_out, nand_40_out, nand_40_out);
  nand nand_49 (nand_49_out, nand_41_out, nand_42_out);
  nand nand_50 (nand_50_out, nand_43_out, nand_44_out);
  nand nand_51 (nand_51_out, nand_45_out, nand_46_out);
  nand nand_52 (nand_52_out, nand_47_out, nand_48_out);
  nand nand_53 (nand_53_out, nand_49_out, nand_49_out);
  nand nand_54 (nand_54_out, nand_50_out, nand_50_out);
  nand nand_55 (nand_55_out, nand_51_out, nand_51_out);
  nand nand_56 (nand_56_out, nand_52_out, nand_52_out);
  nand nand_57 (nand_57_out, nand_53_out, nand_54_out);
  nand nand_58 (nand_58_out, nand_55_out, nand_56_out);
  nand nand_59 (O_1, nand_57_out, nand_57_out);
  nand nand_60 (O_0, nand_58_out, nand_58_out);
endmodule

module memory_time (
  input  [29:0] I_0,
  input  clock_in,
  input  reset,
  input  [3:0] load,
  output carry,
  output [29:0] O_0
);

  wire and_1_out, clock_1_out, comparator_1_eq, comparator_2_eq, comparator_3_eq, comparator_4_eq,
       multiplexer_1_out, or_1_out;
  wire [5:0] binary_to_time_converter_1_output_bus_1, binary_to_time_converter_2_output_bus_1,
       binary_to_time_converter_3_output_bus_1, counter_1_q, counter_2_q, counter_3_q;

  Comparator #(.width(4)) comparator_1 (.a(load), .b(4'b0011), .eq(comparator_1_eq));  // open: gt, lt
  Comparator #(.width(4)) comparator_2 (.a(load), .b(4'b0111), .eq(comparator_2_eq));  // open: gt, lt
  binary_to_time_converter binary_to_time_converter_1 (
    .Input_bus_1(I_0[29:25]), .Input_bus_2(I_0[24:20]), .Output_bus_1(binary_to_time_converter_1_output_bus_1));
  binary_to_time_converter binary_to_time_converter_2 (
    .Input_bus_1(I_0[19:15]), .Input_bus_2(I_0[14:10]), .Output_bus_1(binary_to_time_converter_2_output_bus_1));
  binary_to_time_converter binary_to_time_converter_3 (
    .Input_bus_1(I_0[9:5]), .Input_bus_2(I_0[4:0]), .Output_bus_1(binary_to_time_converter_3_output_bus_1));
  Clock #(.highDuration(40), .lowDuration(40)) clock_1 (.out(clock_1_out));
  or or_1 (or_1_out, comparator_1_eq, comparator_2_eq);
  Multiplexer #(.enable("false")) multiplexer_1 (
    .in0(clock_in), .in1(clock_1_out), .out(multiplexer_1_out), .sel(or_1_out));
  Counter #(.width(6), .max('h17)) counter_1 (
    .clr(reset), .load(or_1_out), .up(1'b1), .count(and_1_out), .clk(multiplexer_1_out),
    .D(binary_to_time_converter_1_output_bus_1), .Q(counter_1_q));  // open: carry
  Counter #(.width(6), .max('h3b)) counter_2 (
    .clr(reset), .load(or_1_out), .up(1'b1), .count(comparator_3_eq), .clk(multiplexer_1_out),
    .D(binary_to_time_converter_2_output_bus_1), .Q(counter_2_q));  // open: carry
  Counter #(.width(6), .max('h3b)) counter_3 (
    .clr(reset), .load(or_1_out), .up(1'b1), .count(1'b1), .clk(multiplexer_1_out),
    .D(binary_to_time_converter_3_output_bus_1), .Q(counter_3_q));  // open: carry
  Comparator #(.width(6)) comparator_3 (.a(6'b111011), .b(counter_3_q), .eq(comparator_3_eq));  // open: gt, lt
  and and_1 (and_1_out, comparator_4_eq, comparator_3_eq);
  Comparator #(.width(6)) comparator_4 (.a(6'b111011), .b(counter_2_q), .eq(comparator_4_eq));  // open: gt, lt
  Comparator #(.width(6)) comparator_5 (.a(6'b010111), .b(counter_1_q), .eq(carry));  // open: gt, lt
  time_to_binary_converter time_to_binary_converter_1 (.t_in(counter_1_q), .O_1(O_0[29:25]), .O_0(O_0[24:20]));
  time_to_binary_converter time_to_binary_converter_2 (.t_in(counter_2_q), .O_1(O_0[19:15]), .O_0(O_0[14:10]));
  time_to_binary_converter time_to_binary_converter_3 (.t_in(counter_3_q), .O_1(O_0[9:5]), .O_0(O_0[4:0]));
endmodule

module inc_6bits (
  input  I_5,
  input  I_4,
  input  I_3,
  input  I_2,
  input  I_1,
  input  I_0,
  input  c_in,
  output c_out,
  output O_5,
  output O_4,
  output O_3,
  output O_2,
  output O_1,
  output O_0
);

  wire half_adder_2_ci, half_adder_3_ci, half_adder_4_ci, half_adder_5_ci, half_adder_6_ci;

  half_adder half_adder_1 (.ai(I_5), .bi(half_adder_2_ci), .si(O_5), .ci(c_out));
  half_adder half_adder_2 (.ai(I_4), .bi(half_adder_3_ci), .si(O_4), .ci(half_adder_2_ci));
  half_adder half_adder_3 (.ai(I_3), .bi(half_adder_4_ci), .si(O_3), .ci(half_adder_3_ci));
  half_adder half_adder_4 (.ai(I_2), .bi(half_adder_5_ci), .si(O_2), .ci(half_adder_4_ci));
  half_adder half_adder_5 (.ai(I_1), .bi(half_adder_6_ci), .si(O_1), .ci(half_adder_5_ci));
  half_adder half_adder_6 (.ai(I_0), .bi(c_in), .si(O_0), .ci(half_adder_6_ci));
endmodule

module half_adder (
  input  ai,
  input  bi,
  output si,
  output ci
);

  xor xor_1 (si, ai, bi);
  and and_1 (ci, ai, bi);
endmodule

module full_adder (
  input  ai,
  input  bi,
  input  ciminus1,
  output si,
  output ci
);

  wire and_4_out, nand_1_out, nand_2_out, nand_3_out, xor_1_out;

  xor xor_1 (xor_1_out, ai, bi);
  // AND_Gate and_1 has open pins: in0=ai, in1=bi, out=open
  nand nand_1 (nand_1_out, ai, bi);
  nand nand_2 (nand_2_out, ai, ciminus1);
  // AND_Gate and_2 has open pins: in0=ai, in1=ciminus1, out=open
  // AND_Gate and_3 has open pins: in0=bi, in1=ciminus1, out=open
  nand nand_3 (nand_3_out, bi, ciminus1);
  xor xor_2 (si, xor_1_out, ciminus1);
  and and_4 (and_4_out, nand_1_out, nand_2_out);
  nand nand_4 (ci, and_4_out, nand_3_out);
endmodule

module set_time_setter (
  input  [29:0] I_0,
  input  [11:0] input_bus,
  input  mode_on,
  input  R,
  output [29:0] O_0
);

  wire not_1_out;

  not not_1 (not_1_out, mode_on);
  set_time_to_23 set_time_to_23_1 (
    .R(R), .B_1(input_bus[11]), .B_0(input_bus[10]), .load(not_1_out), .set_on(input_bus[4]),
    .I_1(I_0[29:25]), .I_0(I_0[24:20]), .O_1(O_0[29:25]), .O_0(O_0[24:20]));
  set_time_to_5 set_time_to_5_1 (
    .R(R), .B_1(input_bus[11]), .B_0(input_bus[10]), .load(not_1_out), .set_on(input_bus[3]),
    .I_0(I_0[19:15]), .O_0(O_0[19:15]));
  set_time_to_9 set_time_to_9_1 (
    .R(R), .B_1(input_bus[11]), .B_0(input_bus[10]), .load(not_1_out), .set_on(input_bus[2]),
    .I_0(I_0[14:10]), .O_0(O_0[14:10]));
  set_time_to_5 set_time_to_5_2 (
    .R(R), .B_1(input_bus[11]), .B_0(input_bus[10]), .load(not_1_out), .set_on(input_bus[1]), .I_0(I_0[9:5]),
    .O_0(O_0[9:5]));
  set_time_to_9 set_time_to_9_2 (
    .R(R), .B_1(input_bus[11]), .B_0(input_bus[10]), .load(not_1_out), .set_on(input_bus[0]), .I_0(I_0[4:0]),
    .O_0(O_0[4:0]));
endmodule

module set_time_to_9 (
  input  R,
  input  B_1,
  input  B_0,
  input  load,
  input  set_on,
  input  [4:0] I_0,
  output [4:0] O_0
);

  wire and_1_out, clock_1_out, or_1_out;

  Clock clock_1 (.out(clock_1_out));
  or or_1 (or_1_out, B_1, B_0);
  and and_1 (and_1_out, or_1_out, set_on);
  Counter #(.width(5), .max('h9)) counter_1 (
    .clr(R), .load(load), .up(B_0), .count(and_1_out), .clk(clock_1_out), .D(I_0), .Q(O_0));  // open: carry
endmodule

module set_time_to_5 (
  input  R,
  input  B_1,
  input  B_0,
  input  load,
  input  set_on,
  input  [4:0] I_0,
  output [4:0] O_0
);

  wire and_1_out, C_out, or_1_out;

  Clock C (.out(C_out));
  or or_1 (or_1_out, B_1, B_0);
  and and_1 (and_1_out, or_1_out, set_on);
  Counter #(.width(5), .max('h5)) counter_1 (
    .clr(R), .load(load), .up(B_0), .count(and_1_out), .clk(C_out), .D(I_0), .Q(O_0));  // open: carry
endmodule

module set_time_to_23 (
  input  R,
  input  B_1,
  input  B_0,
  input  load,
  input  set_on,
  input  [4:0] I_1,
  input  [4:0] I_0,
  output [4:0] O_1,
  output [4:0] O_0
);

  wire and_1_out, and_2_out, and_3_out, and_4_out, and_5_out, and_6_out, C_out, comparator_1_eq,
       comparator_2_eq, counter_1_carry, counter_2_carry, or_1_out, or_2_out, or_3_out, or_4_out;
  wire [4:0] multiplexer_1_out, multiplexer_2_out;

  Clock C (.out(C_out));
  or or_1 (or_1_out, B_1, B_0);
  and and_1 (and_1_out, or_1_out, set_on);
  or or_2 (or_2_out, and_2_out, and_5_out, and_3_out);
  and and_2 (and_2_out, and_1_out, counter_2_carry);
  or or_3 (or_3_out, and_3_out, and_5_out);
  or or_4 (or_4_out, or_3_out, load);
  Multiplexer #(.width(5), .enable("false")) multiplexer_1 (
    .in0(I_0), .in1(multiplexer_2_out), .out(multiplexer_1_out), .sel(or_3_out));
  Multiplexer #(.width(5), .enable("false")) multiplexer_2 (
    .in0({5{1'b0}}), .in1(5'b00011), .out(multiplexer_2_out), .sel(and_5_out));
  Counter #(.width(5), .max('h2)) counter_1 (
    .clr(R), .load(load), .up(B_0), .count(or_2_out), .clk(C_out), .D(I_1), .carry(counter_1_carry), .Q(O_1));
  and and_3 (and_3_out, counter_1_carry, and_4_out);
  and and_4 (and_4_out, comparator_2_eq, ~B_1, B_0, set_on);  // AND_Gate
  and and_5 (and_5_out, counter_1_carry, and_6_out);
  and and_6 (and_6_out, ~B_0, B_1, comparator_1_eq, set_on);  // AND_Gate
  Counter #(.width(5), .max('h9)) counter_2 (
    .clr(R), .load(or_4_out), .up(B_0), .count(and_1_out), .clk(C_out), .D(multiplexer_1_out),
    .carry(counter_2_carry), .Q(O_0));
  Comparator #(.width(5)) comparator_1 (.a({5{1'b0}}), .b(O_0), .eq(comparator_1_eq));  // open: gt, lt
  Comparator #(.width(5)) comparator_2 (.a(5'b00011), .b(O_0), .eq(comparator_2_eq));  // open: gt, lt
endmodule
module time_to_binary_converter (
  input  [5:0] t_in,
  output [4:0] O_1,
  output [4:0] O_0
);

  wire nand_1_out, nand_2_out, nand_3_out, nand_4_out, nand_5_out, nand_6_out, nand_7_out, nand_8_out,
       nand_9_out, nand_10_out, nand_11_out, nand_12_out, nand_13_out, nand_14_out, nand_15_out, nand_16_out,
       nand_17_out, nand_18_out, nand_19_out, nand_20_out, nand_21_out, nand_22_out, nand_23_out,
       nand_24_out, nand_25_out, nand_26_out, nand_27_out, nand_28_out, nand_29_out, nand_30_out,
       nand_31_out, nand_32_out, nand_33_out, nand_34_out, nand_35_out, nand_36_out, nand_37_out,
       nand_38_out, nand_39_out, nand_40_out, nand_41_out, nand_42_out, nand_43_out, nand_44_out,
       nand_45_out, nand_46_out, nand_47_out, nand_48_out, nand_49_out, nand_50_out, nand_51_out,
       nand_52_out, nand_53_out, nand_54_out, nand_56_out, nand_57_out, nand_58_out, nand_59_out,
       nand_60_out, nand_61_out, nand_62_out, nand_63_out, nand_64_out, nand_65_out, nand_66_out,
       nand_67_out, nand_68_out, nand_69_out, nand_70_out, nand_71_out, nand_72_out, nand_73_out,
       nand_74_out, nand_75_out, nand_76_out, nand_77_out, nand_78_out, nand_79_out, nand_80_out,
       nand_81_out, nand_82_out, nand_83_out, nand_84_out, nand_85_out, nand_86_out, nand_87_out,
       nand_88_out, nand_89_out, nand_90_out, nand_91_out, nand_92_out, nand_93_out, nand_94_out,
       nand_95_out, nand_96_out, nand_97_out, nand_98_out, nand_99_out, nand_100_out, nand_101_out,
       nand_102_out, nand_103_out, nand_104_out, nand_105_out, nand_106_out, nand_107_out, nand_108_out,
       nand_109_out, nand_110_out, nand_111_out, nand_112_out, nand_113_out, nand_114_out, nand_115_out,
       nand_116_out, nand_117_out, nand_118_out, nand_119_out, nand_120_out, nand_121_out, nand_122_out,
       nand_123_out, nand_124_out, nand_125_out, nand_126_out, nand_127_out, nand_128_out, nand_129_out,
       nand_130_out, nand_131_out, nand_132_out, nand_133_out, nand_134_out, nand_135_out, nand_136_out,
       nand_137_out, nand_138_out, nand_139_out, nand_140_out, nand_141_out, nand_142_out, nand_143_out,
       nand_144_out, nand_145_out, nand_146_out, nand_147_out, nand_148_out, nand_149_out, nand_150_out,
       nand_151_out, nand_152_out, nand_153_out, nand_154_out, nand_155_out, nand_156_out, nand_157_out,
       nand_158_out, nand_159_out, nand_160_out, nand_161_out, nand_162_out, nand_163_out, nand_164_out,
       nand_165_out, nand_166_out, nand_167_out, nand_168_out, nand_169_out, nand_170_out, nand_171_out,
       nand_172_out, nand_173_out, nand_174_out, nand_175_out, nand_176_out, nand_177_out, nand_178_out,
       nand_179_out, nand_180_out, nand_181_out, nand_182_out, nand_183_out, nand_184_out, nand_185_out,
       nand_186_out, nand_187_out, nand_188_out, nand_189_out, nand_190_out, nand_191_out, nand_192_out,
       nand_193_out, nand_194_out, nand_195_out, nand_196_out, nand_197_out, nand_198_out, nand_199_out,
       nand_200_out, nand_201_out, nand_202_out, nand_203_out, nand_204_out, nand_205_out, nand_206_out,
       nand_207_out, nand_208_out, nand_209_out, nand_210_out, nand_211_out, nand_212_out, nand_213_out,
       nand_214_out, nand_215_out, nand_216_out, nand_217_out, nand_218_out, nand_219_out, nand_220_out,
       nand_221_out, nand_222_out, nand_223_out, nand_224_out, nand_225_out, nand_226_out, nand_227_out,
       nand_228_out, nand_229_out, nand_230_out, nand_231_out, nand_232_out, nand_233_out, nand_234_out,
       nand_235_out, nand_236_out, nand_237_out, nand_238_out, nand_239_out, nand_240_out, nand_241_out,
       nand_242_out, nand_243_out, nand_244_out, nand_245_out, nand_246_out, nand_247_out, nand_248_out,
       nand_249_out, nand_250_out, nand_251_out, nand_252_out, nand_253_out, nand_254_out, nand_255_out,
       nand_256_out, nand_257_out, nand_258_out, nand_259_out, nand_260_out, nand_261_out, nand_262_out,
       nand_263_out, nand_264_out, nand_265_out, nand_266_out, nand_267_out, nand_268_out, nand_269_out,
       nand_270_out, nand_271_out, nand_272_out, nand_273_out, nand_274_out, nand_275_out, nand_276_out,
       nand_277_out, nand_278_out, nand_279_out, nand_280_out, nand_281_out, nand_282_out, nand_283_out,
       nand_284_out, nand_285_out, nand_286_out, nand_287_out, nand_288_out, nand_290_out, nand_291_out,
       nand_292_out, nand_293_out, nand_294_out, nand_295_out, nand_296_out, nand_297_out, nand_298_out,
       nand_299_out, nand_300_out, nand_301_out, nand_302_out, nand_303_out, nand_304_out, nand_305_out,
       nand_306_out, nand_307_out, nand_308_out, nand_309_out, nand_310_out, nand_311_out, nand_313_out,
       nand_314_out, nand_315_out, nand_316_out, nand_317_out, nand_318_out;

  nand nand_1 (nand_1_out, t_in[5], t_in[5]);
  nand nand_2 (nand_2_out, t_in[4], t_in[4]);
  nand nand_3 (nand_3_out, t_in[5], t_in[5]);
  nand nand_4 (nand_4_out, t_in[4], t_in[4]);
  nand nand_5 (nand_5_out, t_in[4], t_in[4]);
  nand nand_6 (nand_6_out, t_in[5], t_in[5]);
  nand nand_7 (nand_7_out, t_in[4], t_in[4]);
  nand nand_8 (nand_8_out, t_in[3], t_in[3]);
  nand nand_9 (nand_9_out, t_in[5], t_in[5]);
  nand nand_10 (nand_10_out, t_in[3], t_in[3]);
  nand nand_11 (nand_11_out, t_in[5], t_in[5]);
  nand nand_12 (nand_12_out, t_in[4], t_in[4]);
  nand nand_13 (nand_13_out, t_in[5], t_in[5]);
  nand nand_14 (nand_14_out, t_in[5], t_in[5]);
  nand nand_15 (nand_15_out, t_in[4], t_in[4]);
  nand nand_16 (nand_16_out, t_in[3], t_in[3]);
  nand nand_17 (nand_17_out, t_in[1], t_in[1]);
  nand nand_18 (nand_18_out, t_in[3], t_in[3]);
  nand nand_19 (nand_19_out, t_in[1], t_in[1]);
  nand nand_20 (nand_20_out, t_in[5], t_in[3]);
  nand nand_21 (nand_21_out, t_in[5], t_in[4]);
  nand nand_22 (nand_22_out, t_in[5], t_in[5]);
  nand nand_23 (nand_23_out, t_in[5], t_in[5]);
  nand nand_24 (nand_24_out, t_in[4], t_in[4]);
  nand nand_25 (nand_25_out, t_in[5], t_in[5]);
  nand nand_26 (nand_26_out, t_in[4], t_in[4]);
  nand nand_27 (nand_27_out, t_in[5], t_in[5]);
  nand nand_28 (nand_28_out, t_in[4], t_in[4]);
  nand nand_29 (nand_29_out, t_in[5], t_in[5]);
  nand nand_30 (nand_30_out, t_in[5], t_in[5]);
  nand nand_31 (nand_31_out, t_in[3], t_in[3]);
  nand nand_32 (nand_32_out, t_in[2], t_in[2]);
  nand nand_33 (nand_33_out, t_in[4], t_in[4]);
  nand nand_34 (nand_34_out, t_in[3], t_in[3]);
  nand nand_35 (nand_35_out, t_in[3], t_in[3]);
  nand nand_36 (nand_36_out, t_in[2], t_in[2]);
  nand nand_37 (nand_37_out, nand_1_out, nand_2_out);
  nand nand_38 (nand_38_out, nand_3_out, t_in[4]);
  nand nand_39 (nand_39_out, t_in[5], nand_4_out);
  nand nand_40 (nand_40_out, t_in[5], t_in[4]);
  nand nand_41 (nand_41_out, t_in[5], nand_5_out);
  nand nand_42 (nand_42_out, t_in[5], t_in[4]);
  nand nand_43 (nand_43_out, nand_6_out, nand_7_out);
  nand nand_44 (nand_44_out, nand_8_out, t_in[1]);
  nand nand_45 (nand_45_out, nand_9_out, nand_10_out);
  nand nand_46 (nand_46_out, t_in[2], t_in[1]);
  nand nand_47 (nand_47_out, nand_11_out, nand_12_out);
  nand nand_48 (nand_48_out, nand_13_out, t_in[4]);
  nand nand_49 (nand_49_out, nand_14_out, t_in[4]);
  nand nand_50 (nand_50_out, t_in[5], nand_15_out);
  nand nand_51 (nand_51_out, nand_16_out, nand_17_out);
  nand nand_52 (nand_52_out, t_in[5], nand_18_out);
  nand nand_53 (nand_53_out, t_in[2], nand_19_out);
  nand nand_54 (nand_54_out, t_in[5], t_in[4]);
  nand nand_55 (O_1[2], nand_20_out, nand_21_out);
  nand nand_56 (nand_56_out, nand_22_out, t_in[4]);
  nand nand_57 (nand_57_out, nand_23_out, t_in[4]);
  nand nand_58 (nand_58_out, t_in[4], t_in[3]);
  nand nand_59 (nand_59_out, t_in[5], nand_24_out);
  nand nand_60 (nand_60_out, nand_25_out, nand_26_out);
  nand nand_61 (nand_61_out, t_in[3], t_in[1]);
  nand nand_62 (nand_62_out, nand_27_out, nand_28_out);
  nand nand_63 (nand_63_out, t_in[3], t_in[2]);
  nand nand_64 (nand_64_out, nand_29_out, t_in[3]);
  nand nand_65 (nand_65_out, t_in[2], t_in[1]);
  nand nand_66 (nand_66_out, nand_30_out, t_in[4]);
  nand nand_67 (nand_67_out, nand_31_out, nand_32_out);
  nand nand_68 (nand_68_out, t_in[5], nand_33_out);
  nand nand_69 (nand_69_out, t_in[5], nand_34_out);
  nand nand_70 (nand_70_out, t_in[5], nand_35_out);
  nand nand_71 (nand_71_out, t_in[5], t_in[4]);
  nand nand_72 (nand_72_out, t_in[3], nand_36_out);
  nand nand_73 (nand_73_out, nand_37_out, nand_37_out);
  nand nand_74 (nand_74_out, t_in[2], t_in[2]);
  nand nand_75 (nand_75_out, t_in[1], t_in[1]);
  nand nand_76 (nand_76_out, nand_38_out, nand_38_out);
  nand nand_77 (nand_77_out, t_in[3], t_in[3]);
  nand nand_78 (nand_78_out, t_in[2], t_in[2]);
  nand nand_79 (nand_79_out, t_in[5], t_in[5]);
  nand nand_80 (nand_80_out, nand_39_out, nand_39_out);
  nand nand_81 (nand_81_out, t_in[3], t_in[3]);
  nand nand_82 (nand_82_out, nand_40_out, nand_40_out);
  nand nand_83 (nand_83_out, t_in[3], t_in[3]);
  nand nand_84 (nand_84_out, t_in[2], t_in[2]);
  nand nand_85 (nand_85_out, t_in[1], t_in[1]);
  nand nand_86 (nand_86_out, t_in[4], t_in[4]);
  nand nand_87 (nand_87_out, t_in[3], t_in[3]);
  nand nand_88 (nand_88_out, t_in[1], t_in[1]);
  nand nand_89 (nand_89_out, t_in[5], t_in[5]);
  nand nand_90 (nand_90_out, t_in[4], t_in[4]);
  nand nand_91 (nand_91_out, t_in[5], t_in[5]);
  nand nand_92 (nand_92_out, t_in[2], t_in[2]);
  nand nand_93 (nand_93_out, t_in[1], t_in[1]);
  nand nand_94 (nand_94_out, t_in[5], t_in[5]);
  nand nand_95 (nand_95_out, t_in[2], t_in[2]);
  nand nand_96 (nand_96_out, t_in[2], t_in[2]);
  nand nand_97 (nand_97_out, t_in[1], t_in[1]);
  nand nand_98 (nand_98_out, nand_41_out, nand_41_out);
  nand nand_99 (nand_99_out, t_in[3], t_in[3]);
  nand nand_100 (nand_100_out, t_in[2], t_in[2]);
  nand nand_101 (nand_101_out, t_in[4], t_in[4]);
  nand nand_102 (nand_102_out, nand_42_out, nand_42_out);
  nand nand_103 (nand_103_out, t_in[3], t_in[3]);
  nand nand_104 (nand_104_out, nand_43_out, nand_43_out);
  nand nand_105 (nand_105_out, nand_44_out, nand_44_out);
  nand nand_106 (nand_106_out, nand_45_out, nand_45_out);
  nand nand_107 (nand_107_out, nand_46_out, nand_46_out);
  nand nand_108 (nand_108_out, nand_47_out, nand_47_out);
  nand nand_109 (nand_109_out, t_in[1], t_in[1]);
  nand nand_110 (nand_110_out, nand_48_out, nand_48_out);
  nand nand_111 (nand_111_out, t_in[3], t_in[3]);
  nand nand_112 (nand_112_out, t_in[2], t_in[2]);
  nand nand_113 (nand_113_out, t_in[1], t_in[1]);
  nand nand_114 (nand_114_out, nand_49_out, nand_49_out);
  nand nand_115 (nand_115_out, t_in[2], t_in[2]);
  nand nand_116 (nand_116_out, nand_50_out, nand_50_out);
  nand nand_117 (nand_117_out, nand_51_out, nand_51_out);
  nand nand_118 (nand_118_out, nand_52_out, nand_52_out);
  nand nand_119 (nand_119_out, nand_53_out, nand_53_out);
  nand nand_120 (nand_120_out, t_in[4], t_in[4]);
  nand nand_121 (nand_121_out, nand_54_out, nand_54_out);
  nand nand_122 (nand_122_out, t_in[2], t_in[2]);
  nand nand_123 (nand_123_out, t_in[1], t_in[1]);
  nand nand_124 (nand_124_out, nand_56_out, nand_56_out);
  nand nand_125 (nand_125_out, nand_57_out, nand_57_out);
  nand nand_126 (nand_126_out, nand_58_out, nand_58_out);
  nand nand_127 (nand_127_out, nand_59_out, nand_59_out);
  nand nand_128 (nand_128_out, t_in[3], t_in[3]);
  nand nand_129 (nand_129_out, nand_60_out, nand_60_out);
  nand nand_130 (nand_130_out, nand_61_out, nand_61_out);
  nand nand_131 (nand_131_out, nand_62_out, nand_62_out);
  nand nand_132 (nand_132_out, nand_63_out, nand_63_out);
  nand nand_133 (nand_133_out, nand_64_out, nand_64_out);
  nand nand_134 (nand_134_out, nand_65_out, nand_65_out);
  nand nand_135 (nand_135_out, nand_66_out, nand_66_out);
  nand nand_136 (nand_136_out, nand_67_out, nand_67_out);
  nand nand_137 (nand_137_out, nand_68_out, nand_68_out);
  nand nand_138 (nand_138_out, t_in[3], t_in[3]);
  nand nand_139 (nand_139_out, nand_69_out, nand_69_out);
  nand nand_140 (nand_140_out, nand_70_out, nand_70_out);
  nand nand_141 (nand_141_out, nand_71_out, nand_71_out);
  nand nand_142 (nand_142_out, nand_72_out, nand_72_out);
  nand nand_143 (nand_143_out, nand_73_out, t_in[3]);
  nand nand_144 (nand_144_out, nand_74_out, nand_75_out);
  nand nand_145 (nand_145_out, nand_76_out, nand_77_out);
  nand nand_146 (nand_146_out, nand_78_out, t_in[1]);
  nand nand_147 (nand_147_out, nand_79_out, t_in[4]);
  nand nand_148 (nand_148_out, nand_80_out, nand_81_out);
  nand nand_149 (nand_149_out, t_in[2], t_in[1]);
  nand nand_150 (nand_150_out, nand_82_out, nand_83_out);
  nand nand_151 (nand_151_out, nand_84_out, nand_85_out);
  nand nand_152 (nand_152_out, t_in[5], t_in[4]);
  nand nand_153 (nand_153_out, nand_86_out, nand_87_out);
  nand nand_154 (nand_154_out, t_in[2], nand_88_out);
  nand nand_155 (nand_155_out, nand_89_out, nand_90_out);
  nand nand_156 (nand_156_out, t_in[2], t_in[1]);
  nand nand_157 (nand_157_out, nand_91_out, t_in[4]);
  nand nand_158 (nand_158_out, nand_92_out, nand_93_out);
  nand nand_159 (nand_159_out, nand_94_out, t_in[4]);
  nand nand_160 (nand_160_out, t_in[3], nand_95_out);
  nand nand_161 (nand_161_out, t_in[4], t_in[3]);
  nand nand_162 (nand_162_out, nand_96_out, nand_97_out);
  nand nand_163 (nand_163_out, nand_98_out, nand_99_out);
  nand nand_164 (nand_164_out, nand_100_out, t_in[1]);
  nand nand_165 (nand_165_out, t_in[5], nand_101_out);
  nand nand_166 (nand_166_out, t_in[3], t_in[2]);
  nand nand_167 (nand_167_out, nand_102_out, nand_103_out);
  nand nand_168 (nand_168_out, t_in[2], t_in[1]);
  nand nand_169 (nand_169_out, nand_104_out, nand_105_out);
  nand nand_170 (nand_170_out, nand_106_out, nand_107_out);
  nand nand_171 (nand_171_out, nand_108_out, t_in[3]);
  nand nand_172 (nand_172_out, t_in[2], nand_109_out);
  nand nand_173 (nand_173_out, nand_110_out, nand_111_out);
  nand nand_174 (nand_174_out, nand_112_out, nand_113_out);
  nand nand_175 (nand_175_out, nand_114_out, t_in[3]);
  nand nand_176 (nand_176_out, nand_115_out, t_in[1]);
  nand nand_177 (nand_177_out, nand_116_out, nand_117_out);
  nand nand_178 (nand_178_out, nand_118_out, nand_119_out);
  nand nand_179 (nand_179_out, t_in[5], nand_120_out);
  nand nand_180 (nand_180_out, t_in[3], t_in[1]);
  nand nand_181 (nand_181_out, t_in[5], t_in[3]);
  nand nand_182 (nand_182_out, t_in[2], t_in[1]);
  nand nand_183 (nand_183_out, nand_121_out, t_in[3]);
  nand nand_184 (nand_184_out, nand_122_out, nand_123_out);
  nand nand_185 (nand_185_out, nand_124_out, t_in[2]);
  nand nand_186 (nand_186_out, nand_125_out, t_in[3]);
  nand nand_187 (nand_187_out, nand_126_out, t_in[2]);
  nand nand_188 (nand_188_out, nand_127_out, nand_128_out);
  nand nand_189 (nand_189_out, nand_129_out, nand_130_out);
  nand nand_190 (nand_190_out, nand_131_out, nand_132_out);
  nand nand_191 (nand_191_out, nand_133_out, nand_134_out);
  nand nand_192 (nand_192_out, nand_135_out, nand_136_out);
  nand nand_193 (nand_193_out, nand_137_out, nand_138_out);
  nand nand_194 (nand_194_out, nand_139_out, t_in[1]);
  nand nand_195 (nand_195_out, nand_140_out, t_in[2]);
  nand nand_196 (nand_196_out, nand_141_out, nand_142_out);
  nand nand_197 (nand_197_out, nand_143_out, nand_143_out);
  nand nand_198 (nand_198_out, nand_144_out, nand_144_out);
  nand nand_199 (nand_199_out, nand_145_out, nand_145_out);
  nand nand_200 (nand_200_out, nand_146_out, nand_146_out);
  nand nand_201 (nand_201_out, nand_147_out, nand_147_out);
  nand nand_202 (nand_202_out, t_in[1], t_in[1]);
  nand nand_203 (nand_203_out, nand_148_out, nand_148_out);
  nand nand_204 (nand_204_out, nand_149_out, nand_149_out);
  nand nand_205 (nand_205_out, nand_150_out, nand_150_out);
  nand nand_206 (nand_206_out, nand_151_out, nand_151_out);
  nand nand_207 (nand_207_out, nand_152_out, nand_152_out);
  nand nand_208 (nand_208_out, t_in[2], t_in[2]);
  nand nand_209 (nand_209_out, nand_153_out, nand_153_out);
  nand nand_210 (nand_210_out, nand_154_out, nand_154_out);
  nand nand_211 (nand_211_out, nand_155_out, nand_155_out);
  nand nand_212 (nand_212_out, nand_156_out, nand_156_out);
  nand nand_213 (nand_213_out, nand_157_out, nand_157_out);
  nand nand_214 (nand_214_out, nand_158_out, nand_158_out);
  nand nand_215 (nand_215_out, nand_159_out, nand_159_out);
  nand nand_216 (nand_216_out, nand_160_out, nand_160_out);
  nand nand_217 (nand_217_out, nand_161_out, nand_161_out);
  nand nand_218 (nand_218_out, nand_162_out, nand_162_out);
  nand nand_219 (nand_219_out, nand_163_out, nand_163_out);
  nand nand_220 (nand_220_out, nand_164_out, nand_164_out);
  nand nand_221 (nand_221_out, nand_165_out, nand_165_out);
  nand nand_222 (nand_222_out, nand_166_out, nand_166_out);
  nand nand_223 (nand_223_out, nand_167_out, nand_167_out);
  nand nand_224 (nand_224_out, nand_168_out, nand_168_out);
  nand nand_225 (nand_225_out, nand_169_out, nand_170_out);
  nand nand_226 (nand_226_out, nand_171_out, nand_171_out);
  nand nand_227 (nand_227_out, nand_172_out, nand_172_out);
  nand nand_228 (nand_228_out, nand_173_out, nand_173_out);
  nand nand_229 (nand_229_out, nand_174_out, nand_174_out);
  nand nand_230 (nand_230_out, nand_175_out, nand_175_out);
  nand nand_231 (nand_231_out, nand_176_out, nand_176_out);
  nand nand_232 (nand_232_out, nand_177_out, nand_178_out);
  nand nand_233 (nand_233_out, nand_179_out, nand_179_out);
  nand nand_234 (nand_234_out, nand_180_out, nand_180_out);
  nand nand_235 (nand_235_out, nand_181_out, nand_181_out);
  nand nand_236 (nand_236_out, nand_182_out, nand_182_out);
  nand nand_237 (nand_237_out, nand_183_out, nand_183_out);
  nand nand_238 (nand_238_out, nand_184_out, nand_184_out);
  nand nand_239 (nand_239_out, nand_185_out, nand_186_out);
  nand nand_240 (nand_240_out, nand_187_out, nand_188_out);
  nand nand_241 (nand_241_out, nand_189_out, nand_190_out);
  nand nand_242 (nand_242_out, nand_191_out, nand_192_out);
  nand nand_243 (nand_243_out, nand_193_out, nand_194_out);
  nand nand_244 (nand_244_out, nand_195_out, nand_196_out);
  nand nand_245 (nand_245_out, nand_197_out, nand_198_out);
  nand nand_246 (nand_246_out, nand_199_out, nand_200_out);
  nand nand_247 (nand_247_out, nand_201_out, t_in[3]);
  nand nand_248 (nand_248_out, t_in[2], nand_202_out);
  nand nand_249 (nand_249_out, nand_203_out, nand_204_out);
  nand nand_250 (nand_250_out, nand_205_out, nand_206_out);
  nand nand_251 (nand_251_out, nand_207_out, t_in[3]);
  nand nand_252 (nand_252_out, nand_208_out, t_in[1]);
  nand nand_253 (nand_253_out, nand_209_out, nand_210_out);
  nand nand_254 (nand_254_out, nand_211_out, nand_212_out);
  nand nand_255 (nand_255_out, nand_213_out, nand_214_out);
  nand nand_256 (nand_256_out, nand_215_out, nand_216_out);
  nand nand_257 (nand_257_out, nand_217_out, nand_218_out);
  nand nand_258 (nand_258_out, nand_219_out, nand_220_out);
  nand nand_259 (nand_259_out, nand_221_out, nand_222_out);
  nand nand_260 (nand_260_out, nand_223_out, nand_224_out);
  nand nand_261 (nand_261_out, nand_225_out, nand_225_out);
  nand nand_262 (nand_262_out, nand_226_out, nand_227_out);
  nand nand_263 (nand_263_out, nand_228_out, nand_229_out);
  nand nand_264 (nand_264_out, nand_230_out, nand_231_out);
  nand nand_265 (nand_265_out, nand_232_out, nand_232_out);
  nand nand_266 (nand_266_out, nand_233_out, nand_234_out);
  nand nand_267 (nand_267_out, nand_235_out, nand_236_out);
  nand nand_268 (nand_268_out, nand_237_out, nand_238_out);
  nand nand_269 (nand_269_out, nand_239_out, nand_239_out);
  nand nand_270 (nand_270_out, nand_240_out, nand_240_out);
  nand nand_271 (nand_271_out, nand_241_out, nand_241_out);
  nand nand_272 (nand_272_out, nand_242_out, nand_242_out);
  nand nand_273 (nand_273_out, nand_243_out, nand_243_out);
  nand nand_274 (nand_274_out, nand_244_out, nand_244_out);
  nand nand_275 (nand_275_out, nand_245_out, nand_246_out);
  nand nand_276 (nand_276_out, nand_247_out, nand_247_out);
  nand nand_277 (nand_277_out, nand_248_out, nand_248_out);
  nand nand_278 (nand_278_out, nand_249_out, nand_250_out);
  nand nand_279 (nand_279_out, nand_251_out, nand_251_out);
  nand nand_280 (nand_280_out, nand_252_out, nand_252_out);
  nand nand_281 (nand_281_out, nand_253_out, nand_254_out);
  nand nand_282 (nand_282_out, nand_255_out, nand_256_out);
  nand nand_283 (nand_283_out, nand_257_out, nand_258_out);
  nand nand_284 (nand_284_out, nand_259_out, nand_260_out);
  nand nand_285 (nand_285_out, nand_261_out, nand_262_out);
  nand nand_286 (nand_286_out, nand_263_out, nand_264_out);
  nand nand_287 (nand_287_out, nand_265_out, nand_266_out);
  nand nand_288 (nand_288_out, nand_267_out, nand_268_out);
  nand nand_289 (O_1[1], nand_269_out, nand_270_out);
  nand nand_290 (nand_290_out, nand_271_out, nand_272_out);
  nand nand_291 (nand_291_out, nand_273_out, nand_274_out);
  nand nand_292 (nand_292_out, nand_275_out, nand_275_out);
  nand nand_293 (nand_293_out, nand_276_out, nand_277_out);
  nand nand_294 (nand_294_out, nand_278_out, nand_278_out);
  nand nand_295 (nand_295_out, nand_279_out, nand_280_out);
  nand nand_296 (nand_296_out, nand_281_out, nand_281_out);
  nand nand_297 (nand_297_out, nand_282_out, nand_282_out);
  nand nand_298 (nand_298_out, nand_283_out, nand_283_out);
  nand nand_299 (nand_299_out, nand_284_out, nand_284_out);
  nand nand_300 (nand_300_out, nand_285_out, nand_285_out);
  nand nand_301 (nand_301_out, nand_286_out, nand_286_out);
  nand nand_302 (nand_302_out, nand_287_out, nand_287_out);
  nand nand_303 (nand_303_out, nand_288_out, nand_288_out);
  nand nand_304 (nand_304_out, nand_290_out, nand_290_out);
  nand nand_305 (nand_305_out, nand_291_out, nand_291_out);
  nand nand_306 (nand_306_out, nand_292_out, nand_293_out);
  nand nand_307 (nand_307_out, nand_294_out, nand_295_out);
  nand nand_308 (nand_308_out, nand_296_out, nand_297_out);
  nand nand_309 (nand_309_out, nand_298_out, nand_299_out);
  nand nand_310 (nand_310_out, nand_300_out, nand_301_out);
  nand nand_311 (nand_311_out, nand_302_out, nand_303_out);
  nand nand_312 (O_1[0], nand_304_out, nand_305_out);
  nand nand_313 (nand_313_out, nand_306_out, nand_306_out);
  nand nand_314 (nand_314_out, nand_307_out, nand_307_out);
  nand nand_315 (nand_315_out, nand_308_out, nand_308_out);
  nand nand_316 (nand_316_out, nand_309_out, nand_309_out);
  nand nand_317 (nand_317_out, nand_310_out, nand_310_out);
  nand nand_318 (nand_318_out, nand_311_out, nand_311_out);
  nand nand_319 (O_0[3], nand_313_out, nand_314_out);
  nand nand_320 (O_0[2], nand_315_out, nand_316_out);
  nand nand_321 (O_0[1], nand_317_out, nand_318_out);

  assign {O_0[4], O_0[0]} = {1'b0, t_in[0]};
  assign O_1[4:3] = 2'b00;
endmodule

module binary_to_time_converter (
  input  [4:0] Input_bus_1,
  input  [4:0] Input_bus_2,
  output [5:0] Output_bus_1
);

  wire nand_1_out, nand_2_out, nand_3_out, nand_4_out, nand_5_out, nand_6_out, nand_7_out, nand_8_out,
       nand_9_out, nand_10_out, nand_11_out, nand_12_out, nand_13_out, nand_14_out, nand_15_out, nand_16_out,
       nand_17_out, nand_18_out, nand_19_out, nand_20_out, nand_21_out, nand_22_out, nand_23_out,
       nand_24_out, nand_25_out, nand_26_out, nand_27_out, nand_28_out, nand_29_out, nand_30_out,
       nand_31_out, nand_32_out, nand_33_out, nand_34_out, nand_35_out, nand_36_out, nand_37_out,
       nand_38_out, nand_39_out, nand_40_out, nand_41_out, nand_42_out, nand_43_out, nand_44_out,
       nand_45_out, nand_46_out, nand_47_out, nand_48_out, nand_49_out, nand_50_out, nand_51_out,
       nand_52_out, nand_53_out, nand_54_out, nand_55_out, nand_56_out, nand_57_out, nand_58_out,
       nand_59_out, nand_60_out, nand_61_out, nand_62_out, nand_63_out, nand_64_out, nand_65_out,
       nand_66_out, nand_67_out, nand_68_out, nand_69_out, nand_71_out, nand_72_out, nand_73_out,
       nand_74_out, nand_75_out, nand_76_out, nand_77_out, nand_78_out, nand_79_out, nand_80_out,
       nand_81_out, nand_82_out, nand_83_out, nand_84_out, nand_85_out, nand_86_out, nand_87_out,
       nand_88_out, nand_89_out, nand_90_out, nand_91_out, nand_92_out, nand_93_out, nand_94_out,
       nand_95_out, nand_96_out, nand_97_out, nand_98_out, nand_99_out, nand_100_out, nand_101_out,
       nand_102_out, nand_103_out, nand_104_out, nand_105_out, nand_106_out, nand_107_out, nand_108_out,
       nand_109_out, nand_110_out, nand_111_out, nand_112_out, nand_113_out, nand_114_out, nand_115_out,
       nand_116_out, nand_117_out, nand_118_out, nand_119_out, nand_120_out, nand_121_out, nand_122_out,
       nand_123_out, nand_124_out, nand_126_out, nand_127_out, nand_128_out, nand_129_out, nand_130_out,
       nand_131_out, nand_132_out, nand_133_out, nand_134_out, nand_135_out, nand_136_out, nand_137_out,
       nand_138_out, nand_139_out, nand_140_out, nand_141_out, nand_142_out, nand_143_out, nand_144_out,
       nand_145_out, nand_146_out, nand_147_out, nand_148_out, nand_149_out, nand_150_out, nand_151_out,
       nand_152_out, nand_153_out, nand_154_out, nand_155_out, nand_156_out, nand_157_out, nand_158_out,
       nand_159_out, nand_160_out, nand_161_out, nand_162_out, nand_163_out, nand_164_out, nand_165_out,
       nand_168_out, nand_169_out, nand_171_out, nand_172_out;

  nand nand_1 (nand_1_out, Input_bus_2[2], Input_bus_2[2]);
  nand nand_2 (nand_2_out, Input_bus_2[0], Input_bus_2[0]);
  nand nand_3 (nand_3_out, Input_bus_1[1], Input_bus_1[1]);
  nand nand_4 (nand_4_out, Input_bus_1[1], Input_bus_1[1]);
  nand nand_5 (nand_5_out, Input_bus_2[3], Input_bus_2[3]);
  nand nand_6 (nand_6_out, Input_bus_2[2], Input_bus_2[2]);
  nand nand_7 (nand_7_out, Input_bus_2[1], Input_bus_2[1]);
  nand nand_8 (nand_8_out, Input_bus_1[2], Input_bus_1[2]);
  nand nand_9 (nand_9_out, Input_bus_1[1], Input_bus_1[1]);
  nand nand_10 (nand_10_out, Input_bus_1[2], Input_bus_1[2]);
  nand nand_11 (nand_11_out, Input_bus_1[1], Input_bus_1[1]);
  nand nand_12 (nand_12_out, Input_bus_1[2], Input_bus_1[2]);
  nand nand_13 (nand_13_out, Input_bus_1[1], Input_bus_1[1]);
  nand nand_14 (nand_14_out, Input_bus_1[0], Input_bus_1[0]);
  nand nand_15 (nand_15_out, Input_bus_1[1], Input_bus_1[1]);
  nand nand_16 (nand_16_out, Input_bus_1[0], Input_bus_1[0]);
  nand nand_17 (nand_17_out, Input_bus_2[2], Input_bus_2[2]);
  nand nand_18 (nand_18_out, Input_bus_1[0], Input_bus_1[0]);
  nand nand_19 (nand_19_out, Input_bus_2[1], Input_bus_2[1]);
  nand nand_20 (nand_20_out, Input_bus_2[2], Input_bus_2[2]);
  nand nand_21 (nand_21_out, Input_bus_2[3], nand_1_out);
  nand nand_22 (nand_22_out, Input_bus_2[1], nand_2_out);
  nand nand_23 (nand_23_out, Input_bus_1[1], Input_bus_1[0]);
  nand nand_24 (nand_24_out, nand_3_out, Input_bus_1[0]);
  nand nand_25 (nand_25_out, Input_bus_2[2], Input_bus_2[1]);
  nand nand_26 (nand_26_out, nand_4_out, Input_bus_1[0]);
  nand nand_27 (nand_27_out, Input_bus_1[1], nand_5_out);
  nand nand_28 (nand_28_out, nand_6_out, nand_7_out);
  nand nand_29 (nand_29_out, nand_8_out, nand_9_out);
  nand nand_30 (nand_30_out, nand_10_out, nand_11_out);
  nand nand_31 (nand_31_out, nand_12_out, Input_bus_1[0]);
  nand nand_32 (nand_32_out, nand_13_out, nand_14_out);
  nand nand_33 (nand_33_out, nand_15_out, Input_bus_2[2]);
  nand nand_34 (nand_34_out, Input_bus_1[1], nand_16_out);
  nand nand_35 (nand_35_out, Input_bus_1[1], nand_17_out);
  nand nand_36 (nand_36_out, nand_18_out, Input_bus_2[1]);
  nand nand_37 (nand_37_out, Input_bus_1[0], nand_19_out);
  nand nand_38 (nand_38_out, Input_bus_2[3], nand_20_out);
  nand nand_39 (nand_39_out, nand_21_out, nand_21_out);
  nand nand_40 (nand_40_out, nand_22_out, nand_22_out);
  nand nand_41 (nand_41_out, nand_23_out, nand_23_out);
  nand nand_42 (nand_42_out, nand_24_out, nand_24_out);
  nand nand_43 (nand_43_out, nand_25_out, nand_25_out);
  nand nand_44 (nand_44_out, nand_26_out, nand_26_out);
  nand nand_45 (nand_45_out, nand_27_out, nand_27_out);
  nand nand_46 (nand_46_out, nand_28_out, nand_28_out);
  nand nand_47 (nand_47_out, Input_bus_1[2], Input_bus_1[2]);
  nand nand_48 (nand_48_out, Input_bus_1[0], Input_bus_1[0]);
  nand nand_49 (nand_49_out, nand_29_out, nand_29_out);
  nand nand_50 (nand_50_out, Input_bus_2[3], Input_bus_2[3]);
  nand nand_51 (nand_51_out, Input_bus_2[2], Input_bus_2[2]);
  nand nand_52 (nand_52_out, nand_30_out, nand_30_out);
  nand nand_53 (nand_53_out, Input_bus_2[3], Input_bus_2[3]);
  nand nand_54 (nand_54_out, Input_bus_2[1], Input_bus_2[1]);
  nand nand_55 (nand_55_out, nand_31_out, nand_31_out);
  nand nand_56 (nand_56_out, Input_bus_2[3], Input_bus_2[3]);
  nand nand_57 (nand_57_out, Input_bus_2[2], Input_bus_2[2]);
  nand nand_58 (nand_58_out, Input_bus_2[1], Input_bus_2[1]);
  nand nand_59 (nand_59_out, Input_bus_1[0], Input_bus_1[0]);
  nand nand_60 (nand_60_out, Input_bus_1[0], Input_bus_1[0]);
  nand nand_61 (nand_61_out, nand_32_out, nand_32_out);
  nand nand_62 (nand_62_out, nand_33_out, nand_33_out);
  nand nand_63 (nand_63_out, Input_bus_2[1], Input_bus_2[1]);
  nand nand_64 (nand_64_out, Input_bus_1[1], Input_bus_1[1]);
  nand nand_65 (nand_65_out, Input_bus_2[2], Input_bus_2[2]);
  nand nand_66 (nand_66_out, nand_34_out, nand_34_out);
  nand nand_67 (nand_67_out, Input_bus_2[2], Input_bus_2[2]);
  nand nand_68 (nand_68_out, nand_35_out, nand_35_out);
  nand nand_69 (nand_69_out, Input_bus_2[1], Input_bus_2[1]);
  nand nand_70 (Output_bus_1[1], nand_36_out, nand_37_out);
  nand nand_71 (nand_71_out, nand_38_out, nand_38_out);
  nand nand_72 (nand_72_out, nand_39_out, nand_40_out);
  nand nand_73 (nand_73_out, nand_41_out, Input_bus_2[1]);
  nand nand_74 (nand_74_out, Input_bus_1[1], Input_bus_1[0]);
  nand nand_75 (nand_75_out, Input_bus_1[1], Input_bus_1[0]);
  nand nand_76 (nand_76_out, nand_42_out, nand_43_out);
  nand nand_77 (nand_77_out, nand_44_out, Input_bus_2[3]);
  nand nand_78 (nand_78_out, nand_45_out, nand_46_out);
  nand nand_79 (nand_79_out, Input_bus_1[2], Input_bus_2[3]);
  nand nand_80 (nand_80_out, nand_47_out, nand_48_out);
  nand nand_81 (nand_81_out, nand_49_out, Input_bus_1[0]);
  nand nand_82 (nand_82_out, nand_50_out, nand_51_out);
  nand nand_83 (nand_83_out, nand_52_out, Input_bus_1[0]);
  nand nand_84 (nand_84_out, nand_53_out, nand_54_out);
  nand nand_85 (nand_85_out, nand_55_out, nand_56_out);
  nand nand_86 (nand_86_out, nand_57_out, nand_58_out);
  nand nand_87 (nand_87_out, Input_bus_1[1], nand_59_out);
  nand nand_88 (nand_88_out, Input_bus_1[2], nand_60_out);
  nand nand_89 (nand_89_out, Input_bus_1[2], Input_bus_2[2]);
  nand nand_90 (nand_90_out, Input_bus_1[2], Input_bus_1[0]);
  nand nand_91 (nand_91_out, nand_61_out, Input_bus_2[2]);
  nand nand_92 (nand_92_out, nand_62_out, nand_63_out);
  nand nand_93 (nand_93_out, nand_64_out, Input_bus_1[0]);
  nand nand_94 (nand_94_out, nand_65_out, Input_bus_2[1]);
  nand nand_95 (nand_95_out, nand_66_out, nand_67_out);
  nand nand_96 (nand_96_out, nand_68_out, nand_69_out);
  nand nand_97 (nand_97_out, Input_bus_1[1], Input_bus_1[0]);
  nand nand_98 (nand_98_out, Input_bus_2[2], Input_bus_2[1]);
  nand nand_99 (nand_99_out, Input_bus_2[0], Input_bus_2[0]);
  nand nand_100 (nand_100_out, nand_71_out, Input_bus_2[1]);
  nand nand_101 (nand_101_out, nand_72_out, nand_73_out);
  nand nand_102 (nand_102_out, nand_74_out, nand_74_out);
  nand nand_103 (nand_103_out, nand_75_out, nand_75_out);
  nand nand_104 (nand_104_out, nand_76_out, nand_77_out);
  nand nand_105 (nand_105_out, Input_bus_1[0], Input_bus_1[0]);
  nand nand_106 (nand_106_out, nand_78_out, nand_79_out);
  nand nand_107 (nand_107_out, nand_80_out, nand_80_out);
  nand nand_108 (nand_108_out, nand_81_out, nand_81_out);
  nand nand_109 (nand_109_out, nand_82_out, nand_82_out);
  nand nand_110 (nand_110_out, nand_83_out, nand_83_out);
  nand nand_111 (nand_111_out, nand_84_out, nand_84_out);
  nand nand_112 (nand_112_out, nand_85_out, nand_85_out);
  nand nand_113 (nand_113_out, nand_86_out, nand_86_out);
  nand nand_114 (nand_114_out, nand_87_out, nand_87_out);
  nand nand_115 (nand_115_out, nand_88_out, nand_88_out);
  nand nand_116 (nand_116_out, Input_bus_2[3], Input_bus_2[3]);
  nand nand_117 (nand_117_out, nand_89_out, nand_89_out);
  nand nand_118 (nand_118_out, nand_90_out, nand_90_out);
  nand nand_119 (nand_119_out, nand_91_out, nand_92_out);
  nand nand_120 (nand_120_out, nand_93_out, nand_93_out);
  nand nand_121 (nand_121_out, nand_94_out, nand_94_out);
  nand nand_122 (nand_122_out, nand_95_out, nand_96_out);
  nand nand_123 (nand_123_out, nand_97_out, nand_97_out);
  nand nand_124 (nand_124_out, nand_98_out, nand_98_out);
  nand nand_125 (Output_bus_1[0], nand_99_out, nand_100_out);
  nand nand_126 (nand_126_out, nand_101_out, nand_101_out);
  nand nand_127 (nand_127_out, nand_102_out, Input_bus_2[2]);
  nand nand_128 (nand_128_out, nand_103_out, Input_bus_2[3]);
  nand nand_129 (nand_129_out, Input_bus_1[2], Input_bus_1[2]);
  nand nand_130 (nand_130_out, nand_104_out, nand_104_out);
  nand nand_131 (nand_131_out, Input_bus_1[1], nand_105_out);
  nand nand_132 (nand_132_out, nand_106_out, nand_106_out);
  nand nand_133 (nand_133_out, Input_bus_1[2], Input_bus_1[0]);
  nand nand_134 (nand_134_out, nand_107_out, Input_bus_2[3]);
  nand nand_135 (nand_135_out, nand_108_out, nand_109_out);
  nand nand_136 (nand_136_out, nand_110_out, nand_111_out);
  nand nand_137 (nand_137_out, nand_112_out, nand_113_out);
  nand nand_138 (nand_138_out, nand_114_out, Input_bus_2[2]);
  nand nand_139 (nand_139_out, nand_115_out, nand_116_out);
  nand nand_140 (nand_140_out, nand_117_out, Input_bus_2[1]);
  nand nand_141 (nand_141_out, nand_118_out, Input_bus_2[3]);
  nand nand_142 (nand_142_out, nand_119_out, nand_119_out);
  nand nand_143 (nand_143_out, nand_120_out, nand_121_out);
  nand nand_144 (nand_144_out, nand_122_out, nand_122_out);
  nand nand_145 (nand_145_out, nand_123_out, nand_124_out);
  nand nand_146 (nand_146_out, nand_126_out, nand_127_out);
  nand nand_147 (nand_147_out, nand_128_out, nand_129_out);
  nand nand_148 (nand_148_out, nand_130_out, nand_131_out);
  nand nand_149 (nand_149_out, nand_132_out, nand_133_out);
  nand nand_150 (nand_150_out, nand_134_out, nand_135_out);
  nand nand_151 (nand_151_out, nand_136_out, nand_137_out);
  nand nand_152 (nand_152_out, nand_138_out, nand_139_out);
  nand nand_153 (nand_153_out, nand_140_out, nand_141_out);
  nand nand_154 (nand_154_out, nand_142_out, nand_143_out);
  nand nand_155 (nand_155_out, nand_144_out, nand_145_out);
  nand nand_156 (nand_156_out, nand_146_out, nand_146_out);
  nand nand_157 (nand_157_out, nand_147_out, nand_147_out);
  nand nand_158 (nand_158_out, nand_148_out, nand_148_out);
  nand nand_159 (nand_159_out, nand_149_out, nand_149_out);
  nand nand_160 (nand_160_out, nand_150_out, nand_150_out);
  nand nand_161 (nand_161_out, nand_151_out, nand_151_out);
  nand nand_162 (nand_162_out, nand_152_out, nand_152_out);
  nand nand_163 (nand_163_out, nand_153_out, nand_153_out);
  nand nand_164 (nand_164_out, nand_154_out, nand_154_out);
  nand nand_165 (nand_165_out, nand_155_out, nand_155_out);
  nand nand_166 (Output_bus_1[5], nand_156_out, nand_157_out);
  nand nand_167 (Output_bus_1[4], nand_158_out, nand_159_out);
  nand nand_168 (nand_168_out, nand_160_out, nand_161_out);
  nand nand_169 (nand_169_out, nand_162_out, nand_163_out);
  nand nand_170 (Output_bus_1[2], nand_164_out, nand_165_out);
  nand nand_171 (nand_171_out, nand_168_out, nand_168_out);
  nand nand_172 (nand_172_out, nand_169_out, nand_169_out);
  nand nand_173 (Output_bus_1[3], nand_171_out, nand_172_out);
endmodule

module test (
  input  C_2,
  input  C_1,
  input  C_0,
  input  S_3,
  input  S_2,
  input  S_1,
  input  S_0,
  output O_3,
  output O_2,
  output O_1,
  output O_0
);

  wire and_1_out, and_2_out, and_3_out, and_4_out, and_5_out, and_6_out, and_7_out, and_8_out, and_9_out,
       and_10_out, and_11_out, and_12_out, and_13_out, and_14_out, and_15_out, and_16_out, and_17_out,
       and_18_out, and_19_out, and_20_out, and_21_out, and_22_out, and_23_out, and_24_out, and_25_out,
       and_26_out, and_27_out, and_28_out, and_29_out, and_30_out, and_31_out, and_32_out, and_33_out,
       and_34_out, and_35_out, and_36_out, and_37_out, not_1_out, not_2_out, not_3_out, not_4_out, not_5_out,
       not_6_out, not_7_out, not_8_out, not_9_out, not_10_out, not_11_out, not_12_out, not_13_out,
       not_14_out, not_15_out, not_16_out, not_17_out, not_18_out, not_19_out, not_20_out, not_21_out,
       not_22_out, not_23_out, not_24_out, not_25_out, not_26_out, not_27_out, not_28_out, not_29_out,
       not_30_out, not_31_out, not_32_out, not_33_out, not_34_out, not_35_out, not_36_out, not_37_out,
       not_38_out, not_39_out, not_40_out, not_41_out, not_42_out, not_43_out, not_44_out, not_45_out,
       not_46_out, not_47_out, not_48_out, not_49_out, not_50_out, not_51_out, not_52_out, not_53_out,
       not_54_out, not_55_out, not_56_out, not_57_out, not_58_out, not_59_out, not_60_out, not_61_out,
       not_62_out, not_63_out, not_64_out, not_65_out, not_66_out, not_67_out, not_68_out, not_69_out,
       not_70_out, not_71_out, not_72_out, not_73_out, not_74_out, not_75_out, not_76_out, not_77_out,
       not_78_out, not_79_out, not_80_out, not_81_out, not_82_out, not_83_out, not_84_out, not_85_out,
       not_86_out, not_87_out, not_88_out, not_89_out, not_90_out, not_91_out, not_92_out, not_93_out,
       not_94_out;

  not not_1 (not_1_out, C_2);
  not not_2 (not_2_out, C_1);
  not not_3 (not_3_out, C_0);
  not not_4 (not_4_out, S_2);
  not not_5 (not_5_out, C_1);
  not not_6 (not_6_out, C_0);
  not not_7 (not_7_out, C_1);
  not not_8 (not_8_out, S_3);
  not not_9 (not_9_out, C_2);
  not not_10 (not_10_out, C_1);
  not not_11 (not_11_out, S_3);
  not not_12 (not_12_out, S_1);
  not not_13 (not_13_out, C_1);
  not not_14 (not_14_out, S_3);
  not not_15 (not_15_out, S_0);
  not not_16 (not_16_out, C_1);
  not not_17 (not_17_out, C_0);
  not not_18 (not_18_out, C_2);
  not not_19 (not_19_out, C_0);
  not not_20 (not_20_out, C_1);
  not not_21 (not_21_out, C_0);
  not not_22 (not_22_out, C_2);
  not not_23 (not_23_out, C_1);
  not not_24 (not_24_out, C_2);
  not not_25 (not_25_out, S_0);
  not not_26 (not_26_out, C_1);
  not not_27 (not_27_out, C_0);
  not not_28 (not_28_out, S_0);
  not not_29 (not_29_out, C_1);
  not not_30 (not_30_out, S_3);
  not not_31 (not_31_out, S_2);
  not not_32 (not_32_out, C_1);
  not not_33 (not_33_out, S_3);
  not not_34 (not_34_out, S_0);
  not not_35 (not_35_out, C_2);
  not not_36 (not_36_out, C_1);
  not not_37 (not_37_out, C_0);
  not not_38 (not_38_out, C_2);
  not not_39 (not_39_out, C_2);
  not not_40 (not_40_out, C_1);
  not not_41 (not_41_out, S_2);
  not not_42 (not_42_out, C_2);
  not not_43 (not_43_out, C_0);
  not not_44 (not_44_out, S_3);
  not not_45 (not_45_out, C_2);
  not not_46 (not_46_out, S_3);
  not not_47 (not_47_out, S_2);
  not not_48 (not_48_out, C_2);
  not not_49 (not_49_out, C_1);
  not not_50 (not_50_out, C_0);
  not not_51 (not_51_out, C_2);
  not not_52 (not_52_out, C_0);
  not not_53 (not_53_out, S_2);
  not not_54 (not_54_out, S_1);
  not not_55 (not_55_out, C_1);
  not not_56 (not_56_out, C_0);
  not not_57 (not_57_out, S_2);
  not not_58 (not_58_out, S_1);
  not not_59 (not_59_out, C_1);
  not not_60 (not_60_out, S_3);
  not not_61 (not_61_out, S_2);
  not not_62 (not_62_out, C_1);
  not not_63 (not_63_out, S_3);
  not not_64 (not_64_out, S_1);
  not not_65 (not_65_out, C_2);
  not not_66 (not_66_out, C_1);
  not not_67 (not_67_out, C_0);
  not not_68 (not_68_out, C_2);
  not not_69 (not_69_out, C_1);
  not not_70 (not_70_out, S_3);
  not not_71 (not_71_out, S_2);
  not not_72 (not_72_out, C_2);
  not not_73 (not_73_out, C_2);
  not not_74 (not_74_out, C_2);
  not not_75 (not_75_out, C_0);
  not not_76 (not_76_out, S_3);
  not not_77 (not_77_out, S_2);
  not not_78 (not_78_out, S_1);
  not not_79 (not_79_out, C_2);
  not not_80 (not_80_out, C_0);
  not not_81 (not_81_out, S_2);
  not not_82 (not_82_out, C_2);
  not not_83 (not_83_out, C_0);
  not not_84 (not_84_out, S_1);
  not not_85 (not_85_out, C_2);
  not not_86 (not_86_out, S_2);
  not not_87 (not_87_out, S_1);
  not not_88 (not_88_out, C_1);
  not not_89 (not_89_out, C_0);
  not not_90 (not_90_out, S_3);
  not not_91 (not_91_out, S_1);
  not not_92 (not_92_out, C_1);
  not not_93 (not_93_out, S_3);
  not not_94 (not_94_out, S_0);
  and and_1 (and_1_out, not_1_out, S_3);
  and and_2 (and_2_out, not_2_out, not_3_out, S_3, not_4_out);
  and and_3 (and_3_out, not_5_out, not_6_out, S_3, S_1);
  and and_4 (and_4_out, C_2, not_7_out, C_0, not_8_out, S_2, S_1, S_0);
  and and_5 (and_5_out, not_9_out, S_2);
  and and_6 (and_6_out, not_10_out, not_11_out, S_2, not_12_out);
  and and_7 (and_7_out, not_13_out, not_14_out, S_2, not_15_out);
  and and_8 (and_8_out, not_16_out, not_17_out, S_2, S_1);
  and and_9 (and_9_out, not_18_out, C_1, not_19_out, S_1, S_0);
  and and_10 (and_10_out, C_2, not_20_out, not_21_out, S_3, S_1, S_0);
  and and_11 (and_11_out, not_22_out, not_23_out, S_1);
  and and_12 (and_12_out, not_24_out, S_1, not_25_out);
  and and_13 (and_13_out, not_26_out, not_27_out, S_1, not_28_out);
  and and_14 (and_14_out, not_29_out, not_30_out, not_31_out, S_1);
  and and_15 (and_15_out, not_32_out, not_33_out, S_1, not_34_out);
  and and_16 (and_16_out, not_35_out, S_2, S_1);
  and and_17 (and_17_out, not_36_out, not_37_out, S_2, S_1);
  and and_18 (and_18_out, not_38_out, C_0, S_1);
  and and_19 (and_19_out, not_39_out, not_40_out, C_0, S_3, not_41_out, S_0);
  and and_20 (and_20_out, not_42_out, C_1, not_43_out, not_44_out, S_2);
  and and_21 (and_21_out, not_45_out, C_1, C_0, not_46_out, not_47_out, S_0);
  and and_22 (and_22_out, not_48_out, not_49_out, not_50_out, S_0);
  and and_23 (and_23_out, not_51_out, not_52_out, not_53_out, not_54_out, S_0);
  and and_24 (and_24_out, not_55_out, not_56_out, not_57_out, not_58_out, S_0);
  and and_25 (and_25_out, not_59_out, not_60_out, not_61_out, S_0);
  and and_26 (and_26_out, not_62_out, not_63_out, not_64_out, S_0);
  and and_27 (and_27_out, not_65_out, S_2, S_1, S_0);
  and and_28 (and_28_out, not_66_out, not_67_out, S_2, S_1, S_0);
  and and_29 (and_29_out, not_68_out, not_69_out, C_0, not_70_out, not_71_out, S_1);
  and and_30 (and_30_out, not_72_out, C_0, S_1, S_0);
  and and_31 (and_31_out, not_73_out, C_0, S_2, S_0);
  and and_32 (and_32_out, not_74_out, C_1, not_75_out, not_76_out, not_77_out, not_78_out);
  and and_33 (and_33_out, not_79_out, C_1, not_80_out, S_3, not_81_out, S_1);
  and and_34 (and_34_out, not_82_out, C_1, not_83_out, S_3, S_2, not_84_out);
  and and_35 (and_35_out, not_85_out, C_1, C_0, S_3, not_86_out, not_87_out);
  and and_36 (and_36_out, C_2, not_88_out, not_89_out, not_90_out, S_2, not_91_out);
  and and_37 (and_37_out, C_2, not_92_out, C_0, not_93_out, S_2, S_1, not_94_out);
  or or_1 (O_3, and_1_out, and_2_out, and_3_out, and_4_out);
  or or_2 (O_2, and_5_out, and_6_out, and_7_out, and_8_out, and_9_out, and_10_out);
  or or_3 (O_1, and_11_out, and_12_out, and_13_out, and_14_out, and_15_out, and_16_out, and_17_out, and_18_out, and_19_out, and_20_out, and_21_out);
  or or_4 (O_0, and_22_out, and_23_out, and_24_out, and_25_out, and_26_out, and_27_out, and_28_out, and_29_out, and_30_out, and_31_out, and_32_out, and_33_out, and_34_out, and_35_out, and_36_out, and_37_out);
endmodule

module memory_alarm (
  input  [5:0] hour_in,
  input  [5:0] min_in,
  input  [5:0] sec_in,
  input  set,
  input  reset,
  input  enable,
  output [5:0] hour,
  output [5:0] min,
  output [5:0] seconds
);

  Register #(.width(6)) register_1 (.D(hour_in), .en(enable), .clk(set), .Q(hour), .clr(reset));
  Register #(.width(6)) register_2 (.D(min_in), .en(enable), .clk(set), .Q(min), .clr(reset));
  Register #(.width(6)) register_3 (.D(sec_in), .en(enable), .clk(set), .Q(seconds), .clr(reset));
endmodule

module musique (
  input  set_on,
  input  [1:0] music,
  output buzzer_0,
  output buzzer_1
);

  wire clock_1_out, demultiplexer_1_out0, Fa_out, FaD5_out, La6_out, Mi_out, not_1_out, ReD5_out, Si5_out,
       Si6_out, Sol5_out;

  Clock #(.highDuration(61162), .lowDuration(61162)) Do1 ();  // open: out
  Clock #(.highDuration(57720), .lowDuration(57720)) DoD1 ();  // open: out
  Clock #(.highDuration(54481), .lowDuration(54481)) Re1 ();  // open: out
  Clock #(.highDuration(51427), .lowDuration(51427)) ReD1 ();  // open: out
  Clock #(.highDuration(48544), .lowDuration(48544)) Mi1 ();  // open: out
  Clock #(.highDuration(45819), .lowDuration(45819)) Fa1 ();  // open: out
  Clock #(.highDuration(43243), .lowDuration(43243)) FaD1 ();  // open: out
  Clock #(.highDuration(40816), .lowDuration(40816)) Sol1 ();  // open: out
  Clock #(.highDuration(38528), .lowDuration(38528)) SolD1 ();  // open: out
  Clock #(.highDuration(36364), .lowDuration(36364)) La1 ();  // open: out
  Clock #(.highDuration(34323), .lowDuration(268)) SiB1 ();  // open: out
  Clock #(.highDuration(32394), .lowDuration(32394)) Si1 ();  // open: out
  Clock #(.highDuration(30576), .lowDuration(30576)) Do2 ();  // open: out
  Clock #(.highDuration(28860), .lowDuration(28860)) DoD2 ();  // open: out
  Clock #(.highDuration(27241), .lowDuration(27241)) Re2 ();  // open: out
  Clock #(.highDuration(25714), .lowDuration(25714)) ReD2 ();  // open: out
  Clock #(.highDuration(24269), .lowDuration(24269)) Mi2 ();  // open: out
  Clock #(.highDuration(22907), .lowDuration(284)) Fa2 ();  // open: out
  Clock #(.highDuration(21622), .lowDuration(21622)) FaD2 ();  // open: out
  Clock #(.highDuration(20408), .lowDuration(20408)) Sol2 ();  // open: out
  Clock #(.highDuration(19262), .lowDuration(19262)) SolD2 ();  // open: out
  Clock #(.highDuration(18182), .lowDuration(18182)) La2 ();  // open: out
  Clock #(.highDuration(17161), .lowDuration(17161)) SiB2 ();  // open: out
  Clock #(.highDuration(16198), .lowDuration(16198)) Si2 ();  // open: out
  Clock #(.highDuration(15289), .lowDuration(15289)) Do3 ();  // open: out
  Clock #(.highDuration(14431), .lowDuration(14431)) DoD3 ();  // open: out
  Clock #(.highDuration(13621), .lowDuration(13621)) Re3 ();  // open: out
  Clock #(.highDuration(12857), .lowDuration(12857)) ReD3 ();  // open: out
  Clock #(.highDuration(12135)) Mi3 ();  // open: out
  Clock #(.highDuration(11454), .lowDuration(11454)) Fa3 ();  // open: out
  Clock #(.highDuration(10811), .lowDuration(268)) FaD3 ();  // open: out
  Clock #(.highDuration(10204), .lowDuration(10204)) Sol3 ();  // open: out
  Clock #(.highDuration(9632), .lowDuration(9632)) SolD3 ();  // open: out
  Clock #(.highDuration(9091), .lowDuration(9091)) La3 ();  // open: out
  Clock #(.highDuration(8581), .lowDuration(8581)) SiB3 ();  // open: out
  Clock #(.highDuration(8099), .lowDuration(8099)) Si3 ();  // open: out
  Clock #(.highDuration(7644), .lowDuration(7644)) Do4 ();  // open: out
  Clock #(.highDuration(7216), .lowDuration(7216)) DoD4 ();  // open: out
  Clock #(.highDuration(6811), .lowDuration(6811)) Re4 ();  // open: out
  Clock #(.highDuration(6428), .lowDuration(6428)) ReD4 ();  // open: out
  Clock #(.highDuration(6067), .lowDuration(6067)) Mi4 ();  // open: out
  Clock #(.highDuration(5727), .lowDuration(284)) Fa4 ();  // open: out
  Clock #(.highDuration(5406), .lowDuration(5406)) FaD4 ();  // open: out
  Clock #(.highDuration(5102), .lowDuration(253)) Sol4 ();  // open: out
  Clock #(.highDuration(4816)) SolD4 ();  // open: out
  Clock #(.highDuration(4545), .lowDuration(4545)) La4 ();  // open: out
  Clock #(.highDuration(4290), .lowDuration(4290)) SiB4 ();  // open: out
  Clock #(.highDuration(4050), .lowDuration(4050)) Si4 ();  // open: out
  Clock #(.highDuration(3822), .lowDuration(3822)) Do5 ();  // open: out
  Clock #(.highDuration(3608), .lowDuration(3608)) DoD5 ();  // open: out
  Clock #(.highDuration(3405), .lowDuration(3405)) Re5 ();  // open: out
  Clock #(.highDuration(3214), .lowDuration(3214)) ReD5 (.out(ReD5_out));
  Clock #(.highDuration(3034), .lowDuration(3034)) Mi (.out(Mi_out));
  Clock #(.highDuration(2863), .lowDuration(2863)) Fa (.out(Fa_out));
  Clock #(.highDuration(2703), .lowDuration(2703)) FaD5 (.out(FaD5_out));
  Clock #(.highDuration(2551), .lowDuration(2551)) Sol5 (.out(Sol5_out));
  Clock #(.highDuration(2408), .lowDuration(2408)) SolD5 ();  // open: out
  Clock #(.highDuration(2273), .lowDuration(2273)) La5 ();  // open: out
  Clock #(.highDuration(2145), .lowDuration(2145)) SiB5 ();  // open: out
  Clock #(.highDuration(2025), .lowDuration(2025)) Si5 (.out(Si5_out));
  Clock #(.highDuration(1911), .lowDuration(1911)) Do6 ();  // open: out
  Clock #(.highDuration(1804), .lowDuration(1804)) DoD6 ();  // open: out
  Clock #(.highDuration(1703), .lowDuration(1703)) Re6 ();  // open: out
  Clock #(.highDuration(1607), .lowDuration(1607)) ReD6 ();  // open: out
  Clock #(.highDuration(1517), .lowDuration(1517)) Mi6 ();  // open: out
  Clock #(.highDuration(1432), .lowDuration(1432)) Fa6 ();  // open: out
  Clock #(.highDuration(1351), .lowDuration(1351)) FaD6 ();  // open: out
  Clock #(.highDuration(1276), .lowDuration(1276)) Sol6 ();  // open: out
  Clock #(.highDuration(1204), .lowDuration(1204)) SolD6 ();  // open: out
  Clock #(.highDuration(1136), .lowDuration(1136)) La6 (.out(La6_out));
  Clock #(.highDuration(1073), .lowDuration(1073)) Sib6 ();  // open: out
  Clock #(.highDuration(1012), .lowDuration(1012)) Si6 (.out(Si6_out));
  Clock #(.highDuration(956), .lowDuration(956)) Do7 ();  // open: out
  Clock #(.highDuration(902), .lowDuration(902)) DoD7 ();  // open: out
  Clock #(.highDuration(851), .lowDuration(851)) Re7 ();  // open: out
  Clock #(.highDuration(804), .lowDuration(804)) ReD7 ();  // open: out
  Clock #(.highDuration(758), .lowDuration(758)) Mi7 ();  // open: out
  Clock #(.highDuration(716), .lowDuration(716)) Fa7 ();  // open: out
  Clock #(.highDuration(676), .lowDuration(676)) FaD7 ();  // open: out
  Clock #(.highDuration(638), .lowDuration(638)) Sol7 ();  // open: out
  Clock #(.highDuration(602), .lowDuration(602)) SolD7 ();  // open: out
  Clock #(.highDuration(568), .lowDuration(568)) La7 ();  // open: out
  Clock #(.highDuration(536), .lowDuration(536)) SiB7 ();  // open: out
  Clock #(.highDuration(506), .lowDuration(506)) Si7 ();  // open: out
  Clock #(.highDuration(478), .lowDuration(478)) Do8 ();  // open: out
  Clock #(.highDuration(451), .lowDuration(451)) DoD8 ();  // open: out
  Clock #(.highDuration(426), .lowDuration(426)) Re8 ();  // open: out
  Clock #(.highDuration(402), .lowDuration(402)) ReD8 ();  // open: out
  Clock #(.highDuration(379), .lowDuration(379)) Mi8 ();  // open: out
  Clock #(.highDuration(358), .lowDuration(358)) Fa8 ();  // open: out
  Clock #(.highDuration(338), .lowDuration(338)) FaD8 ();  // open: out
  Clock #(.highDuration(319), .lowDuration(319)) Sol8 ();  // open: out
  Clock #(.highDuration(301), .lowDuration(301)) SolD8 ();  // open: out
  Clock #(.highDuration(284), .lowDuration(284)) La8 ();  // open: out
  Clock #(.highDuration(268), .lowDuration(268)) SiB8 ();  // open: out
  Clock #(.highDuration(253), .lowDuration(253)) Si8 ();  // open: out
  Demultiplexer #(.select(2), .enable("false")) demultiplexer_1 (
    .out0(demultiplexer_1_out0), .in(set_on), .sel(music));  // open: out1, out2, out3
  not not_1 (not_1_out, demultiplexer_1_out0);
  Clock #(.highDuration(400000), .lowDuration(400000)) clock_1 (.out(clock_1_out));
  music_givenTheme music_givenTheme_1 (
    .set_on(demultiplexer_1_out0), .Ds(ReD5_out), .E(Mi_out), .F(Fa_out), .Fs(FaD5_out), .G(Sol5_out),
    .B(Si5_out), .A2(La6_out), .B2(Si6_out), .reset(not_1_out), .music_clock(clock_1_out), .freq(buzzer_1));

  assign buzzer_0 = 1'b0;
endmodule

module music_givenTheme (
  input  set_on,
  input  Ds,
  input  E,
  input  F,
  input  Fs,
  input  G,
  input  B,
  input  A2,
  input  B2,
  input  reset,
  input  music_clock,
  output freq
);

  wire clock_1_out, multiplexer_1_out, music_givenTheme_logic_1_o_0, music_givenTheme_logic_1_o_1,
       music_givenTheme_logic_1_o_2, music_givenTheme_logic_1_o_3, not_1_out, not_2_out, not_3_out,
       not_4_out, or_1_out, shift_register_1_p2, shift_register_1_p3;
  wire [2:0] counter_1_q;
  wire [3:0] s_r_ff_4_q;

  Clock clock_1 (.out(clock_1_out));
  Counter #(.width(3), .max('h7)) counter_1 (
    .clr(or_1_out), .load(1'b0), .up(1'b1), .count(1'b1), .clk(music_clock), .D(3'b000), .Q(counter_1_q));  // open: carry
  or or_1 (or_1_out, reset, shift_register_1_p3);
  Multiplexer #(.select(4), .enable("false")) multiplexer_1 (
    .in0(B), .in1(E), .in2(G), .in3(F), .in4(E), .in5(B2), .in6(A2), .in7(Fs), .in8(E), .in9(G), .in10(F),
    .in11(Ds), .in12(F), .in13(B), .out(multiplexer_1_out), .sel(s_r_ff_4_q));  // open: in14, in15
  and and_1 (freq, set_on, multiplexer_1_out);
  // Probe on s_r_ff_4_q
  // Shift_Register #(.length(1)) shift_register_1: pin names not known; wires that end beside it: clock_1_out, shift_register_1_p2, shift_register_1_p3
  music_givenTheme_logic music_givenTheme_logic_1 (
    .C_2(counter_1_q[2]), .C_1(counter_1_q[1]), .C_0(counter_1_q[0]), .S_3(s_r_ff_4_q[3]),
    .S_2(s_r_ff_4_q[2]), .S_1(s_r_ff_4_q[1]), .S_0(s_r_ff_4_q[0]), .O_3(music_givenTheme_logic_1_o_3),
    .O_2(music_givenTheme_logic_1_o_2), .O_1(music_givenTheme_logic_1_o_1),
    .O_0(music_givenTheme_logic_1_o_0), .reset(shift_register_1_p2));
  S_R_Flip_Flop s_r_ff_1 (
    .S(music_givenTheme_logic_1_o_3), .R(not_1_out), .clk(clock_1_out), .Q(s_r_ff_4_q[3]), .reset(reset));  // open: Qn, preset
  not not_1 (not_1_out, music_givenTheme_logic_1_o_3);
  S_R_Flip_Flop s_r_ff_2 (
    .S(music_givenTheme_logic_1_o_2), .R(not_2_out), .clk(clock_1_out), .Q(s_r_ff_4_q[2]), .reset(reset));  // open: Qn, preset
  not not_2 (not_2_out, music_givenTheme_logic_1_o_2);
  S_R_Flip_Flop s_r_ff_3 (
    .S(music_givenTheme_logic_1_o_1), .R(not_3_out), .clk(clock_1_out), .Q(s_r_ff_4_q[1]), .reset(reset));  // open: Qn, preset
  not not_3 (not_3_out, music_givenTheme_logic_1_o_1);
  S_R_Flip_Flop s_r_ff_4 (
    .S(music_givenTheme_logic_1_o_0), .R(not_4_out), .clk(clock_1_out), .Q(s_r_ff_4_q[0]), .reset(reset));  // open: Qn, preset
  not not_4 (not_4_out, music_givenTheme_logic_1_o_0);
endmodule

module music_givenTheme_logic (
  input  C_2,
  input  C_1,
  input  C_0,
  input  S_3,
  input  S_2,
  input  S_1,
  input  S_0,
  output O_3,
  output O_2,
  output O_1,
  output O_0,
  output reset
);

  wire and_1_out, and_2_out, and_3_out, and_4_out, and_5_out, and_6_out, and_7_out, and_8_out, and_9_out,
       and_10_out, and_11_out, and_12_out, and_13_out, and_14_out, and_15_out, and_16_out, and_17_out,
       and_18_out, and_19_out, and_20_out, and_21_out, and_22_out, and_23_out, and_24_out, and_25_out,
       and_26_out, and_27_out, and_28_out, and_29_out, and_30_out, and_31_out, and_32_out, and_33_out,
       and_34_out, and_35_out, and_36_out, and_37_out, and_38_out, and_39_out, and_40_out, and_41_out,
       and_42_out, and_43_out, and_44_out, and_45_out, and_46_out, and_47_out, and_48_out, and_49_out,
       and_50_out, not_1_out, not_2_out, not_3_out, not_4_out, not_5_out, not_6_out, not_7_out, not_8_out,
       not_9_out, not_10_out, not_11_out, not_12_out, not_13_out, not_14_out, not_15_out, not_16_out,
       not_17_out, not_18_out, not_19_out, not_20_out, not_21_out, not_22_out, not_23_out, not_24_out,
       not_25_out, not_26_out, not_27_out, not_28_out, not_29_out, not_30_out, not_31_out, not_32_out,
       not_33_out, not_34_out, not_35_out, not_36_out, not_37_out, not_38_out, not_39_out, not_40_out,
       not_41_out, not_42_out, not_43_out, not_44_out, not_45_out, not_46_out, not_47_out, not_48_out,
       not_49_out, not_50_out, not_51_out, not_52_out, not_53_out, not_54_out, not_55_out, not_56_out,
       not_57_out, not_58_out, not_59_out, not_60_out, not_61_out, not_62_out, not_63_out, not_64_out,
       not_65_out, not_66_out, not_67_out, not_68_out, not_69_out, not_70_out, not_71_out, not_72_out,
       not_73_out, not_74_out, not_75_out, not_76_out, not_77_out, not_78_out, not_79_out, not_80_out,
       not_81_out, not_82_out, not_83_out, not_84_out, not_85_out, not_86_out, not_87_out, not_88_out,
       not_89_out, not_90_out, not_91_out, not_92_out, not_93_out, not_94_out, not_95_out, not_96_out,
       not_97_out, not_98_out, not_99_out, not_100_out, not_101_out, not_102_out, not_103_out, not_104_out,
       not_105_out, not_106_out, not_107_out, not_108_out, not_109_out, not_110_out, not_111_out,
       not_112_out, not_113_out, not_114_out, not_115_out, not_116_out, not_117_out, not_118_out,
       not_119_out, not_120_out, not_121_out, not_122_out, not_123_out, not_124_out, not_125_out,
       not_126_out, not_127_out, not_128_out, not_129_out, not_130_out, not_131_out, not_132_out,
       not_133_out, not_134_out, not_135_out, not_136_out, not_137_out, not_138_out, not_139_out,
       not_140_out, not_141_out, not_142_out, not_143_out, not_144_out, not_145_out, not_146_out, not_147_out;

  not not_1 (not_1_out, C_2);
  not not_2 (not_2_out, C_1);
  not not_3 (not_3_out, C_0);
  not not_4 (not_4_out, S_2);
  not not_5 (not_5_out, C_1);
  not not_6 (not_6_out, C_0);
  not not_7 (not_7_out, S_0);
  not not_8 (not_8_out, C_1);
  not not_9 (not_9_out, C_0);
  not not_10 (not_10_out, C_1);
  not not_11 (not_11_out, S_3);
  not not_12 (not_12_out, C_2);
  not not_13 (not_13_out, C_1);
  not not_14 (not_14_out, C_0);
  not not_15 (not_15_out, S_3);
  not not_16 (not_16_out, C_1);
  not not_17 (not_17_out, C_0);
  not not_18 (not_18_out, S_0);
  not not_19 (not_19_out, C_1);
  not not_20 (not_20_out, S_3);
  not not_21 (not_21_out, S_1);
  not not_22 (not_22_out, C_1);
  not not_23 (not_23_out, S_3);
  not not_24 (not_24_out, S_0);
  not not_25 (not_25_out, C_2);
  not not_26 (not_26_out, C_0);
  not not_27 (not_27_out, S_3);
  not not_28 (not_28_out, C_1);
  not not_29 (not_29_out, C_0);
  not not_30 (not_30_out, C_2);
  not not_31 (not_31_out, S_0);
  not not_32 (not_32_out, C_1);
  not not_33 (not_33_out, C_0);
  not not_34 (not_34_out, S_0);
  not not_35 (not_35_out, C_1);
  not not_36 (not_36_out, S_3);
  not not_37 (not_37_out, S_2);
  not not_38 (not_38_out, C_1);
  not not_39 (not_39_out, S_3);
  not not_40 (not_40_out, S_0);
  not not_41 (not_41_out, C_1);
  not not_42 (not_42_out, C_0);
  not not_43 (not_43_out, C_2);
  not not_44 (not_44_out, C_2);
  not not_45 (not_45_out, C_2);
  not not_46 (not_46_out, C_1);
  not not_47 (not_47_out, S_2);
  not not_48 (not_48_out, C_2);
  not not_49 (not_49_out, C_0);
  not not_50 (not_50_out, S_3);
  not not_51 (not_51_out, C_2);
  not not_52 (not_52_out, S_3);
  not not_53 (not_53_out, S_2);
  not not_54 (not_54_out, C_1);
  not not_55 (not_55_out, C_0);
  not not_56 (not_56_out, S_2);
  not not_57 (not_57_out, S_1);
  not not_58 (not_58_out, C_1);
  not not_59 (not_59_out, S_3);
  not not_60 (not_60_out, S_2);
  not not_61 (not_61_out, C_1);
  not not_62 (not_62_out, S_3);
  not not_63 (not_63_out, S_1);
  not not_64 (not_64_out, C_2);
  not not_65 (not_65_out, C_1);
  not not_66 (not_66_out, C_0);
  not not_67 (not_67_out, C_2);
  not not_68 (not_68_out, C_0);
  not not_69 (not_69_out, C_2);
  not not_70 (not_70_out, C_1);
  not not_71 (not_71_out, S_3);
  not not_72 (not_72_out, S_2);
  not not_73 (not_73_out, C_2);
  not not_74 (not_74_out, C_2);
  not not_75 (not_75_out, C_2);
  not not_76 (not_76_out, C_0);
  not not_77 (not_77_out, S_3);
  not not_78 (not_78_out, S_2);
  not not_79 (not_79_out, S_1);
  not not_80 (not_80_out, C_2);
  not not_81 (not_81_out, C_0);
  not not_82 (not_82_out, S_2);
  not not_83 (not_83_out, C_2);
  not not_84 (not_84_out, C_0);
  not not_85 (not_85_out, S_1);
  not not_86 (not_86_out, C_2);
  not not_87 (not_87_out, S_2);
  not not_88 (not_88_out, S_1);
  not not_89 (not_89_out, C_1);
  not not_90 (not_90_out, C_0);
  not not_91 (not_91_out, S_3);
  not not_92 (not_92_out, S_1);
  not not_93 (not_93_out, C_1);
  not not_94 (not_94_out, S_3);
  not not_95 (not_95_out, S_0);
  not not_96 (not_96_out, C_2);
  not not_97 (not_97_out, C_1);
  not not_98 (not_98_out, S_3);
  not not_99 (not_99_out, S_2);
  not not_100 (not_100_out, S_0);
  not not_101 (not_101_out, C_2);
  not not_102 (not_102_out, C_1);
  not not_103 (not_103_out, S_2);
  not not_104 (not_104_out, S_1);
  not not_105 (not_105_out, C_2);
  not not_106 (not_106_out, C_0);
  not not_107 (not_107_out, S_3);
  not not_108 (not_108_out, S_2);
  not not_109 (not_109_out, S_1);
  not not_110 (not_110_out, S_0);
  not not_111 (not_111_out, C_2);
  not not_112 (not_112_out, C_0);
  not not_113 (not_113_out, S_3);
  not not_114 (not_114_out, S_2);
  not not_115 (not_115_out, C_2);
  not not_116 (not_116_out, C_0);
  not not_117 (not_117_out, S_3);
  not not_118 (not_118_out, S_1);
  not not_119 (not_119_out, C_2);
  not not_120 (not_120_out, C_0);
  not not_121 (not_121_out, S_2);
  not not_122 (not_122_out, S_0);
  not not_123 (not_123_out, C_2);
  not not_124 (not_124_out, C_0);
  not not_125 (not_125_out, S_1);
  not not_126 (not_126_out, S_0);
  not not_127 (not_127_out, C_2);
  not not_128 (not_128_out, S_3);
  not not_129 (not_129_out, S_2);
  not not_130 (not_130_out, S_1);
  not not_131 (not_131_out, C_2);
  not not_132 (not_132_out, S_2);
  not not_133 (not_133_out, S_1);
  not not_134 (not_134_out, S_0);
  not not_135 (not_135_out, C_1);
  not not_136 (not_136_out, C_0);
  not not_137 (not_137_out, S_3);
  not not_138 (not_138_out, S_1);
  not not_139 (not_139_out, S_0);
  not not_140 (not_140_out, C_1);
  not not_141 (not_141_out, C_0);
  not not_142 (not_142_out, S_2);
  not not_143 (not_143_out, C_1);
  not not_144 (not_144_out, C_0);
  not not_145 (not_145_out, S_1);
  not not_146 (not_146_out, C_1);
  not not_147 (not_147_out, S_3);
  and and_1 (and_1_out, not_1_out, S_3);
  and and_2 (and_2_out, not_2_out, not_3_out, S_3, not_4_out);
  and and_3 (and_3_out, not_5_out, not_6_out, S_3, not_7_out);
  and and_4 (and_4_out, not_8_out, not_9_out, S_3, S_1);
  and and_5 (and_5_out, C_2, not_10_out, C_0, not_11_out, S_2, S_1, S_0);
  and and_6 (and_6_out, not_12_out, S_2);
  and and_7 (and_7_out, not_13_out, not_14_out, not_15_out, S_2);
  and and_8 (and_8_out, not_16_out, not_17_out, S_2, not_18_out);
  and and_9 (and_9_out, not_19_out, not_20_out, S_2, not_21_out);
  and and_10 (and_10_out, not_22_out, not_23_out, S_2, not_24_out);
  and and_11 (and_11_out, not_25_out, C_1, not_26_out, not_27_out, S_1, S_0);
  and and_12 (and_12_out, C_2, not_28_out, not_29_out, S_3, S_1, S_0);
  and and_13 (and_13_out, not_30_out, S_1, not_31_out);
  and and_14 (and_14_out, not_32_out, not_33_out, S_1, not_34_out);
  and and_15 (and_15_out, not_35_out, not_36_out, not_37_out, S_1);
  and and_16 (and_16_out, not_38_out, not_39_out, S_1, not_40_out);
  and and_17 (and_17_out, not_41_out, not_42_out, S_2, S_1);
  and and_18 (and_18_out, not_43_out, S_3, S_1);
  and and_19 (and_19_out, not_44_out, C_0, S_1);
  and and_20 (and_20_out, not_45_out, not_46_out, C_0, S_3, not_47_out, S_0);
  and and_21 (and_21_out, not_48_out, C_1, not_49_out, not_50_out, S_2, S_0);
  and and_22 (and_22_out, not_51_out, C_1, C_0, not_52_out, not_53_out, S_0);
  and and_23 (and_23_out, not_54_out, not_55_out, not_56_out, not_57_out, S_0);
  and and_24 (and_24_out, not_58_out, not_59_out, not_60_out, S_0);
  and and_25 (and_25_out, not_61_out, not_62_out, not_63_out, S_0);
  and and_26 (and_26_out, not_64_out, S_2, S_1, S_0);
  and and_27 (and_27_out, not_65_out, not_66_out, S_2, S_1, S_0);
  and and_28 (and_28_out, not_67_out, not_68_out, S_3, S_0);
  and and_29 (and_29_out, not_69_out, not_70_out, C_0, not_71_out, not_72_out, S_1);
  and and_30 (and_30_out, not_73_out, C_0, S_1, S_0);
  and and_31 (and_31_out, not_74_out, C_0, S_2, S_0);
  and and_32 (and_32_out, not_75_out, C_1, not_76_out, not_77_out, not_78_out, not_79_out);
  and and_33 (and_33_out, not_80_out, C_1, not_81_out, S_3, not_82_out, S_1);
  and and_34 (and_34_out, not_83_out, C_1, not_84_out, S_3, S_2, not_85_out);
  and and_35 (and_35_out, not_86_out, C_1, C_0, S_3, not_87_out, not_88_out);
  and and_36 (and_36_out, C_2, not_89_out, not_90_out, not_91_out, S_2, not_92_out);
  and and_37 (and_37_out, C_2, not_93_out, C_0, not_94_out, S_2, S_1, not_95_out);
  and and_38 (and_38_out, not_96_out, not_97_out, C_0, not_98_out, not_99_out, S_1, not_100_out);
  and and_39 (and_39_out, not_101_out, not_102_out, C_0, S_3, not_103_out, not_104_out, S_0);
  and and_40 (and_40_out, not_105_out, C_1, not_106_out, not_107_out, not_108_out, not_109_out, not_110_out);
  and and_41 (and_41_out, not_111_out, C_1, not_112_out, not_113_out, not_114_out, S_1, S_0);
  and and_42 (and_42_out, not_115_out, C_1, not_116_out, not_117_out, S_2, not_118_out, S_0);
  and and_43 (and_43_out, not_119_out, C_1, not_120_out, S_3, not_121_out, S_1, not_122_out);
  and and_44 (and_44_out, not_123_out, C_1, not_124_out, S_3, S_2, not_125_out, not_126_out);
  and and_45 (and_45_out, not_127_out, C_1, C_0, not_128_out, not_129_out, not_130_out, S_0);
  and and_46 (and_46_out, not_131_out, C_1, C_0, S_3, not_132_out, not_133_out, not_134_out);
  and and_47 (and_47_out, C_2, not_135_out, not_136_out, not_137_out, S_2, not_138_out, not_139_out);
  and and_48 (and_48_out, C_2, not_140_out, not_141_out, S_3, not_142_out, S_1, S_0);
  and and_49 (and_49_out, C_2, not_143_out, not_144_out, S_3, S_2, not_145_out, S_0);
  and and_50 (and_50_out, C_2, not_146_out, C_0, not_147_out, S_2, S_1);
  or or_1 (O_3, and_1_out, and_2_out, and_3_out, and_4_out, and_5_out);
  or or_2 (O_2, and_6_out, and_7_out, and_8_out, and_9_out, and_10_out, and_11_out, and_12_out);
  or or_3 (O_1, and_13_out, and_14_out, and_15_out, and_16_out, and_17_out, and_18_out, and_19_out, and_20_out, and_21_out, and_22_out);
  or or_4 (O_0, and_23_out, and_24_out, and_25_out, and_26_out, and_27_out, and_28_out, and_29_out, and_30_out, and_31_out, and_32_out, and_33_out, and_34_out, and_35_out, and_36_out, and_37_out);
  or or_5 (reset, and_38_out, and_39_out, and_40_out, and_41_out, and_42_out, and_43_out, and_44_out, and_45_out, and_46_out, and_47_out, and_48_out, and_49_out, and_50_out);
endmodule

module RV230_allegro (
  input  set_on,
  input  La,
  input  Si,
  input  DoD2,
  input  Re2,
  input  Mi2,
  input  FaD2,
  input  Sol22,
  input  La2,
  input  Si2,
  input  Soupir,
  input  reset,
  input  music_clock,
  output freq
);

  wire clock_1_out, multiplexer_1_out, multiplexer_2_out, multiplexer_3_out, multiplexer_4_out,
       multiplexer_5_out, or_1_out, shift_register_1_p1, shift_register_1_p3;
  wire [2:0] counter_1_q;
  wire [7:0] register_1_q, rv230_allegro_logic_1_s_out_0;

  Multiplexer #(.select(5), .enable("false")) multiplexer_1 (
    .in0(FaD2), .in1(FaD2), .in2(Soupir), .in3(FaD2), .in4(FaD2), .in5(La2), .in6(Sol22), .in7(La2),
    .in8(La2), .in9(Re2), .in10(Soupir), .in11(Re2), .in12(Re2), .in13(FaD2), .in14(Mi2), .in15(FaD2),
    .in16(FaD2), .in17(Si), .in18(Soupir), .in19(Si), .in20(Si), .in21(Re2), .in22(DoD2), .in23(Re2),
    .in24(Re2), .in25(DoD2), .in26(Soupir), .in27(La2), .in28(Mi2), .in29(Re2), .in30(Mi2), .in31(Sol22),
    .out(multiplexer_1_out), .sel(register_1_q[4:0]));
  Multiplexer #(.select(5), .enable("false")) multiplexer_2 (
    .in0(FaD2), .in1(Mi2), .in2(FaD2), .in3(La2), .in4(Sol22), .in5(FaD2), .in6(Sol22), .in7(La2),
    .in8(Sol22), .in9(Si2), .in10(La2), .in11(Sol22), .in12(FaD2), .in13(Mi2), .in14(FaD2), .in15(Sol22),
    .in16(FaD2), .in17(La2), .in18(Sol22), .in19(FaD2), .in20(Mi2), .in21(La), .in22(Soupir), .in23(La2),
    .in24(FaD2), .in25(La2), .in26(Sol22), .in27(La2), .in28(La2), .in29(Mi2), .in30(La2), .in31(Sol22),
    .out(multiplexer_2_out), .sel(register_1_q[4:0]));
  Multiplexer #(.select(5), .enable("false")) multiplexer_3 (
    .in0(La2), .in1(La2), .in2(FaD2), .in3(La2), .in4(Sol22), .in5(La2), .in6(La2), .in7(Mi2), .in8(La2),
    .in9(Sol22), .in10(La2), .in11(La2), .in12(FaD2), .in13(La2), .in14(Sol22), .in15(FaD2), .in16(Mi2),
    .in17(Re2), .in18(DoD2), .in19(Si), .in20(La), .in21(Re2), .in22(La), .in23(DoD2), .in24(Re2),
    .in25(FaD2), .in26(Mi2), .in27(Re2), .in28(Mi2), .in29(FaD2), .in30(Sol22), .in31(FaD2),
    .out(multiplexer_3_out), .sel(register_1_q[4:0]));
  Multiplexer #(.select(5), .enable("false")) multiplexer_4 (
    .in0(Mi2), .in1(Re2), .in2(Mi2), .in3(FaD2), .in4(Sol22), .in5(La2), .in6(Sol22), .in7(FaD2), .in8(Mi2),
    .in9(La), .in10(Soupir), .out(multiplexer_4_out), .sel(register_1_q[4:0]));  // open: in11, in12, in13, in14, in15, in16, in17, in18, in19, in20, in21, in22, in23, in24, in25, in26, in27, in28, in29, in30, in31
  Clock clock_1 (.out(clock_1_out));
  Counter #(.width(3), .max('h7)) counter_1 (
    .clr(or_1_out), .load(1'b0), .up(1'b1), .count(1'b1), .clk(music_clock), .D(3'b000), .Q(counter_1_q));  // open: carry
  or or_1 (or_1_out, reset, shift_register_1_p1);
  Multiplexer #(.select(3), .enable("false")) multiplexer_5 (
    .in0(multiplexer_1_out), .in1(multiplexer_2_out), .in2(multiplexer_3_out), .in3(multiplexer_4_out),
    .out(multiplexer_5_out), .sel(register_1_q[7:5]));  // open: in4, in5, in6, in7
  and and_1 (freq, set_on, multiplexer_5_out);
  // Shift_Register #(.length(1)) shift_register_1: pin names not known; wires that end beside it: shift_register_1_p1, clock_1_out, shift_register_1_p3, shift_register_1_p1
  RV230_allegro_logic rv230_allegro_logic_1 (
    .counter_2(counter_1_q[2]), .counter_1(counter_1_q[1]), .counter_0(counter_1_q[0]),
    .state_7(register_1_q[7]), .state_6(register_1_q[6]), .state_5(register_1_q[5]),
    .state_4(register_1_q[4]), .state_3(register_1_q[3]), .state_2(register_1_q[2]),
    .state_1(register_1_q[1]), .state_0(register_1_q[0]), .s_out_7(rv230_allegro_logic_1_s_out_0[7]),
    .s_out_6(rv230_allegro_logic_1_s_out_0[6]), .s_out_5(rv230_allegro_logic_1_s_out_0[5]),
    .s_out_4(rv230_allegro_logic_1_s_out_0[4]), .s_out_3(rv230_allegro_logic_1_s_out_0[3]),
    .s_out_2(rv230_allegro_logic_1_s_out_0[2]), .s_out_1(rv230_allegro_logic_1_s_out_0[1]),
    .s_out_0(rv230_allegro_logic_1_s_out_0[0]), .reset(shift_register_1_p3));
  Register register_1 (.D(rv230_allegro_logic_1_s_out_0), .en(1'b1), .clk(clock_1_out), .Q(register_1_q), .clr(reset));
endmodule

module RV230_allegro_logic (
  input  counter_2,
  input  counter_1,
  input  counter_0,
  input  state_7,
  input  state_6,
  input  state_5,
  input  state_4,
  input  state_3,
  input  state_2,
  input  state_1,
  input  state_0,
  output s_out_7,
  output s_out_6,
  output s_out_5,
  output s_out_4,
  output s_out_3,
  output s_out_2,
  output s_out_1,
  output s_out_0,
  output reset
);

  wire and_1_out, and_2_out, and_3_out, and_4_out, and_5_out, and_6_out, and_7_out, and_8_out, and_9_out,
       and_10_out, and_11_out, and_12_out, and_13_out, and_14_out, and_15_out, and_16_out, and_17_out,
       and_18_out, and_19_out, and_20_out, and_21_out, and_22_out, and_23_out, and_24_out, and_25_out,
       and_26_out, and_27_out, and_28_out, and_29_out, and_30_out, and_31_out, and_32_out, and_33_out,
       and_34_out, and_35_out, and_36_out, and_37_out, and_38_out, and_39_out, and_40_out, and_41_out,
       and_42_out, and_43_out, and_44_out, and_45_out, and_46_out, and_47_out, and_48_out, and_49_out,
       and_50_out, and_51_out, and_52_out, and_53_out, and_54_out, and_55_out, and_56_out, and_57_out,
       and_58_out, and_59_out, and_60_out, and_61_out, and_62_out, and_63_out, and_64_out, and_65_out,
       and_66_out, and_67_out, and_68_out, and_69_out, and_70_out, and_71_out, and_72_out, not_1_out,
       not_2_out, not_3_out, not_4_out, not_5_out, not_6_out, not_7_out, not_8_out, not_9_out, not_10_out,
       not_11_out, not_12_out, not_13_out, not_14_out, not_15_out, not_16_out, not_17_out, not_18_out,
       not_19_out, not_20_out, not_21_out, not_22_out, not_23_out, not_24_out, not_25_out, not_26_out,
       not_27_out, not_28_out, not_29_out, not_30_out, not_31_out, not_32_out, not_33_out, not_34_out,
       not_36_out, not_37_out, not_38_out, not_39_out, not_40_out, not_41_out, not_42_out, not_43_out,
       not_44_out, not_45_out, not_46_out, not_47_out, not_48_out, not_49_out, not_50_out, not_51_out,
       not_52_out, not_53_out, not_54_out, not_55_out, not_56_out, not_57_out, not_58_out, not_59_out,
       not_60_out, not_61_out, not_62_out, not_63_out, not_64_out, not_65_out, not_66_out, not_67_out,
       not_68_out, not_69_out, not_70_out, not_71_out, not_72_out, not_73_out, not_74_out, not_75_out,
       not_76_out, not_77_out, not_78_out, not_79_out, not_80_out, not_81_out, not_82_out, not_83_out,
       not_84_out, not_85_out, not_86_out, not_87_out, not_88_out, not_89_out, not_90_out, not_91_out,
       not_92_out, not_93_out, not_94_out, not_95_out, not_96_out, not_97_out, not_98_out, not_99_out,
       not_100_out, not_101_out, not_102_out, not_103_out, not_104_out, not_105_out, not_106_out,
       not_107_out, not_108_out, not_109_out, not_110_out, not_111_out, not_112_out, not_113_out,
       not_114_out, not_115_out, not_116_out, not_117_out, not_118_out, not_119_out, not_120_out,
       not_121_out, not_122_out, not_123_out, not_124_out, not_125_out, not_126_out, not_127_out,
       not_128_out, not_129_out, not_130_out, not_131_out, not_132_out, not_133_out, not_134_out,
       not_135_out, not_136_out, not_137_out, not_138_out, not_139_out, not_140_out, not_141_out,
       not_142_out, not_143_out, not_144_out, not_145_out, not_146_out, not_147_out, not_148_out,
       not_149_out, not_150_out, not_151_out, not_152_out, not_153_out, not_154_out, not_155_out,
       not_156_out, not_157_out, not_158_out, not_159_out, not_160_out, not_161_out, not_162_out,
       not_163_out, not_164_out, not_165_out, not_166_out, not_167_out, not_168_out, not_169_out,
       not_170_out, not_171_out, not_172_out, not_173_out, not_174_out, not_175_out, not_176_out,
       not_177_out, not_178_out, not_179_out, not_180_out, not_181_out, not_182_out, not_183_out,
       not_184_out, not_185_out, not_186_out, not_187_out, not_188_out, not_189_out, not_190_out,
       not_191_out, not_192_out, not_193_out, not_194_out, not_195_out, not_196_out, not_197_out,
       not_198_out, not_199_out, not_200_out, not_201_out, not_202_out, not_203_out, not_204_out,
       not_205_out, not_206_out, not_207_out, not_208_out, not_209_out, not_210_out, not_211_out,
       not_212_out, not_213_out, not_214_out, not_215_out, not_216_out, not_217_out, not_218_out,
       not_219_out, not_220_out, not_221_out, not_222_out, not_223_out, not_224_out, not_225_out,
       not_226_out, not_227_out, not_228_out, not_229_out, not_230_out, not_231_out, not_232_out,
       not_233_out, not_234_out, not_235_out, not_236_out, not_237_out, not_238_out, not_239_out,
       not_240_out, not_241_out, not_242_out, not_243_out, not_244_out, not_245_out, not_246_out,
       not_247_out, not_248_out, not_249_out, not_250_out, not_251_out, not_252_out, not_253_out,
       not_254_out, not_255_out, not_256_out, not_257_out, not_258_out, not_259_out, not_260_out,
       not_261_out, not_262_out, not_263_out, not_264_out, not_265_out, not_266_out, not_267_out,
       not_268_out, not_269_out, not_270_out, not_271_out, not_272_out, not_273_out, not_274_out,
       not_275_out, not_276_out, not_277_out, not_278_out, not_279_out, not_280_out, not_281_out,
       not_282_out, not_283_out, not_284_out, not_285_out, not_286_out, not_287_out, not_288_out,
       not_289_out, not_290_out, not_291_out, not_292_out, not_293_out, not_294_out, or_7_out, or_8_out;

  not not_1 (not_1_out, state_5);
  not not_2 (not_2_out, state_3);
  not not_3 (not_3_out, state_1);
  not not_4 (not_4_out, state_0);
  not not_5 (not_5_out, state_5);
  not not_6 (not_6_out, state_6);
  not not_7 (not_7_out, state_4);
  not not_8 (not_8_out, state_6);
  not not_9 (not_9_out, state_2);
  not not_10 (not_10_out, state_3);
  not not_11 (not_11_out, state_1);
  not not_12 (not_12_out, state_0);
  not not_13 (not_13_out, state_4);
  not not_14 (not_14_out, state_3);
  not not_15 (not_15_out, state_2);
  not not_16 (not_16_out, state_1);
  not not_17 (not_17_out, state_0);
  not not_18 (not_18_out, state_3);
  not not_19 (not_19_out, state_6);
  not not_20 (not_20_out, state_2);
  not not_21 (not_21_out, state_5);
  not not_22 (not_22_out, state_2);
  not not_23 (not_23_out, state_1);
  not not_24 (not_24_out, state_0);
  not not_25 (not_25_out, state_6);
  not not_26 (not_26_out, state_2);
  not not_27 (not_27_out, state_5);
  not not_28 (not_28_out, state_2);
  not not_29 (not_29_out, state_3);
  not not_30 (not_30_out, state_2);
  not not_31 (not_31_out, state_1);
  not not_32 (not_32_out, state_0);
  not not_33 (not_33_out, state_1);
  not not_34 (not_34_out, state_0);
  not not_35 (s_out_0, state_0);
  not not_36 (not_36_out, counter_2);
  not not_37 (not_37_out, counter_1);
  not not_38 (not_38_out, state_7);
  not not_39 (not_39_out, state_6);
  not not_40 (not_40_out, state_4);
  not not_41 (not_41_out, state_3);
  not not_42 (not_42_out, state_2);
  not not_43 (not_43_out, counter_2);
  not not_44 (not_44_out, counter_1);
  not not_45 (not_45_out, state_7);
  not not_46 (not_46_out, state_6);
  not not_47 (not_47_out, state_5);
  not not_48 (not_48_out, state_3);
  not not_49 (not_49_out, counter_2);
  not not_50 (not_50_out, counter_1);
  not not_51 (not_51_out, state_7);
  not not_52 (not_52_out, state_6);
  not not_53 (not_53_out, state_4);
  not not_54 (not_54_out, counter_2);
  not not_55 (not_55_out, counter_1);
  not not_56 (not_56_out, state_7);
  not not_57 (not_57_out, state_6);
  not not_58 (not_58_out, state_4);
  not not_59 (not_59_out, state_0);
  not not_60 (not_60_out, counter_2);
  not not_61 (not_61_out, counter_1);
  not not_62 (not_62_out, state_7);
  not not_63 (not_63_out, state_6);
  not not_64 (not_64_out, state_3);
  not not_65 (not_65_out, state_1);
  not not_66 (not_66_out, state_0);
  not not_67 (not_67_out, counter_2);
  not not_68 (not_68_out, counter_1);
  not not_69 (not_69_out, state_7);
  not not_70 (not_70_out, state_6);
  not not_71 (not_71_out, state_5);
  not not_72 (not_72_out, counter_2);
  not not_73 (not_73_out, counter_1);
  not not_74 (not_74_out, state_7);
  not not_75 (not_75_out, state_5);
  not not_76 (not_76_out, counter_2);
  not not_77 (not_77_out, counter_1);
  not not_78 (not_78_out, state_7);
  not not_79 (not_79_out, state_6);
  not not_80 (not_80_out, state_5);
  not not_81 (not_81_out, counter_2);
  not not_82 (not_82_out, counter_1);
  not not_83 (not_83_out, state_7);
  not not_84 (not_84_out, state_6);
  not not_85 (not_85_out, state_4);
  not not_86 (not_86_out, counter_2);
  not not_87 (not_87_out, counter_1);
  not not_88 (not_88_out, state_7);
  not not_89 (not_89_out, state_6);
  not not_90 (not_90_out, state_3);
  not not_91 (not_91_out, state_2);
  not not_92 (not_92_out, counter_2);
  not not_93 (not_93_out, counter_1);
  not not_94 (not_94_out, state_7);
  not not_95 (not_95_out, state_4);
  not not_96 (not_96_out, state_3);
  not not_97 (not_97_out, state_2);
  not not_98 (not_98_out, state_1);
  not not_99 (not_99_out, counter_2);
  not not_100 (not_100_out, counter_1);
  not not_101 (not_101_out, state_7);
  not not_102 (not_102_out, state_4);
  not not_103 (not_103_out, state_2);
  not not_104 (not_104_out, state_1);
  not not_105 (not_105_out, state_0);
  not not_106 (not_106_out, counter_2);
  not not_107 (not_107_out, counter_1);
  not not_108 (not_108_out, state_7);
  not not_109 (not_109_out, state_6);
  not not_110 (not_110_out, state_2);
  not not_111 (not_111_out, counter_2);
  not not_112 (not_112_out, counter_1);
  not not_113 (not_113_out, state_7);
  not not_114 (not_114_out, state_4);
  not not_115 (not_115_out, state_3);
  not not_116 (not_116_out, counter_2);
  not not_117 (not_117_out, counter_1);
  not not_118 (not_118_out, state_7);
  not not_119 (not_119_out, state_6);
  not not_120 (not_120_out, counter_2);
  not not_121 (not_121_out, counter_1);
  not not_122 (not_122_out, state_7);
  not not_123 (not_123_out, state_4);
  not not_124 (not_124_out, state_2);
  not not_125 (not_125_out, counter_2);
  not not_126 (not_126_out, counter_1);
  not not_127 (not_127_out, state_7);
  not not_128 (not_128_out, state_5);
  not not_129 (not_129_out, state_3);
  not not_130 (not_130_out, state_1);
  not not_131 (not_131_out, state_0);
  not not_132 (not_132_out, counter_2);
  not not_133 (not_133_out, counter_1);
  not not_134 (not_134_out, state_7);
  not not_135 (not_135_out, state_5);
  not not_136 (not_136_out, state_4);
  not not_137 (not_137_out, state_3);
  not not_138 (not_138_out, state_1);
  not not_139 (not_139_out, counter_2);
  not not_140 (not_140_out, counter_1);
  not not_141 (not_141_out, state_7);
  not not_142 (not_142_out, state_5);
  not not_143 (not_143_out, state_4);
  not not_144 (not_144_out, state_1);
  not not_145 (not_145_out, counter_2);
  not not_146 (not_146_out, counter_1);
  not not_147 (not_147_out, state_7);
  not not_148 (not_148_out, state_5);
  not not_149 (not_149_out, state_0);
  not not_150 (not_150_out, counter_2);
  not not_151 (not_151_out, counter_1);
  not not_152 (not_152_out, state_7);
  not not_153 (not_153_out, state_5);
  not not_154 (not_154_out, state_3);
  not not_155 (not_155_out, state_2);
  not not_156 (not_156_out, counter_2);
  not not_157 (not_157_out, counter_1);
  not not_158 (not_158_out, state_7);
  not not_159 (not_159_out, state_5);
  not not_160 (not_160_out, state_2);
  not not_161 (not_161_out, counter_2);
  not not_162 (not_162_out, counter_0);
  not not_163 (not_163_out, state_7);
  not not_164 (not_164_out, state_6);
  not not_165 (not_165_out, state_5);
  not not_166 (not_166_out, state_4);
  not not_167 (not_167_out, state_1);
  not not_168 (not_168_out, counter_2);
  not not_169 (not_169_out, counter_0);
  not not_170 (not_170_out, state_7);
  not not_171 (not_171_out, state_6);
  not not_172 (not_172_out, state_5);
  not not_173 (not_173_out, state_2);
  not not_174 (not_174_out, state_1);
  not not_175 (not_175_out, counter_2);
  not not_176 (not_176_out, counter_0);
  not not_177 (not_177_out, state_7);
  not not_178 (not_178_out, state_6);
  not not_179 (not_179_out, state_5);
  not not_180 (not_180_out, state_2);
  not not_181 (not_181_out, state_1);
  not not_182 (not_182_out, counter_2);
  not not_183 (not_183_out, counter_0);
  not not_184 (not_184_out, state_7);
  not not_185 (not_185_out, state_6);
  not not_186 (not_186_out, state_3);
  not not_187 (not_187_out, state_1);
  not not_188 (not_188_out, counter_2);
  not not_189 (not_189_out, counter_0);
  not not_190 (not_190_out, state_7);
  not not_191 (not_191_out, state_5);
  not not_192 (not_192_out, state_3);
  not not_193 (not_193_out, state_1);
  not not_194 (not_194_out, counter_2);
  not not_195 (not_195_out, counter_0);
  not not_196 (not_196_out, state_7);
  not not_197 (not_197_out, state_6);
  not not_198 (not_198_out, state_5);
  not not_199 (not_199_out, state_2);
  not not_200 (not_200_out, counter_2);
  not not_201 (not_201_out, counter_0);
  not not_202 (not_202_out, state_7);
  not not_203 (not_203_out, state_6);
  not not_204 (not_204_out, state_3);
  not not_205 (not_205_out, counter_2);
  not not_206 (not_206_out, counter_0);
  not not_207 (not_207_out, state_7);
  not not_208 (not_208_out, state_6);
  not not_209 (not_209_out, state_1);
  not not_210 (not_210_out, counter_2);
  not not_211 (not_211_out, counter_0);
  not not_212 (not_212_out, state_7);
  not not_213 (not_213_out, state_6);
  not not_214 (not_214_out, state_0);
  not not_215 (not_215_out, counter_2);
  not not_216 (not_216_out, counter_0);
  not not_217 (not_217_out, state_7);
  not not_218 (not_218_out, state_5);
  not not_219 (not_219_out, state_4);
  not not_220 (not_220_out, state_3);
  not not_221 (not_221_out, state_2);
  not not_222 (not_222_out, counter_2);
  not not_223 (not_223_out, counter_0);
  not not_224 (not_224_out, state_7);
  not not_225 (not_225_out, state_4);
  not not_226 (not_226_out, state_3);
  not not_227 (not_227_out, state_2);
  not not_228 (not_228_out, counter_2);
  not not_229 (not_229_out, counter_0);
  not not_230 (not_230_out, state_7);
  not not_231 (not_231_out, state_4);
  not not_232 (not_232_out, state_3);
  not not_233 (not_233_out, state_0);
  not not_234 (not_234_out, counter_2);
  not not_235 (not_235_out, counter_0);
  not not_236 (not_236_out, state_7);
  not not_237 (not_237_out, state_5);
  not not_238 (not_238_out, state_4);
  not not_239 (not_239_out, state_2);
  not not_240 (not_240_out, counter_2);
  not not_241 (not_241_out, counter_0);
  not not_242 (not_242_out, state_7);
  not not_243 (not_243_out, state_5);
  not not_244 (not_244_out, state_3);
  not not_245 (not_245_out, counter_2);
  not not_246 (not_246_out, counter_0);
  not not_247 (not_247_out, state_7);
  not not_248 (not_248_out, state_5);
  not not_249 (not_249_out, state_1);
  not not_250 (not_250_out, state_0);
  not not_251 (not_251_out, counter_2);
  not not_252 (not_252_out, counter_0);
  not not_253 (not_253_out, state_7);
  not not_254 (not_254_out, state_5);
  not not_255 (not_255_out, state_1);
  not not_256 (not_256_out, counter_2);
  not not_257 (not_257_out, counter_0);
  not not_258 (not_258_out, state_7);
  not not_259 (not_259_out, state_4);
  not not_260 (not_260_out, state_2);
  not not_261 (not_261_out, state_0);
  not not_262 (not_262_out, counter_2);
  not not_263 (not_263_out, counter_0);
  not not_264 (not_264_out, state_7);
  not not_265 (not_265_out, state_4);
  not not_266 (not_266_out, state_3);
  not not_267 (not_267_out, state_1);
  not not_268 (not_268_out, counter_2);
  not not_269 (not_269_out, counter_0);
  not not_270 (not_270_out, state_7);
  not not_271 (not_271_out, state_4);
  not not_272 (not_272_out, state_2);
  not not_273 (not_273_out, state_1);
  not not_274 (not_274_out, counter_1);
  not not_275 (not_275_out, counter_0);
  not not_276 (not_276_out, state_7);
  not not_277 (not_277_out, state_6);
  not not_278 (not_278_out, state_5);
  not not_279 (not_279_out, state_2);
  not not_280 (not_280_out, state_0);
  not not_281 (not_281_out, counter_0);
  not not_282 (not_282_out, state_7);
  not not_283 (not_283_out, state_6);
  not not_284 (not_284_out, state_5);
  not not_285 (not_285_out, state_4);
  not not_286 (not_286_out, state_2);
  not not_287 (not_287_out, state_0);
  not not_288 (not_288_out, counter_0);
  not not_289 (not_289_out, state_7);
  not not_290 (not_290_out, state_6);
  not not_291 (not_291_out, state_5);
  not not_292 (not_292_out, state_3);
  not not_293 (not_293_out, state_2);
  not not_294 (not_294_out, state_0);
  and and_1 (and_1_out, state_6, not_1_out);
  and and_2 (and_2_out, state_6, not_2_out);
  and and_3 (and_3_out, state_6, not_3_out);
  and and_4 (and_4_out, state_6, not_4_out);
  and and_5 (and_5_out, counter_0, state_5, state_4, state_2, state_1);
  and and_6 (and_6_out, not_5_out, state_4, state_3, state_2, state_1, state_0);
  and and_7 (and_7_out, not_6_out, state_5, not_7_out);
  and and_8 (and_8_out, not_8_out, state_5, not_9_out);
  and and_9 (and_9_out, state_5, not_10_out);
  and and_10 (and_10_out, state_5, not_11_out);
  and and_11 (and_11_out, state_5, not_12_out);
  and and_12 (and_12_out, not_13_out, state_3, state_2, state_1, state_0);
  and and_13 (and_13_out, state_4, not_14_out);
  and and_14 (and_14_out, state_4, not_15_out);
  and and_15 (and_15_out, state_4, not_16_out);
  and and_16 (and_16_out, state_4, not_17_out);
  and and_17 (and_17_out, not_18_out, state_2, state_1, state_0);
  and and_18 (and_18_out, not_19_out, state_3, not_20_out);
  and and_19 (and_19_out, not_21_out, state_3, not_22_out);
  and and_20 (and_20_out, state_3, not_23_out);
  and and_21 (and_21_out, state_3, not_24_out);
  and and_22 (and_22_out, not_25_out, not_26_out, state_1, state_0);
  and and_23 (and_23_out, not_27_out, not_28_out, state_1, state_0);
  and and_24 (and_24_out, not_29_out, not_30_out, state_1, state_0);
  and and_25 (and_25_out, state_2, not_31_out);
  and and_26 (and_26_out, state_2, not_32_out);
  and and_27 (and_27_out, not_33_out, state_0);
  or or_1 (s_out_1, and_27_out, and_28_out);
  and and_28 (and_28_out, state_1, not_34_out);
  and and_29 (and_29_out, not_36_out, not_37_out, counter_0, not_38_out, not_39_out, not_40_out, not_41_out, not_42_out, state_0);
  and and_30 (and_30_out, not_43_out, not_44_out, counter_0, not_45_out, not_46_out, not_47_out, not_48_out, state_1, state_0);
  and and_31 (and_31_out, not_49_out, not_50_out, counter_0, not_51_out, not_52_out, not_53_out, state_1, state_0);
  and and_32 (and_32_out, not_54_out, not_55_out, counter_0, not_56_out, not_57_out, not_58_out, state_2, not_59_out);
  and and_33 (and_33_out, not_60_out, not_61_out, counter_0, not_62_out, not_63_out, not_64_out, state_2, not_65_out, not_66_out);
  and and_34 (and_34_out, not_67_out, not_68_out, counter_0, not_69_out, not_70_out, not_71_out, state_2, state_1);
  and and_35 (and_35_out, not_72_out, not_73_out, counter_0, not_74_out, not_75_out, state_3, state_2, state_1);
  and and_36 (and_36_out, not_76_out, not_77_out, counter_0, not_78_out, not_79_out, not_80_out, state_4, state_3, state_2, state_0);
  and and_37 (and_37_out, not_81_out, not_82_out, counter_0, not_83_out, not_84_out, state_5, not_85_out);
  and and_38 (and_38_out, not_86_out, not_87_out, counter_0, not_88_out, not_89_out, state_5, not_90_out, not_91_out);
  and and_39 (and_39_out, not_92_out, not_93_out, counter_0, not_94_out, state_5, not_95_out, not_96_out, not_97_out, not_98_out);
  and and_40 (and_40_out, not_99_out, not_100_out, counter_0, not_101_out, state_5, not_102_out, not_103_out, not_104_out, not_105_out);
  and and_41 (and_41_out, not_106_out, not_107_out, counter_0, not_108_out, not_109_out, state_5, not_110_out, state_1);
  and and_42 (and_42_out, not_111_out, not_112_out, counter_0, not_113_out, state_5, not_114_out, not_115_out, state_2, state_1, state_0);
  and and_43 (and_43_out, not_116_out, not_117_out, counter_0, not_118_out, not_119_out, state_5, state_3, state_1, state_0);
  and and_44 (and_44_out, not_120_out, not_121_out, counter_0, not_122_out, state_5, not_123_out, state_3, not_124_out, state_1, state_0);
  and and_45 (and_45_out, not_125_out, not_126_out, counter_0, not_127_out, state_6, not_128_out, not_129_out, not_130_out, not_131_out);
  and and_46 (and_46_out, not_132_out, not_133_out, counter_0, not_134_out, state_6, not_135_out, not_136_out, not_137_out, state_2, not_138_out);
  and and_47 (and_47_out, not_139_out, not_140_out, counter_0, not_141_out, state_6, not_142_out, not_143_out, state_3, not_144_out, state_0);
  and and_48 (and_48_out, not_145_out, not_146_out, counter_0, not_147_out, state_6, not_148_out, state_3, state_1, not_149_out);
  and and_49 (and_49_out, not_150_out, not_151_out, counter_0, not_152_out, state_6, not_153_out, state_4, not_154_out, not_155_out);
  and and_50 (and_50_out, not_156_out, not_157_out, counter_0, not_158_out, state_6, not_159_out, state_4, not_160_out, state_1);
  and and_51 (and_51_out, not_161_out, counter_1, not_162_out, not_163_out, not_164_out, not_165_out, not_166_out, state_2, not_167_out, state_0);
  and and_52 (and_52_out, not_168_out, counter_1, not_169_out, not_170_out, not_171_out, not_172_out, state_3, not_173_out, not_174_out);
  and and_53 (and_53_out, not_175_out, counter_1, not_176_out, not_177_out, not_178_out, not_179_out, state_4, not_180_out, not_181_out);
  and and_54 (and_54_out, not_182_out, counter_1, not_183_out, not_184_out, not_185_out, state_4, not_186_out, state_2, not_187_out, state_0);
  and and_55 (and_55_out, not_188_out, counter_1, not_189_out, not_190_out, not_191_out, state_4, not_192_out, state_2, not_193_out, state_0);
  and and_56 (and_56_out, not_194_out, counter_1, not_195_out, not_196_out, not_197_out, not_198_out, state_4, state_3, not_199_out, state_0);
  and and_57 (and_57_out, not_200_out, counter_1, not_201_out, not_202_out, not_203_out, state_5, state_4, not_204_out, state_2, state_1);
  and and_58 (and_58_out, not_205_out, counter_1, not_206_out, not_207_out, not_208_out, state_5, state_4, state_3, not_209_out);
  and and_59 (and_59_out, not_210_out, counter_1, not_211_out, not_212_out, not_213_out, state_5, state_4, state_3, state_2, not_214_out);
  and and_60 (and_60_out, not_215_out, counter_1, not_216_out, not_217_out, state_6, not_218_out, not_219_out, not_220_out, not_221_out, state_0);
  and and_61 (and_61_out, not_222_out, counter_1, not_223_out, not_224_out, state_6, not_225_out, not_226_out, not_227_out, state_1);
  and and_62 (and_62_out, not_228_out, counter_1, not_229_out, not_230_out, state_6, not_231_out, not_232_out, state_1, not_233_out);
  and and_63 (and_63_out, not_234_out, counter_1, not_235_out, not_236_out, state_6, not_237_out, not_238_out, not_239_out, state_1, state_0);
  and and_64 (and_64_out, not_240_out, counter_1, not_241_out, not_242_out, state_6, not_243_out, not_244_out, state_2, state_1);
  and and_65 (and_65_out, not_245_out, counter_1, not_246_out, not_247_out, state_6, not_248_out, state_3, not_249_out, not_250_out);
  and and_66 (and_66_out, not_251_out, counter_1, not_252_out, not_253_out, state_6, not_254_out, state_4, state_3, not_255_out);
  and and_67 (and_67_out, not_256_out, counter_1, not_257_out, not_258_out, state_6, state_5, not_259_out, not_260_out, state_1, not_261_out);
  and and_68 (and_68_out, not_262_out, counter_1, not_263_out, not_264_out, state_6, state_5, not_265_out, not_266_out, state_2, not_267_out);
  and and_69 (and_69_out, not_268_out, counter_1, not_269_out, not_270_out, state_6, state_5, not_271_out, state_3, not_272_out, not_273_out, state_0);
  and and_70 (and_70_out, counter_2, not_274_out, not_275_out, not_276_out, not_277_out, not_278_out, state_4, state_3, not_279_out, state_1, not_280_out);
  and and_71 (and_71_out, counter_2, counter_1, not_281_out, not_282_out, not_283_out, not_284_out, not_285_out, not_286_out, state_1, not_287_out);
  and and_72 (and_72_out, counter_2, counter_1, not_288_out, not_289_out, not_290_out, not_291_out, not_292_out, not_293_out, state_1, not_294_out);
  or or_2 (s_out_6, and_1_out, and_2_out, and_3_out, and_4_out, and_5_out);
  or or_3 (s_out_5, and_6_out, and_7_out, and_8_out, and_9_out, and_10_out, and_11_out);
  or or_4 (s_out_4, and_12_out, and_13_out, and_14_out, and_15_out, and_16_out);
  or or_5 (s_out_3, and_17_out, and_18_out, and_19_out, and_20_out, and_21_out);
  or or_6 (s_out_2, and_22_out, and_23_out, and_24_out, and_25_out, and_26_out);
  or or_7 (or_7_out, and_29_out, and_30_out, and_31_out, and_32_out, and_33_out, and_34_out, and_35_out, and_36_out, and_37_out, and_38_out, and_39_out, and_40_out, and_41_out, and_42_out, and_43_out, and_44_out, and_45_out, and_46_out, and_47_out, and_48_out, and_49_out, and_50_out);
  or or_8 (or_8_out, and_51_out, and_52_out, and_53_out, and_54_out, and_55_out, and_56_out, and_57_out, and_58_out, and_59_out, and_60_out, and_61_out, and_62_out, and_63_out, and_64_out, and_65_out, and_66_out, and_67_out, and_68_out, and_69_out, and_70_out, and_71_out, and_72_out);
  or or_9 (reset, or_7_out, or_8_out);

  assign s_out_7 = 1'b0;
endmodule

module to_one_tic (
  input  I_0,
  input  R,
  output Output_1
);

  wire and_1_out, clock_1_out, d_ff_1_q, d_ff_1_qn, d_ff_2_q;

  Clock clock_1 (.out(clock_1_out));
  D_Flip_Flop d_ff_1 (.D(I_0), .clk(clock_1_out), .Q(d_ff_1_q), .Qn(d_ff_1_qn), .reset(R));  // open: preset
  D_Flip_Flop #(.trigger("falling")) d_ff_2 (
    .D(d_ff_1_qn), .clk(clock_1_out), .Q(d_ff_2_q), .reset(R));  // open: Qn, preset
  D_Flip_Flop #(.trigger("falling")) d_ff_3 (
    .D(and_1_out), .clk(clock_1_out), .Q(Output_1), .reset(R));  // open: Qn, preset
  and and_1 (and_1_out, d_ff_1_q, d_ff_2_q);
endmodule

module reset_mode (
  input  B_1,
  input  B_0,
  output R
);

  wire and_1_out, clock_1_out, d_ff_1_q, d_ff_2_q, d_ff_3_q, t_ff_1_q;

  and and_1 (and_1_out, B_1, B_0);
  Clock #(.highDuration(1000000), .lowDuration(1000000)) clock_1 (.out(clock_1_out));
  T_Flip_Flop t_ff_1 (.T(and_1_out), .clk(clock_1_out), .Q(t_ff_1_q), .reset(d_ff_1_q));  // open: Qn, preset
  D_Flip_Flop d_ff_1 (.D(t_ff_1_q), .clk(clock_1_out), .Q(d_ff_1_q), .reset(d_ff_2_q));  // open: Qn, preset
  D_Flip_Flop d_ff_2 (.D(d_ff_1_q), .clk(clock_1_out), .Q(d_ff_2_q), .reset(d_ff_3_q));  // open: Qn, preset
  D_Flip_Flop d_ff_3 (.D(d_ff_2_q), .clk(clock_1_out), .Q(d_ff_3_q), .reset(d_ff_3_q));  // open: Qn, preset
  and and_2 (R, and_1_out, d_ff_2_q);
endmodule

module check_alarm (
  input  [5:0] t_h,
  input  [5:0] t_m,
  input  [5:0] t_s,
  input  [5:0] a_h,
  input  [5:0] a_m,
  input  [5:0] a_s,
  output alarm_on
);

  wire comparator_1_eq, comparator_2_eq, comparator_3_eq;

  Comparator #(.width(6)) comparator_1 (.a(t_h), .b(a_h), .eq(comparator_1_eq));  // open: gt, lt
  Comparator #(.width(6)) comparator_2 (.a(t_m), .b(a_m), .eq(comparator_2_eq));  // open: gt, lt
  Comparator #(.width(6)) comparator_3 (.a(t_s), .b(a_s), .eq(comparator_3_eq));  // open: gt, lt
  and and_1 (alarm_on, comparator_1_eq, comparator_2_eq, comparator_3_eq);
endmodule

module reset_alarm (
  input  alarm,
  input  B_1,
  input  B_0,
  output reset
);

  wire and_1_out, and_2_out;

  and and_1 (and_1_out, alarm, B_1);
  and and_2 (and_2_out, alarm, B_0);
  or or_1 (reset, and_1_out, and_2_out);
endmodule
module alarme_2 (
  input  [29:0] time_bus,
  input  [11:0] input_bus,
  input  [3:0] mode_on,
  input  B_1,
  input  B_0,
  input  R,
  output alarme,
  output [29:0] O_0
);

  wire check_alarm_1_alarm_on, clock_1_out, comparator_1_eq, reset_alarm_1_reset;
  wire [4:0] time_to_binary_converter_1_o_0, time_to_binary_converter_1_o_1, time_to_binary_converter_2_o_0,
       time_to_binary_converter_2_o_1, time_to_binary_converter_3_o_0, time_to_binary_converter_3_o_1;
  wire [5:0] binary_to_time_converter_1_output_bus_1, binary_to_time_converter_2_output_bus_1,
       binary_to_time_converter_3_output_bus_1, binary_to_time_converter_4_output_bus_1,
       binary_to_time_converter_5_output_bus_1, binary_to_time_converter_6_output_bus_1, memory_alarm_1_hour,
       memory_alarm_1_min, memory_alarm_1_seconds;

  Comparator #(.width(4)) comparator_1 (.a(mode_on), .b(4'b0101), .eq(comparator_1_eq));  // open: gt, lt
  set_time_setter set_time_setter_1 (
    .I_0({time_to_binary_converter_1_o_1, time_to_binary_converter_1_o_0, time_to_binary_converter_2_o_1, time_to_binary_converter_2_o_0, time_to_binary_converter_3_o_1, time_to_binary_converter_3_o_0}),
    .input_bus(input_bus), .mode_on(comparator_1_eq), .R(R), .O_0(O_0));
  binary_to_time_converter binary_to_time_converter_1 (
    .Input_bus_1(time_bus[29:25]), .Input_bus_2(time_bus[24:20]),
    .Output_bus_1(binary_to_time_converter_1_output_bus_1));
  binary_to_time_converter binary_to_time_converter_2 (
    .Input_bus_1(time_bus[19:15]), .Input_bus_2(time_bus[14:10]),
    .Output_bus_1(binary_to_time_converter_2_output_bus_1));
  binary_to_time_converter binary_to_time_converter_3 (
    .Input_bus_1(time_bus[9:5]), .Input_bus_2(time_bus[4:0]),
    .Output_bus_1(binary_to_time_converter_3_output_bus_1));
  binary_to_time_converter binary_to_time_converter_4 (
    .Input_bus_1(O_0[29:25]), .Input_bus_2(O_0[24:20]), .Output_bus_1(binary_to_time_converter_4_output_bus_1));
  binary_to_time_converter binary_to_time_converter_5 (
    .Input_bus_1(O_0[19:15]), .Input_bus_2(O_0[14:10]), .Output_bus_1(binary_to_time_converter_5_output_bus_1));
  binary_to_time_converter binary_to_time_converter_6 (
    .Input_bus_1(O_0[9:5]), .Input_bus_2(O_0[4:0]), .Output_bus_1(binary_to_time_converter_6_output_bus_1));
  Clock clock_1 (.out(clock_1_out));
  time_to_binary_converter time_to_binary_converter_1 (
    .t_in(memory_alarm_1_hour), .O_1(time_to_binary_converter_1_o_1), .O_0(time_to_binary_converter_1_o_0));
  time_to_binary_converter time_to_binary_converter_2 (
    .t_in(memory_alarm_1_min), .O_1(time_to_binary_converter_2_o_1), .O_0(time_to_binary_converter_2_o_0));
  time_to_binary_converter time_to_binary_converter_3 (
    .t_in(memory_alarm_1_seconds), .O_1(time_to_binary_converter_3_o_1), .O_0(time_to_binary_converter_3_o_0));
  memory_alarm memory_alarm_1 (
    .hour_in(binary_to_time_converter_4_output_bus_1), .min_in(binary_to_time_converter_5_output_bus_1),
    .sec_in(binary_to_time_converter_6_output_bus_1), .set(clock_1_out), .reset(R), .enable(comparator_1_eq),
    .hour(memory_alarm_1_hour), .min(memory_alarm_1_min), .seconds(memory_alarm_1_seconds));
  reset_alarm reset_alarm_1 (.alarm(alarme), .B_1(B_1), .B_0(B_0), .reset(reset_alarm_1_reset));
  check_alarm check_alarm_1 (
    .t_h(binary_to_time_converter_1_output_bus_1), .t_m(binary_to_time_converter_2_output_bus_1),
    .t_s(binary_to_time_converter_3_output_bus_1), .a_h(memory_alarm_1_hour), .a_m(memory_alarm_1_min),
    .a_s(memory_alarm_1_seconds), .alarm_on(check_alarm_1_alarm_on));
  S_R_Flip_Flop s_r_ff_1 (
    .S(check_alarm_1_alarm_on), .R(reset_alarm_1_reset), .clk(clock_1_out), .Q(alarme), .reset(R));  // open: Qn, preset
endmodule

// set time zone
module set_time_zone (
  input  [29:0] time_bus,
  input  [3:0] mode_on,
  input  [11:0] input_bus,
  input  R,
  output [29:0] O_text,
  output [29:0] O_time
);

  wire and_1_out, clock_1_out, clock_2_out, clock_3_out, comparator_1_eq, comparator_2_lt, d_ff_1_q,
       not_1_out, or_1_out, set_time_zone_logic_1_s_0, set_time_zone_logic_1_s_1, set_time_zone_logic_1_s_2,
       set_time_zone_logic_1_sign, subtractor_1_bout;
  wire [1:0] d_ff_3_q;
  wire [4:0] register_1_q, register_2_q;
  wire [5:0] adder_1_out, binary_to_time_converter_1_output_bus_1, multiplexer_2_out, multiplexer_3_out,
       multiplexer_4_out, set_time_zone_logic_1_value_0, subtractor_1_out, subtractor_2_out, subtractor_3_out;

  not not_1 (not_1_out, comparator_1_eq);
  Comparator #(.width(4)) comparator_1 (.a(mode_on), .b(4'b0111), .eq(comparator_1_eq));  // open: gt, lt
  or or_1 (or_1_out, not_1_out, and_1_out);
  and and_1 (and_1_out, comparator_1_eq, input_bus[11]);
  Register #(.width(5)) register_1 (.D(time_bus[29:25]), .en(or_1_out), .clk(clock_1_out), .Q(register_1_q), .clr(R));
  Clock clock_1 (.out(clock_1_out));
  Register #(.width(5)) register_2 (.D(time_bus[24:20]), .en(or_1_out), .clk(clock_2_out), .Q(register_2_q), .clr(R));
  Clock clock_2 (.out(clock_2_out));
  // Probe on binary_to_time_converter_1_output_bus_1
  binary_to_time_converter binary_to_time_converter_1 (
    .Input_bus_1(register_1_q), .Input_bus_2(register_2_q),
    .Output_bus_1(binary_to_time_converter_1_output_bus_1));
  Multiplexer #(.select(2), .width(30), .enable("false")) multiplexer_1 (
    .in0(30'h2b8bb717), .in1(30'h2aaf73ff), .in2(30'h2b8bf775), .in3(30'h31c5295f), .out(O_text),
    .sel(d_ff_3_q));
  set_time_zone_logic set_time_zone_logic_1 (
    .old_state_2(d_ff_1_q), .old_state_1(d_ff_3_q[1]), .old_state_0(d_ff_3_q[0]), .in_pressed(and_1_out),
    .mode_on(comparator_1_eq), .sign(set_time_zone_logic_1_sign), .value_5(set_time_zone_logic_1_value_0[5]),
    .value_4(set_time_zone_logic_1_value_0[4]), .value_3(set_time_zone_logic_1_value_0[3]),
    .value_2(set_time_zone_logic_1_value_0[2]), .value_1(set_time_zone_logic_1_value_0[1]),
    .value_0(set_time_zone_logic_1_value_0[0]), .S_2(set_time_zone_logic_1_s_2),
    .S_1(set_time_zone_logic_1_s_1), .S_0(set_time_zone_logic_1_s_0));
  Clock clock_3 (.out(clock_3_out));
  D_Flip_Flop d_ff_1 (.D(set_time_zone_logic_1_s_2), .clk(clock_3_out), .Q(d_ff_1_q), .reset(R));  // open: Qn, preset
  D_Flip_Flop d_ff_2 (
    .D(set_time_zone_logic_1_s_1), .clk(clock_3_out), .Q(d_ff_3_q[1]), .reset(R));  // open: Qn, preset
  D_Flip_Flop d_ff_3 (
    .D(set_time_zone_logic_1_s_0), .clk(clock_3_out), .Q(d_ff_3_q[0]), .reset(R));  // open: Qn, preset
  time_to_binary_converter time_to_binary_converter_1 (
    .t_in(multiplexer_4_out), .O_1(O_time[29:25]), .O_0(O_time[24:20]));
  // Probe on O_time[24:20]
  Subtractor #(.width(6)) subtractor_1 (
    .a(binary_to_time_converter_1_output_bus_1), .b(set_time_zone_logic_1_value_0), .out(subtractor_1_out),
    .bout(subtractor_1_bout));  // open: bin
  // Probe on set_time_zone_logic_1_value_0
  Multiplexer #(.width(6), .enable("false")) multiplexer_2 (
    .in0({6{1'b0}}), .in1(6'b101000), .out(multiplexer_2_out), .sel(subtractor_1_bout));
  Adder #(.width(6)) adder_1 (
    .a(binary_to_time_converter_1_output_bus_1), .b(set_time_zone_logic_1_value_0), .out(adder_1_out));  // open: cin, cout
  // Probe on adder_1_out
  Subtractor #(.width(6)) subtractor_2 (
    .a(subtractor_1_out), .b(multiplexer_2_out), .out(subtractor_2_out));  // open: bin, bout
  // Probe on 6'b010111
  Comparator #(.width(6), .mode("unsigned")) comparator_2 (
    .a(6'b010111), .b(adder_1_out), .lt(comparator_2_lt));  // open: gt, eq
  Multiplexer #(.width(6), .enable("false")) multiplexer_3 (
    .in0({6{1'b0}}), .in1(6'b011000), .out(multiplexer_3_out), .sel(comparator_2_lt));
  Subtractor #(.width(6)) subtractor_3 (
    .a(adder_1_out), .b(multiplexer_3_out), .out(subtractor_3_out));  // open: bin, bout
  // Probe on multiplexer_4_out
  Multiplexer #(.width(6), .enable("false")) multiplexer_4 (
    .in0(subtractor_2_out), .in1(subtractor_3_out), .out(multiplexer_4_out), .sel(set_time_zone_logic_1_sign));

  assign O_time[19:0] = time_bus[19:0];
endmodule

module set_time_zone_logic (
  input  old_state_2,
  input  old_state_1,
  input  old_state_0,
  input  in_pressed,
  input  mode_on,
  output sign,
  output value_5,
  output value_4,
  output value_3,
  output value_2,
  output value_1,
  output value_0,
  output S_2,
  output S_1,
  output S_0
);

  wire nand_1_out, nand_2_out, nand_3_out, nand_4_out, nand_5_out, nand_6_out, nand_7_out, nand_8_out,
       nand_9_out, nand_10_out, nand_11_out, nand_12_out, nand_13_out, nand_14_out, nand_15_out, nand_16_out,
       nand_17_out, nand_18_out, nand_19_out, nand_20_out, nand_21_out, nand_22_out, nand_23_out,
       nand_24_out, nand_25_out, nand_26_out, nand_27_out, nand_28_out, nand_29_out, nand_30_out,
       nand_31_out, nand_32_out, nand_33_out, nand_34_out, nand_35_out, nand_36_out, nand_37_out,
       nand_38_out, nand_39_out, nand_40_out, nand_41_out, nand_42_out, nand_43_out, nand_44_out,
       nand_45_out, nand_46_out, nand_47_out, nand_48_out, nand_49_out, nand_50_out, nand_51_out,
       nand_52_out, nand_53_out, nand_54_out, nand_55_out, nand_56_out, nand_57_out, nand_58_out,
       nand_59_out, nand_60_out, nand_61_out, nand_62_out, nand_63_out, nand_64_out, nand_65_out,
       nand_66_out, nand_67_out, nand_68_out, nand_69_out, nand_70_out, nand_71_out, nand_72_out,
       nand_73_out, nand_74_out, nand_75_out, nand_76_out, nand_77_out, nand_78_out, nand_79_out,
       nand_80_out, nand_81_out, nand_82_out, nand_83_out, nand_84_out, nand_85_out, nand_86_out,
       nand_87_out, nand_88_out, nand_89_out, nand_90_out, nand_91_out, nand_92_out, nand_93_out,
       nand_94_out, nand_95_out, nand_96_out, nand_97_out, nand_98_out, nand_99_out, nand_100_out,
       nand_101_out, nand_102_out, nand_103_out, nand_104_out, nand_105_out, nand_106_out, nand_107_out,
       nand_108_out, nand_109_out, nand_110_out, nand_111_out, nand_112_out, nand_113_out, nand_114_out,
       nand_115_out, nand_116_out, nand_118_out, nand_119_out, nand_120_out, nand_121_out, nand_122_out,
       nand_123_out, nand_124_out, nand_125_out, nand_126_out, nand_127_out, nand_128_out, nand_129_out,
       nand_130_out, nand_131_out, nand_132_out, nand_133_out, nand_134_out, nand_135_out, nand_136_out,
       nand_137_out, nand_138_out, nand_139_out, nand_140_out, nand_141_out, nand_142_out, nand_143_out,
       nand_144_out, nand_145_out, nand_146_out, nand_147_out, nand_148_out, nand_149_out, nand_150_out,
       nand_151_out, nand_152_out, nand_153_out, nand_154_out, nand_155_out, nand_156_out, nand_157_out,
       nand_158_out, nand_159_out, nand_160_out, nand_161_out, nand_162_out, nand_163_out, nand_164_out,
       nand_165_out, nand_166_out, nand_167_out, nand_168_out, nand_169_out, nand_170_out, nand_174_out,
       nand_175_out, nand_176_out, nand_177_out, nand_178_out, nand_179_out, nand_181_out, nand_182_out,
       nand_183_out, nand_184_out, nand_185_out, nand_186_out, nand_187_out, nand_188_out;

  nand nand_1 (nand_1_out, old_state_2, old_state_2);
  nand nand_2 (nand_2_out, old_state_1, old_state_1);
  nand nand_3 (nand_3_out, old_state_1, old_state_1);
  nand nand_4 (nand_4_out, old_state_0, old_state_0);
  nand nand_5 (nand_5_out, mode_on, mode_on);
  nand nand_6 (nand_6_out, old_state_2, old_state_2);
  nand nand_7 (nand_7_out, old_state_1, old_state_1);
  nand nand_8 (nand_8_out, old_state_1, old_state_1);
  nand nand_9 (nand_9_out, old_state_2, old_state_2);
  nand nand_10 (nand_10_out, old_state_0, old_state_0);
  nand nand_11 (nand_11_out, old_state_1, old_state_1);
  nand nand_12 (nand_12_out, old_state_2, old_state_2);
  nand nand_13 (nand_13_out, old_state_0, old_state_0);
  nand nand_14 (nand_14_out, old_state_2, old_state_2);
  nand nand_15 (nand_15_out, old_state_1, old_state_1);
  nand nand_16 (nand_16_out, old_state_1, old_state_1);
  nand nand_17 (nand_17_out, old_state_1, old_state_1);
  nand nand_18 (nand_18_out, old_state_2, old_state_2);
  nand nand_19 (nand_19_out, old_state_2, old_state_2);
  nand nand_20 (nand_20_out, old_state_0, old_state_0);
  nand nand_21 (nand_21_out, nand_1_out, nand_2_out);
  nand nand_22 (nand_22_out, nand_3_out, nand_4_out);
  nand nand_23 (nand_23_out, in_pressed, nand_5_out);
  nand nand_24 (nand_24_out, nand_6_out, old_state_1);
  nand nand_25 (nand_25_out, old_state_0, mode_on);
  nand nand_26 (nand_26_out, old_state_2, nand_7_out);
  nand nand_27 (nand_27_out, nand_8_out, old_state_0);
  nand nand_28 (nand_28_out, nand_9_out, old_state_1);
  nand nand_29 (nand_29_out, nand_10_out, mode_on);
  nand nand_30 (nand_30_out, nand_11_out, old_state_0);
  nand nand_31 (nand_31_out, nand_12_out, old_state_1);
  nand nand_32 (nand_32_out, nand_13_out, mode_on);
  nand nand_33 (nand_33_out, nand_14_out, nand_15_out);
  nand nand_34 (nand_34_out, old_state_2, nand_16_out);
  nand nand_35 (nand_35_out, nand_17_out, old_state_0);
  nand nand_36 (nand_36_out, nand_18_out, old_state_1);
  nand nand_37 (nand_37_out, nand_19_out, old_state_0);
  nand nand_38 (nand_38_out, old_state_2, old_state_1);
  nand nand_39 (nand_39_out, nand_20_out, mode_on);
  nand nand_40 (nand_40_out, nand_21_out, nand_21_out);
  nand nand_41 (nand_41_out, in_pressed, in_pressed);
  nand nand_42 (nand_42_out, nand_22_out, nand_22_out);
  nand nand_43 (nand_43_out, nand_23_out, nand_23_out);
  nand nand_44 (nand_44_out, nand_24_out, nand_24_out);
  nand nand_45 (nand_45_out, nand_25_out, nand_25_out);
  nand nand_46 (nand_46_out, nand_26_out, nand_26_out);
  nand nand_47 (nand_47_out, old_state_0, old_state_0);
  nand nand_48 (nand_48_out, in_pressed, in_pressed);
  nand nand_49 (nand_49_out, nand_27_out, nand_27_out);
  nand nand_50 (nand_50_out, nand_28_out, nand_28_out);
  nand nand_51 (nand_51_out, nand_29_out, nand_29_out);
  nand nand_52 (nand_52_out, old_state_2, old_state_2);
  nand nand_53 (nand_53_out, in_pressed, in_pressed);
  nand nand_54 (nand_54_out, nand_30_out, nand_30_out);
  nand nand_55 (nand_55_out, nand_31_out, nand_31_out);
  nand nand_56 (nand_56_out, nand_32_out, nand_32_out);
  nand nand_57 (nand_57_out, old_state_2, old_state_2);
  nand nand_58 (nand_58_out, in_pressed, in_pressed);
  nand nand_59 (nand_59_out, old_state_1, old_state_1);
  nand nand_60 (nand_60_out, old_state_0, old_state_0);
  nand nand_61 (nand_61_out, nand_33_out, nand_33_out);
  nand nand_62 (nand_62_out, in_pressed, in_pressed);
  nand nand_63 (nand_63_out, old_state_1, old_state_1);
  nand nand_64 (nand_64_out, old_state_0, old_state_0);
  nand nand_65 (nand_65_out, mode_on, mode_on);
  nand nand_66 (nand_66_out, mode_on, mode_on);
  nand nand_67 (nand_67_out, nand_34_out, nand_34_out);
  nand nand_68 (nand_68_out, old_state_0, old_state_0);
  nand nand_69 (nand_69_out, in_pressed, in_pressed);
  nand nand_70 (nand_70_out, nand_35_out, nand_35_out);
  nand nand_71 (nand_71_out, nand_36_out, nand_36_out);
  nand nand_72 (nand_72_out, in_pressed, in_pressed);
  nand nand_73 (nand_73_out, old_state_1, old_state_1);
  nand nand_74 (nand_74_out, old_state_0, old_state_0);
  nand nand_75 (nand_75_out, nand_37_out, nand_37_out);
  nand nand_76 (nand_76_out, in_pressed, in_pressed);
  nand nand_77 (nand_77_out, mode_on, mode_on);
  nand nand_78 (nand_78_out, nand_38_out, nand_38_out);
  nand nand_79 (nand_79_out, nand_39_out, nand_39_out);
  nand nand_80 (nand_80_out, nand_40_out, nand_41_out);
  nand nand_81 (nand_81_out, nand_42_out, nand_43_out);
  nand nand_82 (nand_82_out, old_state_1, in_pressed);
  nand nand_83 (nand_83_out, nand_44_out, nand_45_out);
  nand nand_84 (nand_84_out, nand_46_out, nand_47_out);
  nand nand_85 (nand_85_out, nand_48_out, mode_on);
  nand nand_86 (nand_86_out, nand_49_out, in_pressed);
  nand nand_87 (nand_87_out, nand_50_out, nand_51_out);
  nand nand_88 (nand_88_out, nand_52_out, old_state_1);
  nand nand_89 (nand_89_out, nand_53_out, mode_on);
  nand nand_90 (nand_90_out, nand_54_out, in_pressed);
  nand nand_91 (nand_91_out, nand_55_out, nand_56_out);
  nand nand_92 (nand_92_out, nand_57_out, old_state_1);
  nand nand_93 (nand_93_out, nand_58_out, mode_on);
  nand nand_94 (nand_94_out, nand_59_out, nand_60_out);
  nand nand_95 (nand_95_out, nand_61_out, old_state_0);
  nand nand_96 (nand_96_out, nand_62_out, mode_on);
  nand nand_97 (nand_97_out, old_state_1, old_state_0);
  nand nand_98 (nand_98_out, old_state_2, nand_63_out);
  nand nand_99 (nand_99_out, nand_64_out, mode_on);
  nand nand_100 (nand_100_out, old_state_0, nand_65_out);
  nand nand_101 (nand_101_out, old_state_1, nand_66_out);
  nand nand_102 (nand_102_out, old_state_1, old_state_0);
  nand nand_103 (nand_103_out, nand_67_out, nand_68_out);
  nand nand_104 (nand_104_out, nand_69_out, mode_on);
  nand nand_105 (nand_105_out, old_state_2, old_state_1);
  nand nand_106 (nand_106_out, nand_70_out, in_pressed);
  nand nand_107 (nand_107_out, nand_71_out, nand_72_out);
  nand nand_108 (nand_108_out, old_state_2, nand_73_out);
  nand nand_109 (nand_109_out, old_state_0, mode_on);
  nand nand_110 (nand_110_out, nand_74_out, in_pressed);
  nand nand_111 (nand_111_out, nand_75_out, nand_76_out);
  nand nand_112 (nand_112_out, old_state_0, nand_77_out);
  nand nand_113 (nand_113_out, nand_78_out, nand_79_out);
  nand nand_114 (nand_114_out, nand_80_out, mode_on);
  nand nand_115 (nand_115_out, old_state_0, old_state_0);
  nand nand_116 (nand_116_out, in_pressed, in_pressed);
  nand nand_117 (value_4, nand_81_out, nand_81_out);
  nand nand_118 (nand_118_out, nand_82_out, nand_83_out);
  nand nand_119 (nand_119_out, nand_84_out, nand_84_out);
  nand nand_120 (nand_120_out, nand_85_out, nand_85_out);
  nand nand_121 (nand_121_out, nand_86_out, nand_87_out);
  nand nand_122 (nand_122_out, nand_88_out, nand_88_out);
  nand nand_123 (nand_123_out, nand_89_out, nand_89_out);
  nand nand_124 (nand_124_out, nand_90_out, nand_91_out);
  nand nand_125 (nand_125_out, nand_92_out, nand_92_out);
  nand nand_126 (nand_126_out, nand_93_out, nand_93_out);
  nand nand_127 (nand_127_out, nand_94_out, nand_94_out);
  nand nand_128 (nand_128_out, nand_95_out, nand_95_out);
  nand nand_129 (nand_129_out, nand_96_out, nand_96_out);
  nand nand_130 (nand_130_out, nand_97_out, nand_97_out);
  nand nand_131 (nand_131_out, nand_98_out, nand_98_out);
  nand nand_132 (nand_132_out, nand_99_out, nand_99_out);
  nand nand_133 (nand_133_out, nand_100_out, nand_101_out);
  nand nand_134 (nand_134_out, nand_102_out, nand_102_out);
  nand nand_135 (nand_135_out, nand_103_out, nand_103_out);
  nand nand_136 (nand_136_out, nand_104_out, nand_104_out);
  nand nand_137 (nand_137_out, nand_105_out, nand_105_out);
  nand nand_138 (nand_138_out, nand_106_out, nand_107_out);
  nand nand_139 (nand_139_out, old_state_0, old_state_0);
  nand nand_140 (nand_140_out, mode_on, mode_on);
  nand nand_141 (nand_141_out, nand_108_out, nand_108_out);
  nand nand_142 (nand_142_out, nand_109_out, nand_109_out);
  nand nand_143 (nand_143_out, nand_110_out, nand_111_out);
  nand nand_144 (nand_144_out, nand_112_out, nand_113_out);
  nand nand_145 (nand_145_out, nand_114_out, nand_114_out);
  nand nand_146 (nand_146_out, nand_115_out, in_pressed);
  nand nand_147 (nand_147_out, old_state_0, nand_116_out);
  nand nand_148 (nand_148_out, old_state_2, old_state_1);
  nand nand_149 (nand_149_out, nand_118_out, nand_118_out);
  nand nand_150 (nand_150_out, nand_119_out, nand_120_out);
  nand nand_151 (nand_151_out, nand_121_out, nand_121_out);
  nand nand_152 (nand_152_out, nand_122_out, nand_123_out);
  nand nand_153 (nand_153_out, nand_124_out, nand_124_out);
  nand nand_154 (nand_154_out, nand_125_out, nand_126_out);
  nand nand_155 (nand_155_out, nand_127_out, in_pressed);
  nand nand_156 (nand_156_out, nand_128_out, nand_129_out);
  nand nand_157 (nand_157_out, nand_130_out, in_pressed);
  nand nand_158 (nand_158_out, nand_131_out, nand_132_out);
  nand nand_159 (nand_159_out, nand_133_out, nand_133_out);
  nand nand_160 (nand_160_out, nand_134_out, in_pressed);
  nand nand_161 (nand_161_out, nand_135_out, nand_136_out);
  nand nand_162 (nand_162_out, nand_137_out, old_state_0);
  nand nand_163 (nand_163_out, nand_138_out, nand_138_out);
  nand nand_164 (nand_164_out, old_state_1, nand_139_out);
  nand nand_165 (nand_165_out, old_state_1, nand_140_out);
  nand nand_166 (nand_166_out, nand_141_out, nand_142_out);
  nand nand_167 (nand_167_out, nand_143_out, nand_143_out);
  nand nand_168 (nand_168_out, nand_144_out, nand_144_out);
  nand nand_169 (nand_169_out, nand_145_out, nand_146_out);
  nand nand_170 (nand_170_out, nand_147_out, nand_148_out);
  nand nand_171 (value_3, nand_149_out, nand_150_out);
  nand nand_172 (value_2, nand_151_out, nand_152_out);
  nand nand_173 (value_1, nand_153_out, nand_154_out);
  nand nand_174 (nand_174_out, nand_155_out, nand_156_out);
  nand nand_175 (nand_175_out, nand_157_out, nand_158_out);
  nand nand_176 (nand_176_out, nand_159_out, nand_160_out);
  nand nand_177 (nand_177_out, nand_161_out, nand_162_out);
  nand nand_178 (nand_178_out, nand_163_out, nand_164_out);
  nand nand_179 (nand_179_out, nand_165_out, nand_166_out);
  nand nand_180 (S_0, nand_167_out, nand_168_out);
  nand nand_181 (nand_181_out, nand_169_out, nand_169_out);
  nand nand_182 (nand_182_out, nand_170_out, nand_170_out);
  nand nand_183 (nand_183_out, nand_174_out, nand_174_out);
  nand nand_184 (nand_184_out, nand_175_out, nand_175_out);
  nand nand_185 (nand_185_out, nand_176_out, nand_176_out);
  nand nand_186 (nand_186_out, nand_177_out, nand_177_out);
  nand nand_187 (nand_187_out, nand_178_out, nand_178_out);
  nand nand_188 (nand_188_out, nand_179_out, nand_179_out);
  nand nand_189 (sign, nand_181_out, nand_182_out);
  nand nand_190 (value_0, nand_183_out, nand_184_out);
  nand nand_191 (S_2, nand_185_out, nand_186_out);
  nand nand_192 (S_1, nand_187_out, nand_188_out);

  assign value_5 = 1'b0;
endmodule

module jukebox (
  input  [3:0] mode_on,
  input  [11:0] input_bus,
  input  R,
  output [29:0] O_text,
  output [1:0] O_music,
  output set_music_on
);

  wire and_1_out, clock_1_out;
  wire [1:0] counter_1_q;
  wire [4:0] undriven, undriven_2, undriven_3, undriven_4, undriven_5, undriven_6, undriven_7, undriven_8,
       undriven_9, undriven_10, undriven_11, undriven_12;

  Comparator #(.width(4)) comparator_1 (.a(mode_on), .b(4'b1001), .eq(set_music_on));  // open: gt, lt
  and and_1 (and_1_out, set_music_on, input_bus[11]);
  Clock clock_1 (.out(clock_1_out));
  Counter #(.width(2), .max('h3)) counter_1 (
    .clr(R), .load(1'b0), .up(1'b1), .count(and_1_out), .clk(clock_1_out), .D(2'b00), .Q(counter_1_q));  // open: carry
  Multiplexer #(.select(2), .width(30), .enable("false")) multiplexer_1 (
    .in0(30'h338ef5db), .in1(30'h37f10c1f),
    .in2({undriven_6, undriven_5, undriven_4, undriven_3, undriven_2, undriven}),
    .in3({undriven_12, undriven_11, undriven_10, undriven_9, undriven_8, undriven_7}), .out(O_text),
    .sel(counter_1_q));
  Multiplexer #(.width(2), .enable("false")) multiplexer_2 (
    .in0(2'b00), .in1(counter_1_q), .out(O_music), .sel(set_music_on));
endmodule

module set_time_zone_2 (
  input  [29:0] time_bus,
  input  [11:0] input_bus,
  input  [3:0] mode_on,
  input  R,
  output [29:0] time_outpus,
  output [29:0] out_6
);

  Multiplexer #(.select(2), .width(30), .enable("false")) multiplexer_1 (
    .in0(30'h2b8bb717), .in1(30'h2aaf73ff), .in2(30'h2b8bf775), .in3(30'h31c5295f), .out(out_6));  // open: sel
  set_time_to_23 set_time_to_23_1 (
    .R(R), .I_1(time_bus[29:25]), .I_0(time_bus[24:20]), .O_1(time_outpus[29:25]), .O_0(time_outpus[24:20]));  // open: B_1, B_0, load, set_on

  assign time_outpus[19:0] = time_bus[19:0];
endmodule

module chrono (
  input  [11:0] input_bus,
  input  [3:0] mode_on,
  input  R,
  output [29:0] O_0
);

  wire and_1_out, clock_1_out, clock_2_out, comparator_1_eq, comparator_2_eq, comparator_3_eq, not_1_out,
       or_1_out, t_ff_1_q;
  wire [5:0] binary_to_time_converter_1_output_bus_1, binary_to_time_converter_2_output_bus_1,
       binary_to_time_converter_3_output_bus_1, counter_1_q, counter_2_q, counter_3_q;

  Clock clock_1 (.out(clock_1_out));
  T_Flip_Flop t_ff_1 (.T(input_bus[11]), .clk(clock_2_out), .Q(t_ff_1_q));  // open: Qn, reset, preset
  Clock #(.highDuration(2), .lowDuration(2)) clock_2 (.out(clock_2_out));
  Comparator #(.width(4)) comparator_1 (.a(mode_on), .b(4'b0001), .eq(comparator_1_eq));  // open: gt, lt
  not not_1 (not_1_out, comparator_1_eq);
  or or_1 (or_1_out, not_1_out, R);
  binary_to_time_converter binary_to_time_converter_1 (
    .Input_bus_1({5{1'b0}}), .Input_bus_2({5{1'b0}}), .Output_bus_1(binary_to_time_converter_1_output_bus_1));
  binary_to_time_converter binary_to_time_converter_2 (
    .Input_bus_1({5{1'b0}}), .Input_bus_2({5{1'b0}}), .Output_bus_1(binary_to_time_converter_2_output_bus_1));
  binary_to_time_converter binary_to_time_converter_3 (
    .Input_bus_1({5{1'b0}}), .Input_bus_2({5{1'b0}}), .Output_bus_1(binary_to_time_converter_3_output_bus_1));
  Counter #(.width(6), .max('h17)) counter_1 (
    .clr(or_1_out), .load(1'b0), .up(1'b1), .count(and_1_out), .clk(clock_1_out),
    .D(binary_to_time_converter_1_output_bus_1), .Q(counter_1_q));  // open: carry
  Counter #(.width(6), .max('h3b)) counter_2 (
    .clr(or_1_out), .load(1'b0), .up(1'b1), .count(comparator_3_eq), .clk(clock_1_out),
    .D(binary_to_time_converter_2_output_bus_1), .Q(counter_2_q));  // open: carry
  Counter #(.width(6), .max('h3b)) counter_3 (
    .clr(or_1_out), .load(1'b0), .up(1'b1), .count(t_ff_1_q), .clk(clock_1_out),
    .D(binary_to_time_converter_3_output_bus_1), .Q(counter_3_q));  // open: carry
  Comparator #(.width(6)) comparator_2 (.a(6'b111011), .b(counter_2_q), .eq(comparator_2_eq));  // open: gt, lt
  Comparator #(.width(6)) comparator_3 (.a(6'b111011), .b(counter_3_q), .eq(comparator_3_eq));  // open: gt, lt
  and and_1 (and_1_out, comparator_2_eq, comparator_3_eq);
  time_to_binary_converter time_to_binary_converter_1 (.t_in(counter_1_q), .O_1(O_0[29:25]), .O_0(O_0[24:20]));
  time_to_binary_converter time_to_binary_converter_2 (.t_in(counter_2_q), .O_1(O_0[19:15]), .O_0(O_0[14:10]));
  time_to_binary_converter time_to_binary_converter_3 (.t_in(counter_3_q), .O_1(O_0[9:5]), .O_0(O_0[4:0]));
endmodule
